// Logisim project Voxel_16-CPU.circ as structural Verilog: 9 circuits, main circuit main
module main (
  input  in_1,
  input  in_2,
  input  in_3,
  input  in_4,
  input  in_5,
  input  in_6,
  input  in_7,
  input  in_8,
  input  in_9,
  input  in_10,
  input  in_11,
  input  in_12,
  input  in_13,
  input  in_14,
  input  in_15,
  input  in_16,
  input  in_17,
  input  in_18,
  input  in_19,
  input  in_20,
  input  in_21,
  input  manual_load,
  input  RESET_MEM,
  input  start,
  output out_25,
  output out_26,
  output out_27,
  output out_28
);

  wire and_3_out, and_4_out, and_5_out, and_6_out, and_7_out, and_8_out, and_9_out, and_10_out, and_11_out,
       and_12_out, and_13_out, and_14_out, and_15_out, and_16_out, and_17_out, and_18_out, and_19_out,
       and_20_out, and_21_out, and_22_out, and_23_out, and_24_out, and_25_out, and_26_out, and_27_out,
       and_28_out, and_29_out, and_30_out, and_31_out, and_32_out, and_33_out, and_34_out, and_35_out,
       and_36_out, and_37_out, and_41_out, and_42_out, and_43_out, and_45_out, and_46_out, and_47_out,
       and_48_out, and_49_out, and_50_out, and_51_out, and_64_out, and_73_out, and_82_out, and_83_out,
       clock_1_out, not_1_out, not_2_out, not_3_out, not_4_out, not_5_out, not_6_out, not_7_out, not_8_out,
       not_9_out, not_10_out, not_11_out, not_12_out, not_13_out, not_14_out, not_15_out, not_16_out,
       not_17_out, not_18_out, not_19_out, not_20_out, not_21_out, not_22_out, not_23_out, not_24_out,
       not_25_out, not_26_out, or_2_out, or_3_out, or_4_out, or_7_out, or_8_out, or_10_out, or_11_out,
       or_12_out, or_14_out, or_15_out, or_16_out, or_17_out;
  wire [1:0] state_counter_2bit_1_data_out;
  wire [3:0] alu_16bit_1_c;
  wire [4:0] and_38_out, and_39_out, and_40_out, and_62_out, and_63_out, mar_5bit_1_out_5, or_1_out, or_6_out;
  wire [4:4] and_1_out, load_out, or_9_out, save_out;
  wire [15:0] alu_16bit_1_data_out, and_60_out, and_61_out, and_65_out, and_66_out, and_67_out, and_68_out,
       and_69_out, and_70_out, and_71_out, and_72_out, and_84_out, and_85_out, and_86_out, and_95_out,
       and_96_out, and_97_out, and_98_out, and_99_out, and_100_out, and_101_out, and_102_out, and_103_out,
       and_104_out, and_105_out, and_106_out, and_107_out, and_108_out, and_109_out, and_110_out,
       memory_file_8byte_1_data_out, memory_file_8byte_2_data_out, memory_file_8byte_3_data_out,
       memory_file_8byte_4_data_out, memory_file_8byte_5_data_out, memory_file_8byte_6_data_out,
       memory_file_8byte_7_data_out, memory_file_8byte_8_data_out, or_5_out, or_13_out, or_18_out, or_19_out,
       or_20_out, or_21_out, program_counter_16bit_1_data_out, register_16bit_1_data_out,
       register_16bit_2_data_out, register_16bit_3_data_out, register_file_8byte_1_out_a,
       register_file_8byte_1_out_b, register_file_8byte_1_out_c, register_file_8byte_1_out_d,
       register_file_8byte_2_out_a, register_file_8byte_2_out_b, register_file_8byte_2_out_c,
       register_file_8byte_2_out_d;
  wire [15:15] and_52_out, and_53_out, and_54_out, and_55_out, and_56_out, and_57_out, and_58_out,
       and_59_out, and_74_out, and_75_out, and_76_out, and_77_out, and_78_out, and_79_out, and_80_out,
       and_81_out, and_87_out, and_88_out, and_89_out, and_90_out, and_91_out, and_92_out, and_93_out,
       and_94_out;

  state_counter_2bit state_counter_2bit_1 (.CLOCK(clock_1_out), .LOAD(start), .DATA_OUT(state_counter_2bit_1_data_out));
  not not_1 (not_1_out, state_counter_2bit_1_data_out[1]);
  not not_2 (not_2_out, state_counter_2bit_1_data_out[0]);
  and and_1 (and_1_out[4], not_1_out, not_2_out);
  // AND_Gate and_2 has open pins: in0=not_1_out, in1=state_counter_2bit_1_data_out[0], out=open
  and and_3 (and_3_out, state_counter_2bit_1_data_out[1], not_2_out);
  and and_4 (and_4_out, state_counter_2bit_1_data_out[1], state_counter_2bit_1_data_out[0]);
  Clock clock_1 (.out(clock_1_out));
  and and_5 (and_5_out, and_3_out, and_8_out);
  assign or_1_out = {in_17, in_18, in_19, in_20, in_21} | and_63_out;  // OR_Gate or_1, 5 bits wide
  not not_3 (not_3_out, and_9_out);
  not not_4 (not_4_out, and_8_out);
  and and_6 (and_6_out, not_3_out, and_1_out[4]);
  or or_2 (or_2_out, and_5_out, and_6_out);
  and and_7 (and_7_out, or_2_out, start);
  or or_3 (or_3_out, and_11_out, and_12_out, and_13_out);
  and and_8 (and_8_out, or_3_out, and_3_out, and_41_out);
  and and_9 (and_9_out, and_14_out, and_41_out);
  or or_4 (or_4_out, manual_load, and_10_out);
  and and_10 (and_10_out, and_4_out, save_out[4]);
  and and_11 (and_11_out, not_5_out, not_6_out, register_16bit_1_data_out[0]);
  and and_12 (and_12_out, not_5_out, register_16bit_1_data_out[1], not_7_out, out_26);
  and and_13 (and_13_out, not_5_out, register_16bit_1_data_out[1], register_16bit_1_data_out[0], not_11_out);
  and and_14 (and_14_out, register_16bit_1_data_out[2], not_6_out, not_7_out);
  register_16bit register_16bit_1 (
    .CLOCK(clock_1_out), .LOAD(and_1_out[4]), .DATA_IN(and_86_out), .RESET(RESET_MEM),
    .DATA_OUT(register_16bit_1_data_out));
  not not_5 (not_5_out, register_16bit_1_data_out[2]);
  not not_6 (not_6_out, register_16bit_1_data_out[1]);
  not not_7 (not_7_out, register_16bit_1_data_out[0]);
  assign or_5_out = {in_1, in_2, in_3, in_4, in_5, in_6, in_7, in_8, in_9, in_10, in_11, in_12, in_13, in_14, in_15, in_16} | and_84_out;  // OR_Gate or_5, 16 bits wide
  not not_8 (not_8_out, or_1_out[4]);
  not not_9 (not_9_out, or_1_out[3]);
  not not_10 (not_10_out, or_1_out[2]);
  program_counter_16bit program_counter_16bit_1 (
    .CLOCK(clock_1_out), .FUNC_SELECT(not_4_out), .LOAD(and_7_out), .DATA_IN(or_20_out), .RESET(RESET_MEM),
    .DATA_OUT(program_counter_16bit_1_data_out));
  not not_11 (not_11_out, out_26);
  and and_15 (and_15_out, not_8_out, not_9_out, not_10_out, or_4_out);
  and and_16 (and_16_out, not_8_out, not_9_out, or_1_out[2], or_4_out);
  and and_17 (and_17_out, not_8_out, or_1_out[3], not_10_out, or_4_out);
  and and_18 (and_18_out, not_8_out, or_1_out[3], or_1_out[2], or_4_out);
  and and_19 (and_19_out, or_1_out[4], not_9_out, not_10_out, or_4_out);
  and and_20 (and_20_out, or_1_out[4], not_9_out, or_1_out[2], or_4_out);
  and and_21 (and_21_out, or_1_out[4], or_1_out[3], not_10_out, or_4_out);
  and and_22 (and_22_out, or_1_out[4], or_1_out[3], or_1_out[2], or_4_out);
  not not_12 (not_12_out, register_16bit_1_data_out[5]);
  not not_13 (not_13_out, register_16bit_1_data_out[4]);
  and and_23 (and_23_out, register_16bit_1_data_out[8], load_out[4], and_4_out);
  and and_24 (and_24_out, register_16bit_1_data_out[7], load_out[4], and_4_out);
  and and_25 (and_25_out, register_16bit_1_data_out[6], load_out[4], and_4_out);
  and and_26 (and_26_out, register_16bit_1_data_out[13], save_out[4], and_4_out);
  and and_27 (and_27_out, register_16bit_1_data_out[12], save_out[4], and_4_out);
  and and_28 (and_28_out, register_16bit_1_data_out[11], save_out[4], and_4_out);
  and and_29 (and_29_out, register_16bit_1_data_out[8], and_43_out, and_4_out);
  and and_30 (and_30_out, register_16bit_1_data_out[7], and_43_out, and_4_out);
  and and_31 (and_31_out, register_16bit_1_data_out[6], and_43_out, and_4_out);
  and and_32 (and_32_out, register_16bit_1_data_out[8], and_43_out, and_3_out);
  and and_33 (and_33_out, register_16bit_1_data_out[7], and_43_out, and_3_out);
  and and_34 (and_34_out, register_16bit_1_data_out[6], and_43_out, and_3_out);
  and and_35 (and_35_out, register_16bit_1_data_out[13], and_43_out, and_3_out);
  and and_36 (and_36_out, register_16bit_1_data_out[12], and_43_out, and_3_out);
  and and_37 (and_37_out, register_16bit_1_data_out[11], and_43_out, and_3_out);
  assign and_38_out = program_counter_16bit_1_data_out[4:0] & {5{and_1_out[4]}};  // AND_Gate and_38, 5 bits wide
  assign and_39_out = register_16bit_1_data_out[15:11] & {5{load_out[4]}};  // AND_Gate and_39, 5 bits wide
  assign or_6_out = and_38_out | and_39_out | and_40_out;  // OR_Gate or_6, 5 bits wide
  assign and_40_out = register_16bit_1_data_out[10:6] & {5{save_out[4]}};  // AND_Gate and_40, 5 bits wide
  and and_41 (and_41_out, not_12_out, not_13_out);
  and and_42 (and_42_out, not_12_out, register_16bit_1_data_out[4]);
  and and_43 (and_43_out, register_16bit_1_data_out[5], not_13_out);
  // AND_Gate and_44 has open pins: in0=register_16bit_1_data_out[5], in1=register_16bit_1_data_out[4], out=open
  or or_7 (or_7_out, load_out[4], and_1_out[4], save_out[4]);
  and load (load_out[4], and_42_out, not_14_out, not_15_out, not_16_out);
  and save (save_out[4], and_42_out, not_16_out, register_16bit_1_data_out[0], not_15_out);
  not not_14 (not_14_out, register_16bit_1_data_out[0]);
  not not_15 (not_15_out, register_16bit_1_data_out[1]);
  not not_16 (not_16_out, and_1_out[4]);
  and and_45 (and_45_out, and_3_out, and_8_out, register_16bit_1_data_out[13]);
  and and_46 (and_46_out, and_3_out, and_8_out, register_16bit_1_data_out[12]);
  and and_47 (and_47_out, and_3_out, and_8_out, register_16bit_1_data_out[11]);
  not not_17 (not_17_out, and_62_out[4]);
  not not_18 (not_18_out, and_62_out[3]);
  not not_19 (not_19_out, and_62_out[2]);
  and and_48 (and_48_out, and_43_out, register_16bit_1_data_out[3]);
  and and_49 (and_49_out, and_43_out, register_16bit_1_data_out[2]);
  and and_50 (and_50_out, and_43_out, register_16bit_1_data_out[1]);
  and and_51 (and_51_out, and_43_out, register_16bit_1_data_out[0]);
  or or_8 (or_8_out, and_43_out, load_out[4]);
  and and_52 (and_52_out[15], not_17_out, not_18_out, not_19_out);
  and and_53 (and_53_out[15], not_17_out, not_18_out, and_62_out[2]);
  and and_54 (and_54_out[15], not_17_out, and_62_out[3], not_19_out);
  and and_55 (and_55_out[15], not_17_out, and_62_out[3], and_62_out[2]);
  and and_56 (and_56_out[15], and_62_out[4], not_18_out, not_19_out);
  and and_57 (and_57_out[15], and_62_out[4], not_18_out, and_62_out[2]);
  and and_58 (and_58_out[15], and_62_out[4], and_62_out[3], not_19_out);
  and and_59 (and_59_out[15], and_62_out[4], and_62_out[3], and_62_out[2]);
  MAR_5bit mar_5bit_1 (
    .CLOCK(clock_1_out), .LOAD(or_7_out), .DATA_IN(or_6_out), .RESET(RESET_MEM), .out_5(mar_5bit_1_out_5));
  or or_9 (or_9_out[4], load_out[4], and_1_out[4]);
  or or_10 (or_10_out, and_26_out, and_45_out, and_32_out);
  or or_11 (or_11_out, and_27_out, and_46_out, and_33_out);
  or or_12 (or_12_out, and_28_out, and_47_out, and_34_out);
  memory_file_8byte memory_file_8byte_1 (
    .CLOCK(clock_1_out), .DATA_IN(or_5_out), .LOAD(and_22_out), .LOAD_SELECT_1(or_1_out[1]),
    .LOAD_SELECT_0(or_1_out[0]), .READ_SELECT_1(and_62_out[1]), .READ_SELECT_0(and_62_out[0]),
    .RESET(RESET_MEM), .DATA_OUT(memory_file_8byte_1_data_out));
  assign and_60_out = memory_file_8byte_1_data_out & {16{and_59_out[15]}};  // AND_Gate and_60, 16 bits wide
  memory_file_8byte memory_file_8byte_2 (
    .CLOCK(clock_1_out), .DATA_IN(or_5_out), .LOAD(and_21_out), .LOAD_SELECT_1(or_1_out[1]),
    .LOAD_SELECT_0(or_1_out[0]), .READ_SELECT_1(and_62_out[1]), .READ_SELECT_0(and_62_out[0]),
    .RESET(RESET_MEM), .DATA_OUT(memory_file_8byte_2_data_out));
  assign and_61_out = memory_file_8byte_2_data_out & {16{and_58_out[15]}};  // AND_Gate and_61, 16 bits wide
  memory_file_8byte memory_file_8byte_3 (
    .CLOCK(clock_1_out), .DATA_IN(or_5_out), .LOAD(and_20_out), .LOAD_SELECT_1(or_1_out[1]),
    .LOAD_SELECT_0(or_1_out[0]), .READ_SELECT_1(and_62_out[1]), .READ_SELECT_0(and_62_out[0]),
    .RESET(RESET_MEM), .DATA_OUT(memory_file_8byte_3_data_out));
  memory_file_8byte memory_file_8byte_4 (
    .CLOCK(clock_1_out), .DATA_IN(or_5_out), .LOAD(and_19_out), .LOAD_SELECT_1(or_1_out[1]),
    .LOAD_SELECT_0(or_1_out[0]), .READ_SELECT_1(and_62_out[1]), .READ_SELECT_0(and_62_out[0]),
    .RESET(RESET_MEM), .DATA_OUT(memory_file_8byte_4_data_out));
  memory_file_8byte memory_file_8byte_5 (
    .CLOCK(clock_1_out), .DATA_IN(or_5_out), .LOAD(and_18_out), .LOAD_SELECT_1(or_1_out[1]),
    .LOAD_SELECT_0(or_1_out[0]), .READ_SELECT_1(and_62_out[1]), .READ_SELECT_0(and_62_out[0]),
    .RESET(RESET_MEM), .DATA_OUT(memory_file_8byte_5_data_out));
  memory_file_8byte memory_file_8byte_6 (
    .CLOCK(clock_1_out), .DATA_IN(or_5_out), .LOAD(and_17_out), .LOAD_SELECT_1(or_1_out[1]),
    .LOAD_SELECT_0(or_1_out[0]), .READ_SELECT_1(and_62_out[1]), .READ_SELECT_0(and_62_out[0]),
    .RESET(RESET_MEM), .DATA_OUT(memory_file_8byte_6_data_out));
  memory_file_8byte memory_file_8byte_7 (
    .CLOCK(clock_1_out), .DATA_IN(or_5_out), .LOAD(and_16_out), .LOAD_SELECT_1(or_1_out[1]),
    .LOAD_SELECT_0(or_1_out[0]), .READ_SELECT_1(and_62_out[1]), .READ_SELECT_0(and_62_out[0]),
    .RESET(RESET_MEM), .DATA_OUT(memory_file_8byte_7_data_out));
  memory_file_8byte memory_file_8byte_8 (
    .CLOCK(clock_1_out), .DATA_IN(or_5_out), .LOAD(and_15_out), .LOAD_SELECT_1(or_1_out[1]),
    .LOAD_SELECT_0(or_1_out[0]), .READ_SELECT_1(and_62_out[1]), .READ_SELECT_0(and_62_out[0]),
    .RESET(RESET_MEM), .DATA_OUT(memory_file_8byte_8_data_out));
  assign and_62_out = {5{or_9_out[4]}} & mar_5bit_1_out_5;  // AND_Gate and_62, 5 bits wide
  assign and_63_out = mar_5bit_1_out_5 & {5{save_out[4]}};  // AND_Gate and_63, 5 bits wide
  assign or_13_out = and_71_out | and_72_out;  // OR_Gate or_13, 16 bits wide
  and and_64 (and_64_out, and_3_out, and_43_out);
  or or_14 (or_14_out, and_23_out, and_29_out);
  or or_15 (or_15_out, and_24_out, and_30_out);
  or or_16 (or_16_out, and_25_out, and_31_out);
  not not_20 (not_20_out, or_10_out);
  not not_21 (not_21_out, or_11_out);
  not not_22 (not_22_out, or_12_out);
  assign and_65_out = memory_file_8byte_3_data_out & {16{and_57_out[15]}};  // AND_Gate and_65, 16 bits wide
  assign and_66_out = memory_file_8byte_4_data_out & {16{and_56_out[15]}};  // AND_Gate and_66, 16 bits wide
  assign and_67_out = memory_file_8byte_5_data_out & {16{and_55_out[15]}};  // AND_Gate and_67, 16 bits wide
  assign and_68_out = memory_file_8byte_6_data_out & {16{and_54_out[15]}};  // AND_Gate and_68, 16 bits wide
  assign and_69_out = memory_file_8byte_7_data_out & {16{and_53_out[15]}};  // AND_Gate and_69, 16 bits wide
  assign and_70_out = memory_file_8byte_8_data_out & {16{and_52_out[15]}};  // AND_Gate and_70, 16 bits wide
  assign and_71_out = {16{save_out[4]}} & or_20_out;  // AND_Gate and_71, 16 bits wide
  assign and_72_out = or_18_out & {16{or_9_out[4]}};  // AND_Gate and_72, 16 bits wide
  or or_17 (or_17_out, RESET_MEM, and_64_out);
  and and_73 (and_73_out, or_8_out, and_4_out);
  assign or_18_out = and_60_out | and_61_out | and_65_out | and_66_out | and_68_out | and_69_out | and_70_out | and_67_out;  // OR_Gate or_18, 16 bits wide
  ALU_16bit alu_16bit_1 (
    .FA(and_50_out), .FB(and_51_out), .UA(and_48_out), .UB(and_49_out), .DATA_IN_B(or_21_out),
    .DATA_IN_A(or_20_out), .N(alu_16bit_1_c[3]), .Z(alu_16bit_1_c[2]), .V(alu_16bit_1_c[1]),
    .C(alu_16bit_1_c[0]), .DATA_OUT(alu_16bit_1_data_out));
  and and_74 (and_74_out[15], not_20_out, not_21_out, not_22_out);
  and and_75 (and_75_out[15], not_20_out, not_21_out, or_12_out);
  and and_76 (and_76_out[15], not_20_out, or_11_out, not_22_out);
  and and_77 (and_77_out[15], not_20_out, or_11_out, or_12_out);
  and and_78 (and_78_out[15], or_10_out, not_21_out, not_22_out);
  and and_79 (and_79_out[15], or_10_out, not_21_out, or_12_out);
  and and_80 (and_80_out[15], or_10_out, or_11_out, not_22_out);
  and and_81 (and_81_out[15], or_10_out, or_11_out, or_12_out);
  register_16bit register_16bit_2 (
    .CLOCK(clock_1_out), .LOAD(or_7_out), .DATA_IN(or_13_out), .RESET(RESET_MEM),
    .DATA_OUT(register_16bit_2_data_out));
  assign or_19_out = and_85_out | register_16bit_3_data_out;  // OR_Gate or_19, 16 bits wide
  not not_23 (not_23_out, or_14_out);
  and and_82 (and_82_out, and_73_out, or_14_out);
  and and_83 (and_83_out, and_73_out, not_23_out);
  assign and_84_out = register_16bit_2_data_out & {16{save_out[4]}};  // AND_Gate and_84, 16 bits wide
  assign and_85_out = register_16bit_2_data_out & {16{load_out[4]}};  // AND_Gate and_85, 16 bits wide
  assign and_86_out = register_16bit_2_data_out & {16{and_1_out[4]}};  // AND_Gate and_86, 16 bits wide
  register_4bit register_4bit_1 (
    .CLOCK(clock_1_out), .DATA_IN(alu_16bit_1_c), .LOAD(or_17_out),
    .DATA_OUT({out_25, out_26, out_27, out_28}));  // open: in_4
  not not_24 (not_24_out, and_35_out);
  not not_25 (not_25_out, and_36_out);
  not not_26 (not_26_out, and_37_out);
  register_16bit register_16bit_3 (
    .CLOCK(clock_1_out), .LOAD(or_17_out), .DATA_IN(alu_16bit_1_data_out), .RESET(RESET_MEM),
    .DATA_OUT(register_16bit_3_data_out));
  and and_87 (and_87_out[15], not_24_out, not_25_out, not_26_out);
  and and_88 (and_88_out[15], not_24_out, not_25_out, and_37_out);
  and and_89 (and_89_out[15], not_24_out, and_36_out, not_26_out);
  and and_90 (and_90_out[15], not_24_out, and_36_out, and_37_out);
  and and_91 (and_91_out[15], and_35_out, not_25_out, not_26_out);
  and and_92 (and_92_out[15], and_35_out, not_25_out, and_37_out);
  and and_93 (and_93_out[15], and_35_out, and_36_out, not_26_out);
  and and_94 (and_94_out[15], and_35_out, and_36_out, and_37_out);
  register_file_8byte register_file_8byte_1 (
    .CLOCK(clock_1_out), .DATA_IN(or_19_out), .LOAD(and_83_out), .LOAD_SELECT_1(or_15_out),
    .LOAD_SELECT_0(or_16_out), .RESET(RESET_MEM), .OUT_A(register_file_8byte_1_out_a),
    .OUT_B(register_file_8byte_1_out_b), .OUT_C(register_file_8byte_1_out_c),
    .OUT_D(register_file_8byte_1_out_d));
  register_file_8byte register_file_8byte_2 (
    .CLOCK(clock_1_out), .DATA_IN(or_19_out), .LOAD(and_82_out), .LOAD_SELECT_1(or_15_out),
    .LOAD_SELECT_0(or_16_out), .RESET(RESET_MEM), .OUT_A(register_file_8byte_2_out_a),
    .OUT_B(register_file_8byte_2_out_b), .OUT_C(register_file_8byte_2_out_c),
    .OUT_D(register_file_8byte_2_out_d));
  assign and_95_out = register_file_8byte_1_out_a & {16{and_74_out[15]}};  // AND_Gate and_95, 16 bits wide
  assign and_96_out = register_file_8byte_1_out_b & {16{and_75_out[15]}};  // AND_Gate and_96, 16 bits wide
  assign and_97_out = register_file_8byte_1_out_c & {16{and_76_out[15]}};  // AND_Gate and_97, 16 bits wide
  assign and_98_out = register_file_8byte_1_out_d & {16{and_77_out[15]}};  // AND_Gate and_98, 16 bits wide
  assign and_99_out = register_file_8byte_2_out_a & {16{and_78_out[15]}};  // AND_Gate and_99, 16 bits wide
  assign and_100_out = register_file_8byte_2_out_b & {16{and_79_out[15]}};  // AND_Gate and_100, 16 bits wide
  assign and_101_out = register_file_8byte_2_out_c & {16{and_80_out[15]}};  // AND_Gate and_101, 16 bits wide
  assign and_102_out = register_file_8byte_2_out_d & {16{and_81_out[15]}};  // AND_Gate and_102, 16 bits wide
  assign and_103_out = register_file_8byte_1_out_a & {16{and_87_out[15]}};  // AND_Gate and_103, 16 bits wide
  assign and_104_out = register_file_8byte_1_out_b & {16{and_88_out[15]}};  // AND_Gate and_104, 16 bits wide
  assign and_105_out = register_file_8byte_1_out_c & {16{and_89_out[15]}};  // AND_Gate and_105, 16 bits wide
  assign and_106_out = register_file_8byte_1_out_d & {16{and_90_out[15]}};  // AND_Gate and_106, 16 bits wide
  assign and_107_out = register_file_8byte_2_out_a & {16{and_91_out[15]}};  // AND_Gate and_107, 16 bits wide
  assign and_108_out = register_file_8byte_2_out_b & {16{and_92_out[15]}};  // AND_Gate and_108, 16 bits wide
  assign and_109_out = register_file_8byte_2_out_c & {16{and_93_out[15]}};  // AND_Gate and_109, 16 bits wide
  assign and_110_out = register_file_8byte_2_out_d & {16{and_94_out[15]}};  // AND_Gate and_110, 16 bits wide
  assign or_20_out = and_95_out | and_96_out | and_97_out | and_98_out | and_99_out | and_100_out | and_101_out | and_102_out;  // OR_Gate or_20, 16 bits wide
  assign or_21_out = and_103_out | and_104_out | and_105_out | and_106_out | and_107_out | and_108_out | and_109_out | and_110_out;  // OR_Gate or_21, 16 bits wide

  // Notes on the sheet:
  //   FETCH
  //   DECODE
  //   EXECUTE
  //   MEMORY
  //   00-0000-nop
  //   00-0001-jmp
  //   00-0010-jz
  //   00-0011-jnz
  //   00-0100-hlt
  //   01-0000-load
  //   01-0001-save
  //   10-0000-add
  //   10-0001-sub
  //   10-0010-inc
  //   10-0011-dec
  //   10-0100-and
  //   10-0101-or
  //   10-0110-xor
  //   10-0111-not
  //   10-1000-lsl
  //   10-1001-lsr
  //   10-1010-null
  //   10-1011-null
  //   10-1100-psa
  //   10-1101-psb
  //   10-1110-null
  //   10-1111-null
  //   manual_write
  //   (00-0101)-(00-1111)-null
  //   (01-0010)-(01-1111)-null
  //   (11-0000)-(11-1111)-null
  //   manual_input
  //   mem_write
  //   mem_read
  //   reg1-to
  //   reg2-from
  //   JMP
  //   JZ
  //   JNZ
  //   HLT
  //   INSTRUCTION_REGISTER
  //   mem_load
  //   PROGRAM_COUNTER
  //   REG2
  //   REG1
  //   UNIT
  //   FUNC
  //   unit_enable
  //   MAR
  //   made_by_Lawrence_shuttleworth
  //   in_mem
  //   ALU
  //   MDR
  //   out_mem
  //   ALU_OUT
  //   in_IR
  //   IN_GPR
  //   FLAG_REGISTER
  //   accumulator
  //   GPR
  //   OUT_GPR
endmodule

module memory_file_8byte (
  input  CLOCK,
  input  [15:0] DATA_IN,
  input  LOAD,
  input  LOAD_SELECT_1,
  input  LOAD_SELECT_0,
  input  READ_SELECT_1,
  input  READ_SELECT_0,
  input  RESET,
  output [15:0] DATA_OUT
);

  wire and_3_out, and_4_out, and_5_out, and_6_out, and_7_out, and_8_out, and_9_out, and_10_out, and_11_out,
       and_12_out, and_13_out, and_14_out, and_15_out, and_16_out, and_17_out, and_18_out, and_19_out,
       and_20_out, and_21_out, and_22_out, and_23_out, and_24_out, and_25_out, and_26_out, and_27_out,
       and_28_out, and_29_out, and_30_out, and_31_out, and_32_out, and_33_out, and_34_out, and_35_out,
       and_36_out, and_37_out, and_38_out, and_39_out, and_40_out, and_41_out, and_42_out, and_43_out,
       and_44_out, and_45_out, and_46_out, and_47_out, and_48_out, and_49_out, and_50_out, and_51_out,
       and_52_out, and_53_out, and_54_out, and_55_out, and_56_out, and_57_out, and_58_out, and_59_out,
       and_60_out, and_61_out, and_62_out, and_63_out, and_64_out, and_65_out, and_66_out, and_67_out,
       and_68_out, and_69_out, and_70_out, and_71_out, and_72_out, and_73_out, and_74_out, and_75_out,
       and_76_out, and_77_out, and_78_out, and_79_out, and_80_out, and_81_out, and_82_out, and_83_out,
       and_84_out, and_85_out, and_86_out, and_87_out, and_88_out, and_89_out, and_90_out, and_91_out,
       and_92_out, and_93_out, and_94_out, and_95_out, and_96_out, and_97_out, and_98_out, and_99_out,
       and_100_out, and_101_out, and_102_out, and_103_out, and_104_out, and_105_out, and_106_out,
       and_107_out, and_108_out, and_109_out, and_110_out, and_111_out, and_112_out, and_113_out,
       and_114_out, and_115_out, and_116_out, and_117_out, and_118_out, and_119_out, and_120_out,
       and_121_out, and_122_out, and_123_out, and_124_out, and_125_out, and_126_out, and_127_out,
       and_128_out, and_129_out, and_130_out, and_131_out, and_132_out, and_133_out, and_134_out,
       and_135_out, and_136_out, and_137_out, and_138_out, and_139_out, and_140_out, and_141_out,
       and_142_out, and_143_out, and_144_out, and_145_out, and_146_out, and_147_out, and_148_out,
       and_149_out, and_150_out, and_151_out, and_152_out, and_153_out, and_154_out, and_155_out,
       and_156_out, and_157_out, and_158_out, and_159_out, and_160_out, and_161_out, and_162_out,
       and_163_out, and_164_out, and_165_out, and_166_out, and_167_out, and_168_out, and_169_out,
       and_170_out, and_171_out, and_172_out, and_173_out, and_174_out, and_175_out, and_176_out,
       and_177_out, and_178_out, and_179_out, and_180_out, and_181_out, and_182_out, and_183_out,
       and_184_out, and_185_out, and_186_out, and_187_out, and_188_out, and_189_out, and_190_out,
       and_191_out, and_192_out, and_193_out, and_194_out, and_195_out, and_196_out, and_197_out,
       and_198_out, and_199_out, and_200_out, and_201_out, and_202_out, nand_1_out, nand_2_out, nand_3_out,
       nand_4_out, nand_5_out, nand_6_out, nand_7_out, nand_8_out, nand_9_out, nand_10_out, nand_11_out,
       nand_12_out, nand_13_out, nand_14_out, nand_15_out, nand_16_out, nand_17_out, nand_18_out,
       nand_19_out, nand_20_out, nand_21_out, nand_22_out, nand_23_out, nand_24_out, nand_25_out,
       nand_26_out, nand_27_out, nand_28_out, nand_29_out, nand_30_out, nand_31_out, nand_32_out,
       nand_33_out, nand_34_out, nand_35_out, nand_36_out, nand_37_out, nand_38_out, nand_39_out,
       nand_40_out, nand_41_out, nand_42_out, nand_43_out, nand_44_out, nand_45_out, nand_46_out,
       nand_47_out, nand_48_out, nand_49_out, nand_50_out, nand_51_out, nand_52_out, nand_53_out,
       nand_54_out, nand_55_out, nand_56_out, nand_57_out, nand_58_out, nand_59_out, nand_60_out,
       nand_61_out, nand_62_out, nand_63_out, nand_64_out, nand_65_out, nand_66_out, nand_67_out,
       nand_68_out, nand_69_out, nand_70_out, nand_71_out, nand_72_out, nand_73_out, nand_74_out,
       nand_75_out, nand_76_out, nand_77_out, nand_78_out, nand_79_out, nand_80_out, nand_81_out,
       nand_82_out, nand_83_out, nand_84_out, nand_85_out, nand_86_out, nand_87_out, nand_88_out,
       nand_89_out, nand_90_out, nand_91_out, nand_92_out, nand_93_out, nand_94_out, nand_95_out,
       nand_96_out, nand_97_out, nand_98_out, nand_99_out, nand_100_out, nand_101_out, nand_102_out,
       nand_103_out, nand_104_out, nand_105_out, nand_106_out, nand_107_out, nand_108_out, nand_109_out,
       nand_110_out, nand_111_out, nand_112_out, nand_113_out, nand_114_out, nand_115_out, nand_116_out,
       nand_117_out, nand_118_out, nand_119_out, nand_120_out, nand_121_out, nand_122_out, nand_123_out,
       nand_124_out, nand_125_out, nand_126_out, nand_127_out, nand_128_out, nand_129_out, nand_130_out,
       nand_131_out, nand_132_out, nand_133_out, nand_134_out, nand_135_out, nand_136_out, nand_137_out,
       nand_138_out, nand_139_out, nand_140_out, nand_141_out, nand_142_out, nand_143_out, nand_144_out,
       nand_145_out, nand_146_out, nand_147_out, nand_148_out, nand_149_out, nand_150_out, nand_151_out,
       nand_152_out, nand_153_out, nand_154_out, nand_155_out, nand_156_out, nand_157_out, nand_158_out,
       nand_159_out, nand_160_out, nand_161_out, nand_162_out, nand_163_out, nand_164_out, nand_165_out,
       nand_166_out, nand_167_out, nand_168_out, nand_169_out, nand_170_out, nand_171_out, nand_172_out,
       nand_173_out, nand_174_out, nand_175_out, nand_176_out, nand_177_out, nand_178_out, nand_179_out,
       nand_180_out, nand_181_out, nand_182_out, nand_183_out, nand_184_out, nand_185_out, nand_186_out,
       nand_187_out, nand_188_out, nand_189_out, nand_190_out, nand_191_out, nand_192_out, nand_193_out,
       nand_194_out, nand_195_out, nand_196_out, nand_197_out, nand_198_out, nand_199_out, nand_200_out,
       nand_201_out, nand_202_out, nand_203_out, nand_204_out, nand_205_out, nand_206_out, nand_207_out,
       nand_208_out, nand_209_out, nand_210_out, nand_211_out, nand_212_out, nand_213_out, nand_214_out,
       nand_215_out, nand_216_out, nand_217_out, nand_218_out, nand_219_out, nand_220_out, nand_221_out,
       nand_222_out, nand_223_out, nand_224_out, nand_225_out, nand_226_out, nand_227_out, nand_228_out,
       nand_229_out, nand_230_out, nand_231_out, nand_232_out, nand_233_out, nand_234_out, nand_235_out,
       nand_236_out, nand_237_out, nand_238_out, nand_239_out, nand_240_out, nand_241_out, nand_242_out,
       nand_243_out, nand_244_out, nand_245_out, nand_246_out, nand_247_out, nand_248_out, nand_249_out,
       nand_250_out, nand_251_out, nand_252_out, nand_253_out, nand_254_out, nand_255_out, nand_256_out,
       nand_257_out, nand_258_out, nand_259_out, nand_260_out, nand_261_out, nand_262_out, nand_263_out,
       nand_264_out, nand_265_out, nand_266_out, nand_267_out, nand_268_out, nand_269_out, nand_270_out,
       nand_271_out, nand_272_out, nand_273_out, nand_274_out, nand_275_out, nand_276_out, nand_277_out,
       nand_278_out, nand_279_out, nand_280_out, nand_281_out, nand_282_out, nand_283_out, nand_284_out,
       nand_285_out, nand_286_out, nand_287_out, nand_288_out, nand_289_out, nand_290_out, nand_291_out,
       nand_292_out, nand_293_out, nand_294_out, nand_295_out, nand_296_out, nand_297_out, nand_298_out,
       nand_299_out, nand_300_out, nand_301_out, nand_302_out, nand_303_out, nand_304_out, nand_305_out,
       nand_306_out, nand_307_out, nand_308_out, nand_309_out, nand_310_out, nand_311_out, nand_312_out,
       nand_313_out, nand_314_out, nand_315_out, nand_316_out, nand_317_out, nand_318_out, nand_319_out,
       nand_320_out, nand_321_out, nand_322_out, nand_323_out, nand_324_out, nand_325_out, nand_326_out,
       nand_327_out, nand_328_out, nand_329_out, nand_330_out, nand_331_out, nand_332_out, nand_333_out,
       nand_334_out, nand_335_out, nand_336_out, nand_337_out, nand_338_out, nand_339_out, nand_340_out,
       nand_341_out, nand_342_out, nand_343_out, nand_344_out, nand_345_out, nand_346_out, nand_347_out,
       nand_348_out, nand_349_out, nand_350_out, nand_351_out, nand_352_out, nand_353_out, nand_354_out,
       nand_355_out, nand_356_out, nand_357_out, nand_358_out, nand_359_out, nand_360_out, nand_361_out,
       nand_362_out, nand_363_out, nand_364_out, nand_365_out, nand_366_out, nand_367_out, nand_368_out,
       nand_369_out, nand_370_out, nand_371_out, nand_372_out, nand_373_out, nand_374_out, nand_375_out,
       nand_376_out, nand_377_out, nand_378_out, nand_379_out, nand_380_out, nand_381_out, nand_382_out,
       nand_383_out, nand_384_out, nand_385_out, nand_386_out, nand_387_out, nand_388_out, nand_389_out,
       nand_390_out, nand_391_out, nand_392_out, nand_393_out, nand_394_out, nand_395_out, nand_396_out,
       nand_397_out, nand_398_out, nand_399_out, nand_400_out, nand_401_out, nand_402_out, nand_403_out,
       nand_404_out, nand_405_out, nand_406_out, nand_407_out, nand_408_out, nand_409_out, nand_410_out,
       nand_411_out, nand_412_out, nand_413_out, nand_414_out, nand_415_out, nand_416_out, nand_417_out,
       nand_418_out, nand_419_out, nand_420_out, nand_421_out, nand_422_out, nand_423_out, nand_424_out,
       nand_425_out, nand_426_out, nand_427_out, nand_428_out, nand_429_out, nand_430_out, nand_431_out,
       nand_432_out, nand_433_out, nand_434_out, nand_435_out, nand_436_out, nand_437_out, nand_438_out,
       nand_439_out, nand_440_out, nand_441_out, nand_442_out, nand_443_out, nand_444_out, nand_445_out,
       nand_446_out, nand_447_out, nand_448_out, nand_449_out, nand_450_out, nand_451_out, nand_452_out,
       nand_453_out, nand_454_out, nand_455_out, nand_456_out, nand_457_out, nand_458_out, nand_459_out,
       nand_460_out, nand_461_out, nand_462_out, nand_463_out, nand_464_out, nand_465_out, nand_466_out,
       nand_467_out, nand_468_out, nand_469_out, nand_470_out, nand_471_out, nand_472_out, nand_473_out,
       nand_474_out, nand_475_out, nand_476_out, nand_477_out, nand_478_out, nand_479_out, nand_480_out,
       nand_481_out, nand_482_out, nand_483_out, nand_484_out, nand_485_out, nand_486_out, nand_487_out,
       nand_488_out, nand_489_out, nand_490_out, nand_491_out, nand_492_out, nand_493_out, nand_494_out,
       nand_495_out, nand_496_out, nand_497_out, nand_498_out, nand_499_out, nand_500_out, nand_501_out,
       nand_502_out, nand_503_out, nand_504_out, nand_505_out, nand_506_out, nand_507_out, nand_508_out,
       nand_509_out, nand_510_out, nand_511_out, nand_512_out, not_2_out, not_3_out, not_4_out, not_5_out,
       not_6_out, not_7_out, not_8_out, not_9_out, not_10_out, not_11_out, not_12_out, not_13_out,
       not_14_out, not_15_out, not_16_out, not_17_out, not_18_out, not_19_out, not_20_out, not_21_out,
       not_22_out, not_23_out, not_24_out, not_25_out, not_26_out, not_27_out, not_28_out, not_29_out,
       not_30_out, not_31_out, not_32_out, not_33_out, not_34_out, not_35_out, not_36_out, not_37_out,
       not_38_out, not_39_out, not_40_out, not_41_out, not_42_out, not_43_out, not_44_out, not_45_out,
       not_46_out, not_47_out, not_48_out, not_49_out, not_50_out, not_51_out, not_52_out, not_53_out,
       not_54_out, not_55_out, not_56_out, not_57_out, not_58_out, not_59_out, not_60_out, not_61_out,
       not_62_out, not_63_out, not_64_out, not_65_out, not_66_out, not_67_out, not_68_out, not_69_out,
       not_70_out, not_71_out, not_72_out, not_73_out, not_74_out, not_75_out, not_76_out, not_77_out,
       not_78_out, not_79_out, not_80_out, not_81_out, not_82_out, not_83_out, not_84_out, not_85_out,
       not_86_out, not_87_out, not_88_out, not_89_out, not_90_out, not_91_out, not_92_out, not_93_out,
       not_94_out, not_95_out, not_96_out, not_97_out, not_98_out, not_99_out, not_100_out, not_101_out,
       not_102_out, not_103_out, not_104_out, not_105_out, not_106_out, not_107_out, not_108_out,
       not_109_out, not_110_out, not_111_out, not_112_out, not_113_out, not_114_out, not_115_out,
       not_116_out, not_117_out, not_118_out, not_119_out, not_120_out, not_121_out, not_122_out,
       not_123_out, not_124_out, not_125_out, not_126_out, not_127_out, not_128_out, not_129_out,
       not_130_out, not_131_out, not_132_out, not_133_out, not_134_out, not_135_out, not_136_out,
       not_137_out, not_138_out, not_139_out, not_140_out, not_141_out, not_142_out, not_143_out,
       not_144_out, not_145_out, not_146_out, not_147_out, not_148_out, not_149_out, not_150_out,
       not_151_out, not_152_out, not_153_out, not_154_out, not_155_out, not_156_out, not_157_out,
       not_158_out, not_159_out, not_160_out, not_161_out, not_162_out, not_163_out, not_164_out,
       not_165_out, not_166_out, not_167_out, not_168_out, not_169_out, not_170_out, not_171_out,
       not_172_out, not_173_out, not_174_out, not_175_out, not_176_out, not_177_out, not_178_out,
       not_179_out, not_180_out, not_181_out, not_182_out, not_183_out, not_184_out, not_185_out,
       not_186_out, not_187_out, not_188_out, not_189_out, not_190_out, not_191_out, not_192_out,
       not_193_out, not_194_out, not_195_out, not_196_out, not_197_out, not_198_out, not_199_out,
       not_200_out, not_201_out, not_202_out, not_203_out, not_204_out, not_205_out, not_206_out,
       not_207_out, not_208_out, not_209_out, not_210_out, not_211_out, not_212_out, not_213_out,
       not_214_out, not_215_out, not_216_out, not_217_out, not_218_out, not_219_out, not_220_out,
       not_221_out, not_222_out, not_223_out, not_224_out, not_225_out, not_226_out, not_227_out,
       not_228_out, not_229_out, not_230_out, not_231_out, not_232_out, not_233_out, not_234_out,
       not_235_out, not_236_out, not_237_out, not_238_out, not_239_out, not_240_out, not_241_out,
       not_242_out, not_243_out, not_244_out, not_245_out, not_246_out, not_247_out, not_248_out,
       not_249_out, not_250_out, not_251_out, not_252_out, not_253_out, not_254_out, not_255_out,
       not_256_out, not_257_out, not_258_out, not_259_out, not_260_out, not_261_out, or_2_out, or_3_out,
       or_4_out, or_5_out, or_6_out, or_7_out, or_8_out, or_9_out, or_10_out, or_11_out, or_12_out,
       or_13_out, or_14_out, or_15_out, or_16_out, or_17_out, or_18_out, or_19_out, or_20_out, or_21_out,
       or_22_out, or_23_out, or_24_out, or_25_out, or_26_out, or_27_out, or_28_out, or_29_out, or_30_out,
       or_31_out, or_32_out, or_33_out, or_34_out, or_35_out, or_36_out, or_37_out, or_38_out, or_39_out,
       or_40_out, or_41_out, or_42_out, or_43_out, or_44_out, or_45_out, or_46_out, or_47_out, or_48_out,
       or_49_out, or_50_out, or_51_out, or_52_out, or_53_out, or_54_out, or_55_out, or_56_out, or_57_out,
       or_58_out, or_59_out, or_60_out, or_61_out, or_62_out, or_63_out, or_64_out, or_65_out, or_66_out,
       or_67_out, or_68_out, or_69_out, or_70_out, or_71_out, or_72_out, or_73_out, or_74_out, or_75_out,
       or_76_out, or_77_out, or_78_out, or_79_out, or_80_out, or_81_out, or_82_out, or_83_out, or_84_out,
       or_85_out, or_86_out, or_87_out, or_88_out, or_89_out, or_90_out, or_91_out, or_92_out, or_93_out,
       or_94_out, or_95_out, or_96_out, or_97_out, or_98_out, or_99_out, or_100_out, or_101_out, or_102_out;
  wire [15:0] and_1_out, and_2_out, not_1_out, or_1_out;

  assign and_1_out = {16{RESET}} & {16{1'b0}};  // AND_Gate and_1, 16 bits wide
  assign or_1_out = and_1_out | and_2_out;  // OR_Gate or_1, 16 bits wide
  assign and_2_out = not_1_out & DATA_IN;  // AND_Gate and_2, 16 bits wide
  assign not_1_out = ~{16{RESET}};  // NOT_Gate not_1, 16 bits wide
  or or_2 (or_2_out, RESET, LOAD);
  not not_2 (not_2_out, or_19_out);
  not not_3 (not_3_out, or_19_out);
  not not_4 (not_4_out, or_19_out);
  not not_5 (not_5_out, or_19_out);
  not not_6 (not_6_out, or_19_out);
  not not_7 (not_7_out, or_19_out);
  not not_8 (not_8_out, or_19_out);
  not not_9 (not_9_out, or_19_out);
  not not_10 (not_10_out, or_19_out);
  not not_11 (not_11_out, or_19_out);
  not not_12 (not_12_out, or_19_out);
  not not_13 (not_13_out, or_19_out);
  not not_14 (not_14_out, or_19_out);
  not not_15 (not_15_out, or_19_out);
  not not_16 (not_16_out, or_19_out);
  not not_17 (not_17_out, or_19_out);
  and and_3 (and_3_out, or_1_out[15], or_19_out);
  and and_4 (and_4_out, nand_97_out, not_2_out);
  and and_5 (and_5_out, or_1_out[14], or_19_out);
  and and_6 (and_6_out, nand_99_out, not_3_out);
  and and_7 (and_7_out, or_1_out[13], or_19_out);
  and and_8 (and_8_out, nand_101_out, not_4_out);
  and and_9 (and_9_out, or_1_out[12], or_19_out);
  and and_10 (and_10_out, nand_103_out, not_5_out);
  and and_11 (and_11_out, or_1_out[11], or_19_out);
  and and_12 (and_12_out, nand_105_out, not_6_out);
  and and_13 (and_13_out, or_1_out[10], or_19_out);
  and and_14 (and_14_out, nand_107_out, not_7_out);
  and and_15 (and_15_out, or_1_out[9], or_19_out);
  and and_16 (and_16_out, nand_109_out, not_8_out);
  and and_17 (and_17_out, or_1_out[8], or_19_out);
  and and_18 (and_18_out, nand_111_out, not_9_out);
  and and_19 (and_19_out, or_1_out[7], or_19_out);
  and and_20 (and_20_out, nand_113_out, not_10_out);
  and and_21 (and_21_out, or_1_out[6], or_19_out);
  and and_22 (and_22_out, nand_115_out, not_11_out);
  and and_23 (and_23_out, or_1_out[5], or_19_out);
  and and_24 (and_24_out, nand_117_out, not_12_out);
  and and_25 (and_25_out, or_1_out[4], or_19_out);
  and and_26 (and_26_out, nand_119_out, not_13_out);
  and and_27 (and_27_out, or_1_out[3], or_19_out);
  and and_28 (and_28_out, nand_121_out, not_14_out);
  and and_29 (and_29_out, or_1_out[2], or_19_out);
  and and_30 (and_30_out, nand_123_out, not_15_out);
  and and_31 (and_31_out, or_1_out[1], or_19_out);
  and and_32 (and_32_out, nand_125_out, not_16_out);
  and and_33 (and_33_out, or_1_out[0], or_19_out);
  and and_34 (and_34_out, nand_127_out, not_17_out);
  not not_18 (not_18_out, LOAD_SELECT_1);
  not not_19 (not_19_out, LOAD_SELECT_0);
  not not_20 (not_20_out, READ_SELECT_1);
  not not_21 (not_21_out, READ_SELECT_0);
  or or_3 (or_3_out, and_3_out, and_4_out);
  or or_4 (or_4_out, and_5_out, and_6_out);
  or or_5 (or_5_out, and_7_out, and_8_out);
  or or_6 (or_6_out, and_9_out, and_10_out);
  or or_7 (or_7_out, and_11_out, and_12_out);
  or or_8 (or_8_out, and_13_out, and_14_out);
  or or_9 (or_9_out, and_15_out, and_16_out);
  or or_10 (or_10_out, and_17_out, and_18_out);
  or or_11 (or_11_out, and_19_out, and_20_out);
  or or_12 (or_12_out, and_21_out, and_22_out);
  or or_13 (or_13_out, and_23_out, and_24_out);
  or or_14 (or_14_out, and_25_out, and_26_out);
  or or_15 (or_15_out, and_27_out, and_28_out);
  or or_16 (or_16_out, and_29_out, and_30_out);
  or or_17 (or_17_out, and_31_out, and_32_out);
  or or_18 (or_18_out, and_33_out, and_34_out);
  and and_35 (and_35_out, LOAD_SELECT_1, or_2_out, LOAD_SELECT_0);
  and and_36 (and_36_out, LOAD_SELECT_1, or_2_out, not_19_out);
  and and_37 (and_37_out, not_18_out, or_2_out, LOAD_SELECT_0);
  and and_38 (and_38_out, not_18_out, or_2_out, not_19_out);
  or or_19 (or_19_out, and_38_out, RESET);
  and and_39 (and_39_out, READ_SELECT_1, READ_SELECT_0);
  and and_40 (and_40_out, READ_SELECT_1, not_21_out);
  and and_41 (and_41_out, not_20_out, READ_SELECT_0);
  and and_42 (and_42_out, not_20_out, not_21_out);
  nand nand_1 (nand_1_out, or_3_out, CLOCK);
  nand nand_2 (nand_2_out, CLOCK, not_22_out);
  not not_22 (not_22_out, or_3_out);
  nand nand_3 (nand_3_out, or_4_out, CLOCK);
  nand nand_4 (nand_4_out, CLOCK, not_23_out);
  not not_23 (not_23_out, or_4_out);
  nand nand_5 (nand_5_out, or_5_out, CLOCK);
  nand nand_6 (nand_6_out, CLOCK, not_24_out);
  not not_24 (not_24_out, or_5_out);
  nand nand_7 (nand_7_out, or_6_out, CLOCK);
  nand nand_8 (nand_8_out, CLOCK, not_25_out);
  not not_25 (not_25_out, or_6_out);
  nand nand_9 (nand_9_out, or_7_out, CLOCK);
  nand nand_10 (nand_10_out, CLOCK, not_26_out);
  not not_26 (not_26_out, or_7_out);
  nand nand_11 (nand_11_out, or_8_out, CLOCK);
  nand nand_12 (nand_12_out, CLOCK, not_27_out);
  not not_27 (not_27_out, or_8_out);
  nand nand_13 (nand_13_out, or_9_out, CLOCK);
  nand nand_14 (nand_14_out, CLOCK, not_28_out);
  not not_28 (not_28_out, or_9_out);
  nand nand_15 (nand_15_out, or_10_out, CLOCK);
  nand nand_16 (nand_16_out, CLOCK, not_29_out);
  not not_29 (not_29_out, or_10_out);
  nand nand_17 (nand_17_out, or_11_out, CLOCK);
  nand nand_18 (nand_18_out, CLOCK, not_30_out);
  not not_30 (not_30_out, or_11_out);
  nand nand_19 (nand_19_out, or_12_out, CLOCK);
  nand nand_20 (nand_20_out, CLOCK, not_31_out);
  not not_31 (not_31_out, or_12_out);
  nand nand_21 (nand_21_out, or_13_out, CLOCK);
  nand nand_22 (nand_22_out, CLOCK, not_32_out);
  not not_32 (not_32_out, or_13_out);
  nand nand_23 (nand_23_out, or_14_out, CLOCK);
  nand nand_24 (nand_24_out, CLOCK, not_33_out);
  not not_33 (not_33_out, or_14_out);
  nand nand_25 (nand_25_out, or_15_out, CLOCK);
  nand nand_26 (nand_26_out, CLOCK, not_34_out);
  not not_34 (not_34_out, or_15_out);
  nand nand_27 (nand_27_out, or_16_out, CLOCK);
  nand nand_28 (nand_28_out, CLOCK, not_35_out);
  not not_35 (not_35_out, or_16_out);
  nand nand_29 (nand_29_out, or_17_out, CLOCK);
  nand nand_30 (nand_30_out, CLOCK, not_36_out);
  not not_36 (not_36_out, or_17_out);
  nand nand_31 (nand_31_out, or_18_out, CLOCK);
  nand nand_32 (nand_32_out, CLOCK, not_37_out);
  not not_37 (not_37_out, or_18_out);
  or or_20 (or_20_out, and_35_out, RESET);
  or or_21 (or_21_out, and_36_out, RESET);
  or or_22 (or_22_out, and_37_out, RESET);
  nand nand_33 (nand_33_out, nand_1_out, nand_34_out);
  nand nand_34 (nand_34_out, nand_33_out, nand_2_out);
  not not_38 (not_38_out, CLOCK);
  nand nand_35 (nand_35_out, nand_3_out, nand_36_out);
  nand nand_36 (nand_36_out, nand_35_out, nand_4_out);
  not not_39 (not_39_out, CLOCK);
  nand nand_37 (nand_37_out, nand_5_out, nand_38_out);
  nand nand_38 (nand_38_out, nand_37_out, nand_6_out);
  not not_40 (not_40_out, CLOCK);
  nand nand_39 (nand_39_out, nand_7_out, nand_40_out);
  nand nand_40 (nand_40_out, nand_39_out, nand_8_out);
  not not_41 (not_41_out, CLOCK);
  nand nand_41 (nand_41_out, nand_9_out, nand_42_out);
  nand nand_42 (nand_42_out, nand_41_out, nand_10_out);
  not not_42 (not_42_out, CLOCK);
  nand nand_43 (nand_43_out, nand_11_out, nand_44_out);
  nand nand_44 (nand_44_out, nand_43_out, nand_12_out);
  not not_43 (not_43_out, CLOCK);
  nand nand_45 (nand_45_out, nand_13_out, nand_46_out);
  nand nand_46 (nand_46_out, nand_45_out, nand_14_out);
  not not_44 (not_44_out, CLOCK);
  nand nand_47 (nand_47_out, nand_15_out, nand_48_out);
  nand nand_48 (nand_48_out, nand_47_out, nand_16_out);
  not not_45 (not_45_out, CLOCK);
  nand nand_49 (nand_49_out, nand_17_out, nand_50_out);
  nand nand_50 (nand_50_out, nand_49_out, nand_18_out);
  not not_46 (not_46_out, CLOCK);
  nand nand_51 (nand_51_out, nand_19_out, nand_52_out);
  nand nand_52 (nand_52_out, nand_51_out, nand_20_out);
  not not_47 (not_47_out, CLOCK);
  nand nand_53 (nand_53_out, nand_21_out, nand_54_out);
  nand nand_54 (nand_54_out, nand_53_out, nand_22_out);
  not not_48 (not_48_out, CLOCK);
  nand nand_55 (nand_55_out, nand_23_out, nand_56_out);
  nand nand_56 (nand_56_out, nand_55_out, nand_24_out);
  not not_49 (not_49_out, CLOCK);
  nand nand_57 (nand_57_out, nand_25_out, nand_58_out);
  nand nand_58 (nand_58_out, nand_57_out, nand_26_out);
  not not_50 (not_50_out, CLOCK);
  nand nand_59 (nand_59_out, nand_27_out, nand_60_out);
  nand nand_60 (nand_60_out, nand_59_out, nand_28_out);
  not not_51 (not_51_out, CLOCK);
  nand nand_61 (nand_61_out, nand_29_out, nand_62_out);
  nand nand_62 (nand_62_out, nand_61_out, nand_30_out);
  not not_52 (not_52_out, CLOCK);
  nand nand_63 (nand_63_out, nand_31_out, nand_64_out);
  nand nand_64 (nand_64_out, nand_63_out, nand_32_out);
  not not_53 (not_53_out, CLOCK);
  not not_54 (not_54_out, nand_33_out);
  not not_55 (not_55_out, nand_35_out);
  not not_56 (not_56_out, nand_37_out);
  not not_57 (not_57_out, nand_39_out);
  not not_58 (not_58_out, nand_41_out);
  not not_59 (not_59_out, nand_43_out);
  not not_60 (not_60_out, nand_45_out);
  not not_61 (not_61_out, nand_47_out);
  not not_62 (not_62_out, nand_49_out);
  not not_63 (not_63_out, nand_51_out);
  not not_64 (not_64_out, nand_53_out);
  not not_65 (not_65_out, nand_55_out);
  not not_66 (not_66_out, nand_57_out);
  not not_67 (not_67_out, nand_59_out);
  not not_68 (not_68_out, nand_61_out);
  not not_69 (not_69_out, nand_63_out);
  nand nand_65 (nand_65_out, nand_33_out, not_38_out);
  nand nand_66 (nand_66_out, not_38_out, not_54_out);
  nand nand_67 (nand_67_out, nand_35_out, not_39_out);
  nand nand_68 (nand_68_out, not_39_out, not_55_out);
  nand nand_69 (nand_69_out, nand_37_out, not_40_out);
  nand nand_70 (nand_70_out, not_40_out, not_56_out);
  nand nand_71 (nand_71_out, nand_39_out, not_41_out);
  nand nand_72 (nand_72_out, not_41_out, not_57_out);
  nand nand_73 (nand_73_out, nand_41_out, not_42_out);
  nand nand_74 (nand_74_out, not_42_out, not_58_out);
  nand nand_75 (nand_75_out, nand_43_out, not_43_out);
  nand nand_76 (nand_76_out, not_43_out, not_59_out);
  nand nand_77 (nand_77_out, nand_45_out, not_44_out);
  nand nand_78 (nand_78_out, not_44_out, not_60_out);
  nand nand_79 (nand_79_out, nand_47_out, not_45_out);
  nand nand_80 (nand_80_out, not_45_out, not_61_out);
  nand nand_81 (nand_81_out, nand_49_out, not_46_out);
  nand nand_82 (nand_82_out, not_46_out, not_62_out);
  nand nand_83 (nand_83_out, nand_51_out, not_47_out);
  nand nand_84 (nand_84_out, not_47_out, not_63_out);
  nand nand_85 (nand_85_out, nand_53_out, not_48_out);
  nand nand_86 (nand_86_out, not_48_out, not_64_out);
  nand nand_87 (nand_87_out, nand_55_out, not_49_out);
  nand nand_88 (nand_88_out, not_49_out, not_65_out);
  nand nand_89 (nand_89_out, nand_57_out, not_50_out);
  nand nand_90 (nand_90_out, not_50_out, not_66_out);
  nand nand_91 (nand_91_out, nand_59_out, not_51_out);
  nand nand_92 (nand_92_out, not_51_out, not_67_out);
  nand nand_93 (nand_93_out, nand_61_out, not_52_out);
  nand nand_94 (nand_94_out, not_52_out, not_68_out);
  nand nand_95 (nand_95_out, nand_63_out, not_53_out);
  nand nand_96 (nand_96_out, not_53_out, not_69_out);
  nand nand_97 (nand_97_out, nand_65_out, nand_98_out);
  nand nand_98 (nand_98_out, nand_97_out, nand_66_out);
  nand nand_99 (nand_99_out, nand_67_out, nand_100_out);
  nand nand_100 (nand_100_out, nand_99_out, nand_68_out);
  nand nand_101 (nand_101_out, nand_69_out, nand_102_out);
  nand nand_102 (nand_102_out, nand_101_out, nand_70_out);
  nand nand_103 (nand_103_out, nand_71_out, nand_104_out);
  nand nand_104 (nand_104_out, nand_103_out, nand_72_out);
  nand nand_105 (nand_105_out, nand_73_out, nand_106_out);
  nand nand_106 (nand_106_out, nand_105_out, nand_74_out);
  nand nand_107 (nand_107_out, nand_75_out, nand_108_out);
  nand nand_108 (nand_108_out, nand_107_out, nand_76_out);
  nand nand_109 (nand_109_out, nand_77_out, nand_110_out);
  nand nand_110 (nand_110_out, nand_109_out, nand_78_out);
  nand nand_111 (nand_111_out, nand_79_out, nand_112_out);
  nand nand_112 (nand_112_out, nand_111_out, nand_80_out);
  nand nand_113 (nand_113_out, nand_81_out, nand_114_out);
  nand nand_114 (nand_114_out, nand_113_out, nand_82_out);
  nand nand_115 (nand_115_out, nand_83_out, nand_116_out);
  nand nand_116 (nand_116_out, nand_115_out, nand_84_out);
  nand nand_117 (nand_117_out, nand_85_out, nand_118_out);
  nand nand_118 (nand_118_out, nand_117_out, nand_86_out);
  nand nand_119 (nand_119_out, nand_87_out, nand_120_out);
  nand nand_120 (nand_120_out, nand_119_out, nand_88_out);
  nand nand_121 (nand_121_out, nand_89_out, nand_122_out);
  nand nand_122 (nand_122_out, nand_121_out, nand_90_out);
  nand nand_123 (nand_123_out, nand_91_out, nand_124_out);
  nand nand_124 (nand_124_out, nand_123_out, nand_92_out);
  nand nand_125 (nand_125_out, nand_93_out, nand_126_out);
  nand nand_126 (nand_126_out, nand_125_out, nand_94_out);
  nand nand_127 (nand_127_out, nand_95_out, nand_128_out);
  nand nand_128 (nand_128_out, nand_127_out, nand_96_out);
  and and_43 (and_43_out, nand_97_out, and_42_out);
  and and_44 (and_44_out, nand_99_out, and_42_out);
  and and_45 (and_45_out, nand_101_out, and_42_out);
  and and_46 (and_46_out, nand_103_out, and_42_out);
  and and_47 (and_47_out, nand_105_out, and_42_out);
  and and_48 (and_48_out, nand_107_out, and_42_out);
  and and_49 (and_49_out, nand_109_out, and_42_out);
  and and_50 (and_50_out, nand_111_out, and_42_out);
  and and_51 (and_51_out, nand_113_out, and_42_out);
  and and_52 (and_52_out, nand_115_out, and_42_out);
  and and_53 (and_53_out, nand_117_out, and_42_out);
  and and_54 (and_54_out, nand_119_out, and_42_out);
  and and_55 (and_55_out, nand_121_out, and_42_out);
  and and_56 (and_56_out, nand_123_out, and_42_out);
  and and_57 (and_57_out, nand_125_out, and_42_out);
  and and_58 (and_58_out, nand_127_out, and_42_out);
  not not_70 (not_70_out, or_22_out);
  not not_71 (not_71_out, or_22_out);
  not not_72 (not_72_out, or_22_out);
  not not_73 (not_73_out, or_22_out);
  not not_74 (not_74_out, or_22_out);
  not not_75 (not_75_out, or_22_out);
  not not_76 (not_76_out, or_22_out);
  not not_77 (not_77_out, or_22_out);
  not not_78 (not_78_out, or_22_out);
  not not_79 (not_79_out, or_22_out);
  not not_80 (not_80_out, or_22_out);
  not not_81 (not_81_out, or_22_out);
  not not_82 (not_82_out, or_22_out);
  not not_83 (not_83_out, or_22_out);
  not not_84 (not_84_out, or_22_out);
  not not_85 (not_85_out, or_22_out);
  and and_59 (and_59_out, or_1_out[15], or_22_out);
  and and_60 (and_60_out, nand_225_out, not_70_out);
  and and_61 (and_61_out, or_1_out[14], or_22_out);
  and and_62 (and_62_out, nand_227_out, not_71_out);
  and and_63 (and_63_out, or_1_out[13], or_22_out);
  and and_64 (and_64_out, nand_229_out, not_72_out);
  and and_65 (and_65_out, or_1_out[12], or_22_out);
  and and_66 (and_66_out, nand_231_out, not_73_out);
  and and_67 (and_67_out, or_1_out[11], or_22_out);
  and and_68 (and_68_out, nand_233_out, not_74_out);
  and and_69 (and_69_out, or_1_out[10], or_22_out);
  and and_70 (and_70_out, nand_235_out, not_75_out);
  and and_71 (and_71_out, or_1_out[9], or_22_out);
  and and_72 (and_72_out, nand_237_out, not_76_out);
  and and_73 (and_73_out, or_1_out[8], or_22_out);
  and and_74 (and_74_out, nand_239_out, not_77_out);
  and and_75 (and_75_out, or_1_out[7], or_22_out);
  and and_76 (and_76_out, nand_241_out, not_78_out);
  and and_77 (and_77_out, or_1_out[6], or_22_out);
  and and_78 (and_78_out, nand_243_out, not_79_out);
  and and_79 (and_79_out, or_1_out[5], or_22_out);
  and and_80 (and_80_out, nand_245_out, not_80_out);
  and and_81 (and_81_out, or_1_out[4], or_22_out);
  and and_82 (and_82_out, nand_247_out, not_81_out);
  and and_83 (and_83_out, or_1_out[3], or_22_out);
  and and_84 (and_84_out, nand_249_out, not_82_out);
  and and_85 (and_85_out, or_1_out[2], or_22_out);
  and and_86 (and_86_out, nand_251_out, not_83_out);
  and and_87 (and_87_out, or_1_out[1], or_22_out);
  and and_88 (and_88_out, nand_253_out, not_84_out);
  and and_89 (and_89_out, or_1_out[0], or_22_out);
  and and_90 (and_90_out, nand_255_out, not_85_out);
  or or_23 (or_23_out, and_59_out, and_60_out);
  or or_24 (or_24_out, and_61_out, and_62_out);
  or or_25 (or_25_out, and_63_out, and_64_out);
  or or_26 (or_26_out, and_65_out, and_66_out);
  or or_27 (or_27_out, and_67_out, and_68_out);
  or or_28 (or_28_out, and_69_out, and_70_out);
  or or_29 (or_29_out, and_71_out, and_72_out);
  or or_30 (or_30_out, and_73_out, and_74_out);
  or or_31 (or_31_out, and_75_out, and_76_out);
  or or_32 (or_32_out, and_77_out, and_78_out);
  or or_33 (or_33_out, and_79_out, and_80_out);
  or or_34 (or_34_out, and_81_out, and_82_out);
  or or_35 (or_35_out, and_83_out, and_84_out);
  or or_36 (or_36_out, and_85_out, and_86_out);
  or or_37 (or_37_out, and_87_out, and_88_out);
  or or_38 (or_38_out, and_89_out, and_90_out);
  not not_86 (not_86_out, or_23_out);
  not not_87 (not_87_out, or_24_out);
  not not_88 (not_88_out, or_25_out);
  not not_89 (not_89_out, or_26_out);
  not not_90 (not_90_out, or_27_out);
  not not_91 (not_91_out, or_28_out);
  not not_92 (not_92_out, or_29_out);
  not not_93 (not_93_out, or_30_out);
  not not_94 (not_94_out, or_31_out);
  not not_95 (not_95_out, or_32_out);
  not not_96 (not_96_out, or_33_out);
  not not_97 (not_97_out, or_34_out);
  not not_98 (not_98_out, or_35_out);
  not not_99 (not_99_out, or_36_out);
  not not_100 (not_100_out, or_37_out);
  not not_101 (not_101_out, or_38_out);
  nand nand_129 (nand_129_out, or_23_out, CLOCK);
  nand nand_130 (nand_130_out, CLOCK, not_86_out);
  nand nand_131 (nand_131_out, or_24_out, CLOCK);
  nand nand_132 (nand_132_out, CLOCK, not_87_out);
  nand nand_133 (nand_133_out, or_25_out, CLOCK);
  nand nand_134 (nand_134_out, CLOCK, not_88_out);
  nand nand_135 (nand_135_out, or_26_out, CLOCK);
  nand nand_136 (nand_136_out, CLOCK, not_89_out);
  nand nand_137 (nand_137_out, or_27_out, CLOCK);
  nand nand_138 (nand_138_out, CLOCK, not_90_out);
  nand nand_139 (nand_139_out, or_28_out, CLOCK);
  nand nand_140 (nand_140_out, CLOCK, not_91_out);
  nand nand_141 (nand_141_out, or_29_out, CLOCK);
  nand nand_142 (nand_142_out, CLOCK, not_92_out);
  nand nand_143 (nand_143_out, or_30_out, CLOCK);
  nand nand_144 (nand_144_out, CLOCK, not_93_out);
  nand nand_145 (nand_145_out, or_31_out, CLOCK);
  nand nand_146 (nand_146_out, CLOCK, not_94_out);
  nand nand_147 (nand_147_out, or_32_out, CLOCK);
  nand nand_148 (nand_148_out, CLOCK, not_95_out);
  nand nand_149 (nand_149_out, or_33_out, CLOCK);
  nand nand_150 (nand_150_out, CLOCK, not_96_out);
  nand nand_151 (nand_151_out, or_34_out, CLOCK);
  nand nand_152 (nand_152_out, CLOCK, not_97_out);
  nand nand_153 (nand_153_out, or_35_out, CLOCK);
  nand nand_154 (nand_154_out, CLOCK, not_98_out);
  nand nand_155 (nand_155_out, or_36_out, CLOCK);
  nand nand_156 (nand_156_out, CLOCK, not_99_out);
  nand nand_157 (nand_157_out, or_37_out, CLOCK);
  nand nand_158 (nand_158_out, CLOCK, not_100_out);
  nand nand_159 (nand_159_out, or_38_out, CLOCK);
  nand nand_160 (nand_160_out, CLOCK, not_101_out);
  nand nand_161 (nand_161_out, nand_129_out, nand_162_out);
  nand nand_162 (nand_162_out, nand_161_out, nand_130_out);
  nand nand_163 (nand_163_out, nand_131_out, nand_164_out);
  nand nand_164 (nand_164_out, nand_163_out, nand_132_out);
  nand nand_165 (nand_165_out, nand_133_out, nand_166_out);
  nand nand_166 (nand_166_out, nand_165_out, nand_134_out);
  nand nand_167 (nand_167_out, nand_135_out, nand_168_out);
  nand nand_168 (nand_168_out, nand_167_out, nand_136_out);
  nand nand_169 (nand_169_out, nand_137_out, nand_170_out);
  nand nand_170 (nand_170_out, nand_169_out, nand_138_out);
  nand nand_171 (nand_171_out, nand_139_out, nand_172_out);
  nand nand_172 (nand_172_out, nand_171_out, nand_140_out);
  nand nand_173 (nand_173_out, nand_141_out, nand_174_out);
  nand nand_174 (nand_174_out, nand_173_out, nand_142_out);
  nand nand_175 (nand_175_out, nand_143_out, nand_176_out);
  nand nand_176 (nand_176_out, nand_175_out, nand_144_out);
  nand nand_177 (nand_177_out, nand_145_out, nand_178_out);
  nand nand_178 (nand_178_out, nand_177_out, nand_146_out);
  nand nand_179 (nand_179_out, nand_147_out, nand_180_out);
  nand nand_180 (nand_180_out, nand_179_out, nand_148_out);
  nand nand_181 (nand_181_out, nand_149_out, nand_182_out);
  nand nand_182 (nand_182_out, nand_181_out, nand_150_out);
  nand nand_183 (nand_183_out, nand_151_out, nand_184_out);
  nand nand_184 (nand_184_out, nand_183_out, nand_152_out);
  nand nand_185 (nand_185_out, nand_153_out, nand_186_out);
  nand nand_186 (nand_186_out, nand_185_out, nand_154_out);
  nand nand_187 (nand_187_out, nand_155_out, nand_188_out);
  nand nand_188 (nand_188_out, nand_187_out, nand_156_out);
  nand nand_189 (nand_189_out, nand_157_out, nand_190_out);
  nand nand_190 (nand_190_out, nand_189_out, nand_158_out);
  nand nand_191 (nand_191_out, nand_159_out, nand_192_out);
  nand nand_192 (nand_192_out, nand_191_out, nand_160_out);
  not not_102 (not_102_out, nand_161_out);
  not not_103 (not_103_out, CLOCK);
  not not_104 (not_104_out, nand_163_out);
  not not_105 (not_105_out, CLOCK);
  not not_106 (not_106_out, nand_165_out);
  not not_107 (not_107_out, CLOCK);
  not not_108 (not_108_out, nand_167_out);
  not not_109 (not_109_out, CLOCK);
  not not_110 (not_110_out, nand_169_out);
  not not_111 (not_111_out, CLOCK);
  not not_112 (not_112_out, nand_171_out);
  not not_113 (not_113_out, CLOCK);
  not not_114 (not_114_out, nand_173_out);
  not not_115 (not_115_out, CLOCK);
  not not_116 (not_116_out, nand_175_out);
  not not_117 (not_117_out, CLOCK);
  not not_118 (not_118_out, nand_177_out);
  not not_119 (not_119_out, CLOCK);
  not not_120 (not_120_out, nand_179_out);
  not not_121 (not_121_out, CLOCK);
  not not_122 (not_122_out, nand_181_out);
  not not_123 (not_123_out, CLOCK);
  not not_124 (not_124_out, nand_183_out);
  not not_125 (not_125_out, CLOCK);
  not not_126 (not_126_out, nand_185_out);
  not not_127 (not_127_out, CLOCK);
  not not_128 (not_128_out, nand_187_out);
  not not_129 (not_129_out, CLOCK);
  not not_130 (not_130_out, nand_189_out);
  not not_131 (not_131_out, CLOCK);
  not not_132 (not_132_out, nand_191_out);
  not not_133 (not_133_out, CLOCK);
  nand nand_193 (nand_193_out, nand_161_out, not_103_out);
  nand nand_194 (nand_194_out, not_103_out, not_102_out);
  nand nand_195 (nand_195_out, nand_163_out, not_105_out);
  nand nand_196 (nand_196_out, not_105_out, not_104_out);
  nand nand_197 (nand_197_out, nand_165_out, not_107_out);
  nand nand_198 (nand_198_out, not_107_out, not_106_out);
  nand nand_199 (nand_199_out, nand_167_out, not_109_out);
  nand nand_200 (nand_200_out, not_109_out, not_108_out);
  nand nand_201 (nand_201_out, nand_169_out, not_111_out);
  nand nand_202 (nand_202_out, not_111_out, not_110_out);
  nand nand_203 (nand_203_out, nand_171_out, not_113_out);
  nand nand_204 (nand_204_out, not_113_out, not_112_out);
  nand nand_205 (nand_205_out, nand_173_out, not_115_out);
  nand nand_206 (nand_206_out, not_115_out, not_114_out);
  nand nand_207 (nand_207_out, nand_175_out, not_117_out);
  nand nand_208 (nand_208_out, not_117_out, not_116_out);
  nand nand_209 (nand_209_out, nand_177_out, not_119_out);
  nand nand_210 (nand_210_out, not_119_out, not_118_out);
  nand nand_211 (nand_211_out, nand_179_out, not_121_out);
  nand nand_212 (nand_212_out, not_121_out, not_120_out);
  nand nand_213 (nand_213_out, nand_181_out, not_123_out);
  nand nand_214 (nand_214_out, not_123_out, not_122_out);
  nand nand_215 (nand_215_out, nand_183_out, not_125_out);
  nand nand_216 (nand_216_out, not_125_out, not_124_out);
  nand nand_217 (nand_217_out, nand_185_out, not_127_out);
  nand nand_218 (nand_218_out, not_127_out, not_126_out);
  nand nand_219 (nand_219_out, nand_187_out, not_129_out);
  nand nand_220 (nand_220_out, not_129_out, not_128_out);
  nand nand_221 (nand_221_out, nand_189_out, not_131_out);
  nand nand_222 (nand_222_out, not_131_out, not_130_out);
  nand nand_223 (nand_223_out, nand_191_out, not_133_out);
  nand nand_224 (nand_224_out, not_133_out, not_132_out);
  nand nand_225 (nand_225_out, nand_193_out, nand_226_out);
  nand nand_226 (nand_226_out, nand_225_out, nand_194_out);
  nand nand_227 (nand_227_out, nand_195_out, nand_228_out);
  nand nand_228 (nand_228_out, nand_227_out, nand_196_out);
  nand nand_229 (nand_229_out, nand_197_out, nand_230_out);
  nand nand_230 (nand_230_out, nand_229_out, nand_198_out);
  nand nand_231 (nand_231_out, nand_199_out, nand_232_out);
  nand nand_232 (nand_232_out, nand_231_out, nand_200_out);
  nand nand_233 (nand_233_out, nand_201_out, nand_234_out);
  nand nand_234 (nand_234_out, nand_233_out, nand_202_out);
  nand nand_235 (nand_235_out, nand_203_out, nand_236_out);
  nand nand_236 (nand_236_out, nand_235_out, nand_204_out);
  nand nand_237 (nand_237_out, nand_205_out, nand_238_out);
  nand nand_238 (nand_238_out, nand_237_out, nand_206_out);
  nand nand_239 (nand_239_out, nand_207_out, nand_240_out);
  nand nand_240 (nand_240_out, nand_239_out, nand_208_out);
  nand nand_241 (nand_241_out, nand_209_out, nand_242_out);
  nand nand_242 (nand_242_out, nand_241_out, nand_210_out);
  nand nand_243 (nand_243_out, nand_211_out, nand_244_out);
  nand nand_244 (nand_244_out, nand_243_out, nand_212_out);
  nand nand_245 (nand_245_out, nand_213_out, nand_246_out);
  nand nand_246 (nand_246_out, nand_245_out, nand_214_out);
  nand nand_247 (nand_247_out, nand_215_out, nand_248_out);
  nand nand_248 (nand_248_out, nand_247_out, nand_216_out);
  nand nand_249 (nand_249_out, nand_217_out, nand_250_out);
  nand nand_250 (nand_250_out, nand_249_out, nand_218_out);
  nand nand_251 (nand_251_out, nand_219_out, nand_252_out);
  nand nand_252 (nand_252_out, nand_251_out, nand_220_out);
  nand nand_253 (nand_253_out, nand_221_out, nand_254_out);
  nand nand_254 (nand_254_out, nand_253_out, nand_222_out);
  nand nand_255 (nand_255_out, nand_223_out, nand_256_out);
  nand nand_256 (nand_256_out, nand_255_out, nand_224_out);
  or or_39 (or_39_out, and_43_out, and_91_out);
  and and_91 (and_91_out, nand_225_out, and_41_out);
  or or_40 (or_40_out, and_44_out, and_92_out);
  and and_92 (and_92_out, nand_227_out, and_41_out);
  or or_41 (or_41_out, and_45_out, and_93_out);
  and and_93 (and_93_out, nand_229_out, and_41_out);
  or or_42 (or_42_out, and_46_out, and_94_out);
  and and_94 (and_94_out, nand_231_out, and_41_out);
  or or_43 (or_43_out, and_47_out, and_95_out);
  and and_95 (and_95_out, nand_233_out, and_41_out);
  or or_44 (or_44_out, and_48_out, and_96_out);
  and and_96 (and_96_out, nand_235_out, and_41_out);
  or or_45 (or_45_out, and_49_out, and_97_out);
  and and_97 (and_97_out, nand_237_out, and_41_out);
  or or_46 (or_46_out, and_50_out, and_98_out);
  and and_98 (and_98_out, nand_239_out, and_41_out);
  or or_47 (or_47_out, and_51_out, and_99_out);
  and and_99 (and_99_out, nand_241_out, and_41_out);
  or or_48 (or_48_out, and_52_out, and_100_out);
  and and_100 (and_100_out, nand_243_out, and_41_out);
  or or_49 (or_49_out, and_53_out, and_101_out);
  and and_101 (and_101_out, nand_245_out, and_41_out);
  or or_50 (or_50_out, and_54_out, and_102_out);
  and and_102 (and_102_out, nand_247_out, and_41_out);
  or or_51 (or_51_out, and_55_out, and_103_out);
  and and_103 (and_103_out, nand_249_out, and_41_out);
  or or_52 (or_52_out, and_56_out, and_104_out);
  and and_104 (and_104_out, nand_251_out, and_41_out);
  or or_53 (or_53_out, and_57_out, and_105_out);
  and and_105 (and_105_out, nand_253_out, and_41_out);
  or or_54 (or_54_out, and_58_out, and_106_out);
  and and_106 (and_106_out, nand_255_out, and_41_out);
  and and_107 (and_107_out, or_1_out[15], or_21_out);
  and and_108 (and_108_out, nand_353_out, not_134_out);
  not not_134 (not_134_out, or_21_out);
  and and_109 (and_109_out, or_1_out[14], or_21_out);
  and and_110 (and_110_out, nand_355_out, not_135_out);
  not not_135 (not_135_out, or_21_out);
  and and_111 (and_111_out, or_1_out[13], or_21_out);
  and and_112 (and_112_out, nand_357_out, not_136_out);
  not not_136 (not_136_out, or_21_out);
  and and_113 (and_113_out, or_1_out[12], or_21_out);
  and and_114 (and_114_out, nand_359_out, not_137_out);
  not not_137 (not_137_out, or_21_out);
  and and_115 (and_115_out, or_1_out[11], or_21_out);
  and and_116 (and_116_out, nand_361_out, not_138_out);
  not not_138 (not_138_out, or_21_out);
  and and_117 (and_117_out, or_1_out[10], or_21_out);
  and and_118 (and_118_out, nand_363_out, not_139_out);
  not not_139 (not_139_out, or_21_out);
  and and_119 (and_119_out, or_1_out[9], or_21_out);
  and and_120 (and_120_out, nand_365_out, not_140_out);
  not not_140 (not_140_out, or_21_out);
  and and_121 (and_121_out, or_1_out[8], or_21_out);
  and and_122 (and_122_out, nand_367_out, not_141_out);
  not not_141 (not_141_out, or_21_out);
  and and_123 (and_123_out, or_1_out[7], or_21_out);
  and and_124 (and_124_out, nand_369_out, not_142_out);
  not not_142 (not_142_out, or_21_out);
  and and_125 (and_125_out, or_1_out[6], or_21_out);
  and and_126 (and_126_out, nand_371_out, not_143_out);
  not not_143 (not_143_out, or_21_out);
  and and_127 (and_127_out, or_1_out[5], or_21_out);
  and and_128 (and_128_out, nand_373_out, not_144_out);
  not not_144 (not_144_out, or_21_out);
  and and_129 (and_129_out, or_1_out[4], or_21_out);
  and and_130 (and_130_out, nand_375_out, not_145_out);
  not not_145 (not_145_out, or_21_out);
  and and_131 (and_131_out, or_1_out[3], or_21_out);
  and and_132 (and_132_out, nand_377_out, not_146_out);
  not not_146 (not_146_out, or_21_out);
  and and_133 (and_133_out, or_1_out[2], or_21_out);
  and and_134 (and_134_out, nand_379_out, not_147_out);
  not not_147 (not_147_out, or_21_out);
  and and_135 (and_135_out, or_1_out[1], or_21_out);
  and and_136 (and_136_out, nand_381_out, not_148_out);
  not not_148 (not_148_out, or_21_out);
  and and_137 (and_137_out, or_1_out[0], or_21_out);
  and and_138 (and_138_out, nand_383_out, not_149_out);
  not not_149 (not_149_out, or_21_out);
  or or_55 (or_55_out, and_107_out, and_108_out);
  or or_56 (or_56_out, and_109_out, and_110_out);
  or or_57 (or_57_out, and_111_out, and_112_out);
  or or_58 (or_58_out, and_113_out, and_114_out);
  or or_59 (or_59_out, and_115_out, and_116_out);
  or or_60 (or_60_out, and_117_out, and_118_out);
  or or_61 (or_61_out, and_119_out, and_120_out);
  or or_62 (or_62_out, and_121_out, and_122_out);
  or or_63 (or_63_out, and_123_out, and_124_out);
  or or_64 (or_64_out, and_125_out, and_126_out);
  or or_65 (or_65_out, and_127_out, and_128_out);
  or or_66 (or_66_out, and_129_out, and_130_out);
  or or_67 (or_67_out, and_131_out, and_132_out);
  or or_68 (or_68_out, and_133_out, and_134_out);
  or or_69 (or_69_out, and_135_out, and_136_out);
  or or_70 (or_70_out, and_137_out, and_138_out);
  not not_150 (not_150_out, or_55_out);
  not not_151 (not_151_out, or_56_out);
  not not_152 (not_152_out, or_57_out);
  not not_153 (not_153_out, or_58_out);
  not not_154 (not_154_out, or_59_out);
  not not_155 (not_155_out, or_60_out);
  not not_156 (not_156_out, or_61_out);
  not not_157 (not_157_out, or_62_out);
  not not_158 (not_158_out, or_63_out);
  not not_159 (not_159_out, or_64_out);
  not not_160 (not_160_out, or_65_out);
  not not_161 (not_161_out, or_66_out);
  not not_162 (not_162_out, or_67_out);
  not not_163 (not_163_out, or_68_out);
  not not_164 (not_164_out, or_69_out);
  not not_165 (not_165_out, or_70_out);
  nand nand_257 (nand_257_out, or_55_out, CLOCK);
  nand nand_258 (nand_258_out, CLOCK, not_150_out);
  nand nand_259 (nand_259_out, or_56_out, CLOCK);
  nand nand_260 (nand_260_out, CLOCK, not_151_out);
  nand nand_261 (nand_261_out, or_57_out, CLOCK);
  nand nand_262 (nand_262_out, CLOCK, not_152_out);
  nand nand_263 (nand_263_out, or_58_out, CLOCK);
  nand nand_264 (nand_264_out, CLOCK, not_153_out);
  nand nand_265 (nand_265_out, or_59_out, CLOCK);
  nand nand_266 (nand_266_out, CLOCK, not_154_out);
  nand nand_267 (nand_267_out, or_60_out, CLOCK);
  nand nand_268 (nand_268_out, CLOCK, not_155_out);
  nand nand_269 (nand_269_out, or_61_out, CLOCK);
  nand nand_270 (nand_270_out, CLOCK, not_156_out);
  nand nand_271 (nand_271_out, or_62_out, CLOCK);
  nand nand_272 (nand_272_out, CLOCK, not_157_out);
  nand nand_273 (nand_273_out, or_63_out, CLOCK);
  nand nand_274 (nand_274_out, CLOCK, not_158_out);
  nand nand_275 (nand_275_out, or_64_out, CLOCK);
  nand nand_276 (nand_276_out, CLOCK, not_159_out);
  nand nand_277 (nand_277_out, or_65_out, CLOCK);
  nand nand_278 (nand_278_out, CLOCK, not_160_out);
  nand nand_279 (nand_279_out, or_66_out, CLOCK);
  nand nand_280 (nand_280_out, CLOCK, not_161_out);
  nand nand_281 (nand_281_out, or_67_out, CLOCK);
  nand nand_282 (nand_282_out, CLOCK, not_162_out);
  nand nand_283 (nand_283_out, or_68_out, CLOCK);
  nand nand_284 (nand_284_out, CLOCK, not_163_out);
  nand nand_285 (nand_285_out, or_69_out, CLOCK);
  nand nand_286 (nand_286_out, CLOCK, not_164_out);
  nand nand_287 (nand_287_out, or_70_out, CLOCK);
  nand nand_288 (nand_288_out, CLOCK, not_165_out);
  nand nand_289 (nand_289_out, nand_257_out, nand_290_out);
  nand nand_290 (nand_290_out, nand_289_out, nand_258_out);
  nand nand_291 (nand_291_out, nand_259_out, nand_292_out);
  nand nand_292 (nand_292_out, nand_291_out, nand_260_out);
  nand nand_293 (nand_293_out, nand_261_out, nand_294_out);
  nand nand_294 (nand_294_out, nand_293_out, nand_262_out);
  nand nand_295 (nand_295_out, nand_263_out, nand_296_out);
  nand nand_296 (nand_296_out, nand_295_out, nand_264_out);
  nand nand_297 (nand_297_out, nand_265_out, nand_298_out);
  nand nand_298 (nand_298_out, nand_297_out, nand_266_out);
  nand nand_299 (nand_299_out, nand_267_out, nand_300_out);
  nand nand_300 (nand_300_out, nand_299_out, nand_268_out);
  nand nand_301 (nand_301_out, nand_269_out, nand_302_out);
  nand nand_302 (nand_302_out, nand_301_out, nand_270_out);
  nand nand_303 (nand_303_out, nand_271_out, nand_304_out);
  nand nand_304 (nand_304_out, nand_303_out, nand_272_out);
  nand nand_305 (nand_305_out, nand_273_out, nand_306_out);
  nand nand_306 (nand_306_out, nand_305_out, nand_274_out);
  nand nand_307 (nand_307_out, nand_275_out, nand_308_out);
  nand nand_308 (nand_308_out, nand_307_out, nand_276_out);
  nand nand_309 (nand_309_out, nand_277_out, nand_310_out);
  nand nand_310 (nand_310_out, nand_309_out, nand_278_out);
  nand nand_311 (nand_311_out, nand_279_out, nand_312_out);
  nand nand_312 (nand_312_out, nand_311_out, nand_280_out);
  nand nand_313 (nand_313_out, nand_281_out, nand_314_out);
  nand nand_314 (nand_314_out, nand_313_out, nand_282_out);
  nand nand_315 (nand_315_out, nand_283_out, nand_316_out);
  nand nand_316 (nand_316_out, nand_315_out, nand_284_out);
  nand nand_317 (nand_317_out, nand_285_out, nand_318_out);
  nand nand_318 (nand_318_out, nand_317_out, nand_286_out);
  nand nand_319 (nand_319_out, nand_287_out, nand_320_out);
  nand nand_320 (nand_320_out, nand_319_out, nand_288_out);
  not not_166 (not_166_out, nand_289_out);
  not not_167 (not_167_out, CLOCK);
  not not_168 (not_168_out, nand_291_out);
  not not_169 (not_169_out, CLOCK);
  not not_170 (not_170_out, nand_293_out);
  not not_171 (not_171_out, CLOCK);
  not not_172 (not_172_out, nand_295_out);
  not not_173 (not_173_out, CLOCK);
  not not_174 (not_174_out, nand_297_out);
  not not_175 (not_175_out, CLOCK);
  not not_176 (not_176_out, nand_299_out);
  not not_177 (not_177_out, CLOCK);
  not not_178 (not_178_out, nand_301_out);
  not not_179 (not_179_out, CLOCK);
  not not_180 (not_180_out, nand_303_out);
  not not_181 (not_181_out, CLOCK);
  not not_182 (not_182_out, nand_305_out);
  not not_183 (not_183_out, CLOCK);
  not not_184 (not_184_out, nand_307_out);
  not not_185 (not_185_out, CLOCK);
  not not_186 (not_186_out, nand_309_out);
  not not_187 (not_187_out, CLOCK);
  not not_188 (not_188_out, nand_311_out);
  not not_189 (not_189_out, CLOCK);
  not not_190 (not_190_out, nand_313_out);
  not not_191 (not_191_out, CLOCK);
  not not_192 (not_192_out, nand_315_out);
  not not_193 (not_193_out, CLOCK);
  not not_194 (not_194_out, nand_317_out);
  not not_195 (not_195_out, CLOCK);
  not not_196 (not_196_out, nand_319_out);
  not not_197 (not_197_out, CLOCK);
  nand nand_321 (nand_321_out, nand_289_out, not_167_out);
  nand nand_322 (nand_322_out, not_167_out, not_166_out);
  nand nand_323 (nand_323_out, nand_291_out, not_169_out);
  nand nand_324 (nand_324_out, not_169_out, not_168_out);
  nand nand_325 (nand_325_out, nand_293_out, not_171_out);
  nand nand_326 (nand_326_out, not_171_out, not_170_out);
  nand nand_327 (nand_327_out, nand_295_out, not_173_out);
  nand nand_328 (nand_328_out, not_173_out, not_172_out);
  nand nand_329 (nand_329_out, nand_297_out, not_175_out);
  nand nand_330 (nand_330_out, not_175_out, not_174_out);
  nand nand_331 (nand_331_out, nand_299_out, not_177_out);
  nand nand_332 (nand_332_out, not_177_out, not_176_out);
  nand nand_333 (nand_333_out, nand_301_out, not_179_out);
  nand nand_334 (nand_334_out, not_179_out, not_178_out);
  nand nand_335 (nand_335_out, nand_303_out, not_181_out);
  nand nand_336 (nand_336_out, not_181_out, not_180_out);
  nand nand_337 (nand_337_out, nand_305_out, not_183_out);
  nand nand_338 (nand_338_out, not_183_out, not_182_out);
  nand nand_339 (nand_339_out, nand_307_out, not_185_out);
  nand nand_340 (nand_340_out, not_185_out, not_184_out);
  nand nand_341 (nand_341_out, nand_309_out, not_187_out);
  nand nand_342 (nand_342_out, not_187_out, not_186_out);
  nand nand_343 (nand_343_out, nand_311_out, not_189_out);
  nand nand_344 (nand_344_out, not_189_out, not_188_out);
  nand nand_345 (nand_345_out, nand_313_out, not_191_out);
  nand nand_346 (nand_346_out, not_191_out, not_190_out);
  nand nand_347 (nand_347_out, nand_315_out, not_193_out);
  nand nand_348 (nand_348_out, not_193_out, not_192_out);
  nand nand_349 (nand_349_out, nand_317_out, not_195_out);
  nand nand_350 (nand_350_out, not_195_out, not_194_out);
  nand nand_351 (nand_351_out, nand_319_out, not_197_out);
  nand nand_352 (nand_352_out, not_197_out, not_196_out);
  nand nand_353 (nand_353_out, nand_321_out, nand_354_out);
  nand nand_354 (nand_354_out, nand_353_out, nand_322_out);
  nand nand_355 (nand_355_out, nand_323_out, nand_356_out);
  nand nand_356 (nand_356_out, nand_355_out, nand_324_out);
  nand nand_357 (nand_357_out, nand_325_out, nand_358_out);
  nand nand_358 (nand_358_out, nand_357_out, nand_326_out);
  nand nand_359 (nand_359_out, nand_327_out, nand_360_out);
  nand nand_360 (nand_360_out, nand_359_out, nand_328_out);
  nand nand_361 (nand_361_out, nand_329_out, nand_362_out);
  nand nand_362 (nand_362_out, nand_361_out, nand_330_out);
  nand nand_363 (nand_363_out, nand_331_out, nand_364_out);
  nand nand_364 (nand_364_out, nand_363_out, nand_332_out);
  nand nand_365 (nand_365_out, nand_333_out, nand_366_out);
  nand nand_366 (nand_366_out, nand_365_out, nand_334_out);
  nand nand_367 (nand_367_out, nand_335_out, nand_368_out);
  nand nand_368 (nand_368_out, nand_367_out, nand_336_out);
  nand nand_369 (nand_369_out, nand_337_out, nand_370_out);
  nand nand_370 (nand_370_out, nand_369_out, nand_338_out);
  nand nand_371 (nand_371_out, nand_339_out, nand_372_out);
  nand nand_372 (nand_372_out, nand_371_out, nand_340_out);
  nand nand_373 (nand_373_out, nand_341_out, nand_374_out);
  nand nand_374 (nand_374_out, nand_373_out, nand_342_out);
  nand nand_375 (nand_375_out, nand_343_out, nand_376_out);
  nand nand_376 (nand_376_out, nand_375_out, nand_344_out);
  nand nand_377 (nand_377_out, nand_345_out, nand_378_out);
  nand nand_378 (nand_378_out, nand_377_out, nand_346_out);
  nand nand_379 (nand_379_out, nand_347_out, nand_380_out);
  nand nand_380 (nand_380_out, nand_379_out, nand_348_out);
  nand nand_381 (nand_381_out, nand_349_out, nand_382_out);
  nand nand_382 (nand_382_out, nand_381_out, nand_350_out);
  nand nand_383 (nand_383_out, nand_351_out, nand_384_out);
  nand nand_384 (nand_384_out, nand_383_out, nand_352_out);
  or or_71 (or_71_out, or_39_out, and_139_out);
  and and_139 (and_139_out, nand_353_out, and_40_out);
  or or_72 (or_72_out, or_40_out, and_140_out);
  and and_140 (and_140_out, nand_355_out, and_40_out);
  or or_73 (or_73_out, or_41_out, and_141_out);
  and and_141 (and_141_out, nand_357_out, and_40_out);
  or or_74 (or_74_out, or_42_out, and_142_out);
  and and_142 (and_142_out, nand_359_out, and_40_out);
  or or_75 (or_75_out, or_43_out, and_143_out);
  and and_143 (and_143_out, nand_361_out, and_40_out);
  or or_76 (or_76_out, or_44_out, and_144_out);
  and and_144 (and_144_out, nand_363_out, and_40_out);
  or or_77 (or_77_out, or_45_out, and_145_out);
  and and_145 (and_145_out, nand_365_out, and_40_out);
  or or_78 (or_78_out, or_46_out, and_146_out);
  and and_146 (and_146_out, nand_367_out, and_40_out);
  or or_79 (or_79_out, or_47_out, and_147_out);
  and and_147 (and_147_out, nand_369_out, and_40_out);
  or or_80 (or_80_out, or_48_out, and_148_out);
  and and_148 (and_148_out, nand_371_out, and_40_out);
  or or_81 (or_81_out, or_49_out, and_149_out);
  and and_149 (and_149_out, nand_373_out, and_40_out);
  or or_82 (or_82_out, or_50_out, and_150_out);
  and and_150 (and_150_out, nand_375_out, and_40_out);
  or or_83 (or_83_out, or_51_out, and_151_out);
  and and_151 (and_151_out, nand_377_out, and_40_out);
  or or_84 (or_84_out, or_52_out, and_152_out);
  and and_152 (and_152_out, nand_379_out, and_40_out);
  or or_85 (or_85_out, or_53_out, and_153_out);
  and and_153 (and_153_out, nand_381_out, and_40_out);
  or or_86 (or_86_out, or_54_out, and_154_out);
  and and_154 (and_154_out, nand_383_out, and_40_out);
  not not_198 (not_198_out, or_20_out);
  not not_199 (not_199_out, or_20_out);
  not not_200 (not_200_out, or_20_out);
  not not_201 (not_201_out, or_20_out);
  not not_202 (not_202_out, or_20_out);
  not not_203 (not_203_out, or_20_out);
  not not_204 (not_204_out, or_20_out);
  not not_205 (not_205_out, or_20_out);
  not not_206 (not_206_out, or_20_out);
  not not_207 (not_207_out, or_20_out);
  not not_208 (not_208_out, or_20_out);
  not not_209 (not_209_out, or_20_out);
  not not_210 (not_210_out, or_20_out);
  not not_211 (not_211_out, or_20_out);
  not not_212 (not_212_out, or_20_out);
  not not_213 (not_213_out, or_20_out);
  and and_155 (and_155_out, or_1_out[15], or_20_out);
  or or_87 (or_87_out, and_155_out, and_156_out);
  and and_156 (and_156_out, nand_481_out, not_198_out);
  and and_157 (and_157_out, or_1_out[14], or_20_out);
  or or_88 (or_88_out, and_157_out, and_158_out);
  and and_158 (and_158_out, nand_483_out, not_199_out);
  and and_159 (and_159_out, or_1_out[13], or_20_out);
  or or_89 (or_89_out, and_159_out, and_160_out);
  and and_160 (and_160_out, nand_485_out, not_200_out);
  and and_161 (and_161_out, or_1_out[12], or_20_out);
  or or_90 (or_90_out, and_161_out, and_162_out);
  and and_162 (and_162_out, nand_487_out, not_201_out);
  and and_163 (and_163_out, or_1_out[11], or_20_out);
  or or_91 (or_91_out, and_163_out, and_164_out);
  and and_164 (and_164_out, nand_489_out, not_202_out);
  and and_165 (and_165_out, or_1_out[10], or_20_out);
  or or_92 (or_92_out, and_165_out, and_166_out);
  and and_166 (and_166_out, nand_491_out, not_203_out);
  and and_167 (and_167_out, or_1_out[9], or_20_out);
  or or_93 (or_93_out, and_167_out, and_168_out);
  and and_168 (and_168_out, nand_493_out, not_204_out);
  and and_169 (and_169_out, or_1_out[8], or_20_out);
  or or_94 (or_94_out, and_169_out, and_170_out);
  and and_170 (and_170_out, nand_495_out, not_205_out);
  and and_171 (and_171_out, or_1_out[7], or_20_out);
  or or_95 (or_95_out, and_171_out, and_172_out);
  and and_172 (and_172_out, nand_497_out, not_206_out);
  and and_173 (and_173_out, or_1_out[6], or_20_out);
  or or_96 (or_96_out, and_173_out, and_174_out);
  and and_174 (and_174_out, nand_499_out, not_207_out);
  and and_175 (and_175_out, or_1_out[5], or_20_out);
  or or_97 (or_97_out, and_175_out, and_176_out);
  and and_176 (and_176_out, nand_501_out, not_208_out);
  and and_177 (and_177_out, or_1_out[4], or_20_out);
  or or_98 (or_98_out, and_177_out, and_178_out);
  and and_178 (and_178_out, nand_503_out, not_209_out);
  and and_179 (and_179_out, or_1_out[3], or_20_out);
  or or_99 (or_99_out, and_179_out, and_180_out);
  and and_180 (and_180_out, nand_505_out, not_210_out);
  and and_181 (and_181_out, or_1_out[2], or_20_out);
  or or_100 (or_100_out, and_181_out, and_182_out);
  and and_182 (and_182_out, nand_507_out, not_211_out);
  and and_183 (and_183_out, or_1_out[1], or_20_out);
  or or_101 (or_101_out, and_183_out, and_184_out);
  and and_184 (and_184_out, nand_509_out, not_212_out);
  and and_185 (and_185_out, or_1_out[0], or_20_out);
  or or_102 (or_102_out, and_185_out, and_186_out);
  and and_186 (and_186_out, nand_511_out, not_213_out);
  not not_214 (not_214_out, or_87_out);
  not not_215 (not_215_out, or_88_out);
  not not_216 (not_216_out, or_89_out);
  not not_217 (not_217_out, or_90_out);
  not not_218 (not_218_out, or_91_out);
  not not_219 (not_219_out, or_92_out);
  not not_220 (not_220_out, or_93_out);
  not not_221 (not_221_out, or_94_out);
  not not_222 (not_222_out, or_95_out);
  not not_223 (not_223_out, or_96_out);
  not not_224 (not_224_out, or_97_out);
  not not_225 (not_225_out, or_98_out);
  not not_226 (not_226_out, or_99_out);
  not not_227 (not_227_out, or_100_out);
  not not_228 (not_228_out, or_101_out);
  not not_229 (not_229_out, or_102_out);
  nand nand_385 (nand_385_out, or_87_out, CLOCK);
  nand nand_386 (nand_386_out, CLOCK, not_214_out);
  nand nand_387 (nand_387_out, or_88_out, CLOCK);
  nand nand_388 (nand_388_out, CLOCK, not_215_out);
  nand nand_389 (nand_389_out, or_89_out, CLOCK);
  nand nand_390 (nand_390_out, CLOCK, not_216_out);
  nand nand_391 (nand_391_out, or_90_out, CLOCK);
  nand nand_392 (nand_392_out, CLOCK, not_217_out);
  nand nand_393 (nand_393_out, or_91_out, CLOCK);
  nand nand_394 (nand_394_out, CLOCK, not_218_out);
  nand nand_395 (nand_395_out, or_92_out, CLOCK);
  nand nand_396 (nand_396_out, CLOCK, not_219_out);
  nand nand_397 (nand_397_out, or_93_out, CLOCK);
  nand nand_398 (nand_398_out, CLOCK, not_220_out);
  nand nand_399 (nand_399_out, or_94_out, CLOCK);
  nand nand_400 (nand_400_out, CLOCK, not_221_out);
  nand nand_401 (nand_401_out, or_95_out, CLOCK);
  nand nand_402 (nand_402_out, CLOCK, not_222_out);
  nand nand_403 (nand_403_out, or_96_out, CLOCK);
  nand nand_404 (nand_404_out, CLOCK, not_223_out);
  nand nand_405 (nand_405_out, or_97_out, CLOCK);
  nand nand_406 (nand_406_out, CLOCK, not_224_out);
  nand nand_407 (nand_407_out, or_98_out, CLOCK);
  nand nand_408 (nand_408_out, CLOCK, not_225_out);
  nand nand_409 (nand_409_out, or_99_out, CLOCK);
  nand nand_410 (nand_410_out, CLOCK, not_226_out);
  nand nand_411 (nand_411_out, or_100_out, CLOCK);
  nand nand_412 (nand_412_out, CLOCK, not_227_out);
  nand nand_413 (nand_413_out, or_101_out, CLOCK);
  nand nand_414 (nand_414_out, CLOCK, not_228_out);
  nand nand_415 (nand_415_out, or_102_out, CLOCK);
  nand nand_416 (nand_416_out, CLOCK, not_229_out);
  nand nand_417 (nand_417_out, nand_385_out, nand_418_out);
  nand nand_418 (nand_418_out, nand_417_out, nand_386_out);
  nand nand_419 (nand_419_out, nand_387_out, nand_420_out);
  nand nand_420 (nand_420_out, nand_419_out, nand_388_out);
  nand nand_421 (nand_421_out, nand_389_out, nand_422_out);
  nand nand_422 (nand_422_out, nand_421_out, nand_390_out);
  nand nand_423 (nand_423_out, nand_391_out, nand_424_out);
  nand nand_424 (nand_424_out, nand_423_out, nand_392_out);
  nand nand_425 (nand_425_out, nand_393_out, nand_426_out);
  nand nand_426 (nand_426_out, nand_425_out, nand_394_out);
  nand nand_427 (nand_427_out, nand_395_out, nand_428_out);
  nand nand_428 (nand_428_out, nand_427_out, nand_396_out);
  nand nand_429 (nand_429_out, nand_397_out, nand_430_out);
  nand nand_430 (nand_430_out, nand_429_out, nand_398_out);
  nand nand_431 (nand_431_out, nand_399_out, nand_432_out);
  nand nand_432 (nand_432_out, nand_431_out, nand_400_out);
  nand nand_433 (nand_433_out, nand_401_out, nand_434_out);
  nand nand_434 (nand_434_out, nand_433_out, nand_402_out);
  nand nand_435 (nand_435_out, nand_403_out, nand_436_out);
  nand nand_436 (nand_436_out, nand_435_out, nand_404_out);
  nand nand_437 (nand_437_out, nand_405_out, nand_438_out);
  nand nand_438 (nand_438_out, nand_437_out, nand_406_out);
  nand nand_439 (nand_439_out, nand_407_out, nand_440_out);
  nand nand_440 (nand_440_out, nand_439_out, nand_408_out);
  nand nand_441 (nand_441_out, nand_409_out, nand_442_out);
  nand nand_442 (nand_442_out, nand_441_out, nand_410_out);
  nand nand_443 (nand_443_out, nand_411_out, nand_444_out);
  nand nand_444 (nand_444_out, nand_443_out, nand_412_out);
  nand nand_445 (nand_445_out, nand_413_out, nand_446_out);
  nand nand_446 (nand_446_out, nand_445_out, nand_414_out);
  nand nand_447 (nand_447_out, nand_415_out, nand_448_out);
  nand nand_448 (nand_448_out, nand_447_out, nand_416_out);
  not not_230 (not_230_out, nand_417_out);
  not not_231 (not_231_out, CLOCK);
  not not_232 (not_232_out, nand_419_out);
  not not_233 (not_233_out, CLOCK);
  not not_234 (not_234_out, nand_421_out);
  not not_235 (not_235_out, CLOCK);
  not not_236 (not_236_out, nand_423_out);
  not not_237 (not_237_out, CLOCK);
  not not_238 (not_238_out, nand_425_out);
  not not_239 (not_239_out, CLOCK);
  not not_240 (not_240_out, nand_427_out);
  not not_241 (not_241_out, CLOCK);
  not not_242 (not_242_out, nand_429_out);
  not not_243 (not_243_out, CLOCK);
  not not_244 (not_244_out, nand_431_out);
  not not_245 (not_245_out, CLOCK);
  not not_246 (not_246_out, nand_433_out);
  not not_247 (not_247_out, CLOCK);
  not not_248 (not_248_out, nand_435_out);
  not not_249 (not_249_out, CLOCK);
  not not_250 (not_250_out, nand_437_out);
  not not_251 (not_251_out, CLOCK);
  not not_252 (not_252_out, nand_439_out);
  not not_253 (not_253_out, CLOCK);
  not not_254 (not_254_out, nand_441_out);
  not not_255 (not_255_out, CLOCK);
  not not_256 (not_256_out, nand_443_out);
  not not_257 (not_257_out, CLOCK);
  not not_258 (not_258_out, nand_445_out);
  not not_259 (not_259_out, CLOCK);
  not not_260 (not_260_out, nand_447_out);
  not not_261 (not_261_out, CLOCK);
  nand nand_449 (nand_449_out, nand_417_out, not_231_out);
  nand nand_450 (nand_450_out, not_231_out, not_230_out);
  nand nand_451 (nand_451_out, nand_419_out, not_233_out);
  nand nand_452 (nand_452_out, not_233_out, not_232_out);
  nand nand_453 (nand_453_out, nand_421_out, not_235_out);
  nand nand_454 (nand_454_out, not_235_out, not_234_out);
  nand nand_455 (nand_455_out, nand_423_out, not_237_out);
  nand nand_456 (nand_456_out, not_237_out, not_236_out);
  nand nand_457 (nand_457_out, nand_425_out, not_239_out);
  nand nand_458 (nand_458_out, not_239_out, not_238_out);
  nand nand_459 (nand_459_out, nand_427_out, not_241_out);
  nand nand_460 (nand_460_out, not_241_out, not_240_out);
  nand nand_461 (nand_461_out, nand_429_out, not_243_out);
  nand nand_462 (nand_462_out, not_243_out, not_242_out);
  nand nand_463 (nand_463_out, nand_431_out, not_245_out);
  nand nand_464 (nand_464_out, not_245_out, not_244_out);
  nand nand_465 (nand_465_out, nand_433_out, not_247_out);
  nand nand_466 (nand_466_out, not_247_out, not_246_out);
  nand nand_467 (nand_467_out, nand_435_out, not_249_out);
  nand nand_468 (nand_468_out, not_249_out, not_248_out);
  nand nand_469 (nand_469_out, nand_437_out, not_251_out);
  nand nand_470 (nand_470_out, not_251_out, not_250_out);
  nand nand_471 (nand_471_out, nand_439_out, not_253_out);
  nand nand_472 (nand_472_out, not_253_out, not_252_out);
  nand nand_473 (nand_473_out, nand_441_out, not_255_out);
  nand nand_474 (nand_474_out, not_255_out, not_254_out);
  nand nand_475 (nand_475_out, nand_443_out, not_257_out);
  nand nand_476 (nand_476_out, not_257_out, not_256_out);
  nand nand_477 (nand_477_out, nand_445_out, not_259_out);
  nand nand_478 (nand_478_out, not_259_out, not_258_out);
  nand nand_479 (nand_479_out, nand_447_out, not_261_out);
  nand nand_480 (nand_480_out, not_261_out, not_260_out);
  nand nand_481 (nand_481_out, nand_449_out, nand_482_out);
  nand nand_482 (nand_482_out, nand_481_out, nand_450_out);
  nand nand_483 (nand_483_out, nand_451_out, nand_484_out);
  nand nand_484 (nand_484_out, nand_483_out, nand_452_out);
  nand nand_485 (nand_485_out, nand_453_out, nand_486_out);
  nand nand_486 (nand_486_out, nand_485_out, nand_454_out);
  nand nand_487 (nand_487_out, nand_455_out, nand_488_out);
  nand nand_488 (nand_488_out, nand_487_out, nand_456_out);
  nand nand_489 (nand_489_out, nand_457_out, nand_490_out);
  nand nand_490 (nand_490_out, nand_489_out, nand_458_out);
  nand nand_491 (nand_491_out, nand_459_out, nand_492_out);
  nand nand_492 (nand_492_out, nand_491_out, nand_460_out);
  nand nand_493 (nand_493_out, nand_461_out, nand_494_out);
  nand nand_494 (nand_494_out, nand_493_out, nand_462_out);
  nand nand_495 (nand_495_out, nand_463_out, nand_496_out);
  nand nand_496 (nand_496_out, nand_495_out, nand_464_out);
  nand nand_497 (nand_497_out, nand_465_out, nand_498_out);
  nand nand_498 (nand_498_out, nand_497_out, nand_466_out);
  nand nand_499 (nand_499_out, nand_467_out, nand_500_out);
  nand nand_500 (nand_500_out, nand_499_out, nand_468_out);
  nand nand_501 (nand_501_out, nand_469_out, nand_502_out);
  nand nand_502 (nand_502_out, nand_501_out, nand_470_out);
  nand nand_503 (nand_503_out, nand_471_out, nand_504_out);
  nand nand_504 (nand_504_out, nand_503_out, nand_472_out);
  nand nand_505 (nand_505_out, nand_473_out, nand_506_out);
  nand nand_506 (nand_506_out, nand_505_out, nand_474_out);
  nand nand_507 (nand_507_out, nand_475_out, nand_508_out);
  nand nand_508 (nand_508_out, nand_507_out, nand_476_out);
  nand nand_509 (nand_509_out, nand_477_out, nand_510_out);
  nand nand_510 (nand_510_out, nand_509_out, nand_478_out);
  nand nand_511 (nand_511_out, nand_479_out, nand_512_out);
  nand nand_512 (nand_512_out, nand_511_out, nand_480_out);
  or or_103 (DATA_OUT[15], or_71_out, and_187_out);
  and and_187 (and_187_out, nand_481_out, and_39_out);
  or or_104 (DATA_OUT[14], or_72_out, and_188_out);
  and and_188 (and_188_out, nand_483_out, and_39_out);
  or or_105 (DATA_OUT[13], or_73_out, and_189_out);
  and and_189 (and_189_out, nand_485_out, and_39_out);
  or or_106 (DATA_OUT[12], or_74_out, and_190_out);
  and and_190 (and_190_out, nand_487_out, and_39_out);
  or or_107 (DATA_OUT[11], or_75_out, and_191_out);
  and and_191 (and_191_out, nand_489_out, and_39_out);
  or or_108 (DATA_OUT[10], or_76_out, and_192_out);
  and and_192 (and_192_out, nand_491_out, and_39_out);
  or or_109 (DATA_OUT[9], or_77_out, and_193_out);
  and and_193 (and_193_out, nand_493_out, and_39_out);
  or or_110 (DATA_OUT[8], or_78_out, and_194_out);
  and and_194 (and_194_out, nand_495_out, and_39_out);
  or or_111 (DATA_OUT[7], or_79_out, and_195_out);
  and and_195 (and_195_out, nand_497_out, and_39_out);
  or or_112 (DATA_OUT[6], or_80_out, and_196_out);
  and and_196 (and_196_out, nand_499_out, and_39_out);
  or or_113 (DATA_OUT[5], or_81_out, and_197_out);
  and and_197 (and_197_out, nand_501_out, and_39_out);
  or or_114 (DATA_OUT[4], or_82_out, and_198_out);
  and and_198 (and_198_out, nand_503_out, and_39_out);
  or or_115 (DATA_OUT[3], or_83_out, and_199_out);
  and and_199 (and_199_out, nand_505_out, and_39_out);
  or or_116 (DATA_OUT[2], or_84_out, and_200_out);
  and and_200 (and_200_out, nand_507_out, and_39_out);
  or or_117 (DATA_OUT[1], or_85_out, and_201_out);
  and and_201 (and_201_out, nand_509_out, and_39_out);
  or or_118 (DATA_OUT[0], or_86_out, and_202_out);
  and and_202 (and_202_out, nand_511_out, and_39_out);
endmodule
module ALU_16bit (
  input  FA,
  input  FB,
  input  UA,
  input  UB,
  input  [15:0] DATA_IN_B,
  input  [15:0] DATA_IN_A,
  output N,
  output Z,
  output V,
  output C,
  output [15:0] DATA_OUT
);

  wire and_1_out, and_2_out, and_3_out, and_4_out, and_5_out, and_6_out, and_7_out, and_8_out, and_9_out,
       and_10_out, and_11_out, and_12_out, and_13_out, and_14_out, and_15_out, and_16_out, and_17_out,
       and_18_out, and_19_out, and_20_out, and_21_out, and_22_out, and_23_out, and_24_out, and_25_out,
       and_26_out, and_27_out, and_28_out, and_29_out, and_30_out, and_31_out, and_32_out, and_33_out,
       and_34_out, and_35_out, and_36_out, and_37_out, and_38_out, and_39_out, and_40_out, and_41_out,
       and_42_out, and_43_out, and_44_out, and_45_out, and_46_out, and_47_out, and_48_out, and_49_out,
       and_50_out, and_51_out, and_52_out, and_53_out, and_54_out, and_55_out, and_56_out, and_57_out,
       and_58_out, and_59_out, and_60_out, and_61_out, and_62_out, and_63_out, and_64_out, and_65_out,
       and_66_out, and_67_out, and_68_out, and_69_out, and_70_out, and_71_out, and_72_out, and_73_out,
       and_74_out, and_75_out, and_76_out, and_77_out, and_78_out, and_79_out, and_80_out, and_81_out,
       and_82_out, and_83_out, and_84_out, and_85_out, and_86_out, and_87_out, and_88_out, and_89_out,
       and_90_out, and_91_out, and_92_out, and_93_out, and_94_out, and_95_out, and_96_out, and_97_out,
       and_98_out, and_99_out, and_100_out, and_101_out, and_102_out, and_103_out, and_104_out, and_105_out,
       and_106_out, and_107_out, and_108_out, and_109_out, and_110_out, and_111_out, and_112_out,
       and_113_out, and_114_out, and_115_out, and_116_out, and_117_out, and_118_out, and_119_out,
       and_120_out, and_121_out, and_122_out, and_123_out, and_124_out, and_125_out, and_126_out,
       and_127_out, and_128_out, and_129_out, and_130_out, and_131_out, and_132_out, and_133_out,
       and_134_out, and_135_out, and_136_out, and_137_out, and_138_out, and_139_out, and_140_out,
       and_141_out, and_142_out, and_143_out, and_144_out, and_145_out, and_146_out, and_147_out,
       and_148_out, and_149_out, and_150_out, and_151_out, and_152_out, and_153_out, and_154_out,
       and_155_out, and_156_out, and_157_out, and_158_out, and_159_out, and_160_out, and_161_out,
       and_162_out, and_163_out, and_164_out, and_165_out, and_166_out, and_167_out, and_168_out,
       and_169_out, and_170_out, and_171_out, and_172_out, and_173_out, and_174_out, and_175_out,
       and_176_out, and_177_out, and_178_out, and_179_out, and_180_out, and_181_out, and_182_out,
       and_183_out, and_184_out, and_185_out, and_186_out, and_187_out, and_188_out, and_189_out,
       and_190_out, and_191_out, and_192_out, and_193_out, and_194_out, and_195_out, and_196_out,
       and_197_out, and_198_out, and_199_out, and_200_out, and_201_out, and_202_out, and_203_out,
       and_204_out, and_205_out, and_206_out, and_207_out, and_208_out, and_209_out, and_210_out,
       and_211_out, and_212_out, and_213_out, and_214_out, and_215_out, and_216_out, and_217_out,
       and_218_out, and_219_out, and_220_out, and_221_out, and_222_out, and_223_out, and_224_out,
       and_225_out, and_226_out, and_227_out, and_228_out, and_229_out, and_230_out, and_231_out,
       and_232_out, and_233_out, and_234_out, and_235_out, and_236_out, and_237_out, and_238_out,
       and_239_out, and_240_out, and_241_out, and_242_out, and_243_out, and_244_out, and_245_out,
       and_246_out, and_247_out, and_248_out, and_249_out, and_250_out, and_251_out, and_252_out,
       and_253_out, and_254_out, and_255_out, and_256_out, and_257_out, and_258_out, and_259_out,
       and_260_out, and_261_out, and_262_out, and_263_out, and_264_out, and_265_out, and_266_out,
       and_267_out, and_268_out, and_269_out, and_270_out, and_271_out, and_272_out, not_1_out, not_2_out,
       not_3_out, not_4_out, not_5_out, not_6_out, not_7_out, not_8_out, not_9_out, not_10_out, not_11_out,
       not_12_out, not_13_out, not_14_out, not_15_out, not_16_out, not_17_out, not_18_out, not_19_out,
       not_20_out, not_21_out, not_22_out, not_23_out, not_24_out, not_25_out, not_26_out, not_27_out,
       not_28_out, not_29_out, not_30_out, not_31_out, not_32_out, not_33_out, not_34_out, not_35_out,
       not_36_out, not_37_out, not_38_out, not_39_out, not_40_out, not_41_out, not_42_out, not_43_out,
       not_44_out, not_45_out, not_46_out, not_47_out, not_48_out, not_49_out, not_50_out, not_51_out,
       not_52_out, not_53_out, not_54_out, not_55_out, not_56_out, not_57_out, not_58_out, not_59_out,
       not_60_out, not_61_out, not_62_out, not_63_out, not_64_out, not_65_out, not_66_out, not_67_out,
       not_68_out, not_69_out, not_70_out, not_71_out, not_72_out, not_73_out, not_74_out, not_75_out,
       not_76_out, not_77_out, not_78_out, not_79_out, not_80_out, not_81_out, not_82_out, not_83_out,
       not_84_out, not_85_out, not_86_out, not_87_out, not_88_out, not_89_out, not_90_out, not_91_out,
       not_92_out, not_93_out, not_94_out, not_95_out, not_96_out, not_97_out, not_98_out, not_99_out,
       not_100_out, not_101_out, not_102_out, not_103_out, not_104_out, not_105_out, not_106_out,
       not_107_out, not_108_out, not_109_out, not_110_out, not_111_out, not_112_out, not_113_out,
       not_114_out, not_115_out, not_116_out, not_117_out, not_118_out, not_119_out, not_120_out,
       not_121_out, not_122_out, not_123_out, not_124_out, not_125_out, not_126_out, not_127_out,
       not_128_out, or_1_out, or_2_out, or_3_out, or_4_out, or_5_out, or_6_out, or_7_out, or_8_out, or_9_out,
       or_10_out, or_11_out, or_12_out, or_13_out, or_14_out, or_15_out, or_16_out, or_18_out, or_19_out,
       or_20_out, or_21_out, or_22_out, or_23_out, or_24_out, or_25_out, or_26_out, or_27_out, or_28_out,
       or_29_out, or_30_out, or_31_out, or_32_out, or_33_out, or_34_out, or_35_out, or_36_out, or_37_out,
       or_38_out, or_39_out, or_40_out, or_41_out, or_42_out, or_43_out, or_44_out, or_45_out, or_46_out,
       or_47_out, or_48_out, or_49_out, or_50_out, or_51_out, or_52_out, or_53_out, or_54_out, or_55_out,
       or_56_out, or_57_out, or_58_out, or_59_out, or_60_out, or_61_out, or_62_out, or_63_out, or_64_out,
       or_65_out, or_66_out, or_67_out, or_68_out, or_69_out, or_70_out, or_71_out, or_72_out, or_73_out,
       or_74_out, or_75_out, or_76_out, or_77_out, or_78_out, or_79_out, or_80_out, or_81_out, or_82_out,
       or_83_out, or_84_out, or_85_out, or_86_out, or_87_out, or_88_out, or_89_out, or_90_out, or_91_out,
       or_92_out, or_93_out, or_94_out, or_95_out, or_96_out, or_113_out, xor_1_out, xor_2_out, xor_3_out,
       xor_4_out, xor_5_out, xor_6_out, xor_7_out, xor_8_out, xor_9_out, xor_10_out, xor_11_out, xor_12_out,
       xor_13_out, xor_14_out, xor_15_out, xor_16_out, xor_17_out, xor_18_out, xor_19_out, xor_20_out,
       xor_21_out, xor_22_out, xor_23_out, xor_24_out, xor_25_out, xor_26_out, xor_27_out, xor_28_out,
       xor_29_out, xor_30_out, xor_31_out, xor_32_out, xor_33_out, xor_35_out, xor_36_out, xor_37_out,
       xor_38_out, xor_39_out, xor_40_out, xor_41_out, xor_42_out, xor_43_out, xor_44_out, xor_45_out,
       xor_46_out, xor_47_out, xor_48_out, xor_49_out, xor_50_out, xor_51_out, xor_52_out, xor_53_out,
       xor_54_out, xor_55_out, xor_56_out, xor_57_out, xor_58_out, xor_59_out, xor_60_out, xor_61_out,
       xor_62_out, xor_63_out, xor_64_out, xor_65_out, xor_66_out;

  not not_1 (not_1_out, FA);
  not not_2 (not_2_out, FA);
  not not_3 (not_3_out, FA);
  not not_4 (not_4_out, FA);
  not not_5 (not_5_out, FA);
  not not_6 (not_6_out, FA);
  not not_7 (not_7_out, FA);
  not not_8 (not_8_out, FA);
  not not_9 (not_9_out, FA);
  not not_10 (not_10_out, FA);
  not not_11 (not_11_out, FA);
  not not_12 (not_12_out, FA);
  not not_13 (not_13_out, FA);
  not not_14 (not_14_out, FA);
  not not_15 (not_15_out, FA);
  not not_16 (not_16_out, FA);
  and and_1 (and_1_out, 1'b0, FA);
  and and_2 (and_2_out, DATA_IN_B[15], not_1_out);
  and and_3 (and_3_out, 1'b0, FA);
  and and_4 (and_4_out, DATA_IN_B[14], not_2_out);
  and and_5 (and_5_out, 1'b0, FA);
  and and_6 (and_6_out, DATA_IN_B[13], not_3_out);
  and and_7 (and_7_out, 1'b0, FA);
  and and_8 (and_8_out, DATA_IN_B[12], not_4_out);
  and and_9 (and_9_out, 1'b0, FA);
  and and_10 (and_10_out, DATA_IN_B[11], not_5_out);
  and and_11 (and_11_out, 1'b0, FA);
  and and_12 (and_12_out, DATA_IN_B[10], not_6_out);
  and and_13 (and_13_out, 1'b0, FA);
  and and_14 (and_14_out, DATA_IN_B[9], not_7_out);
  and and_15 (and_15_out, 1'b0, FA);
  and and_16 (and_16_out, DATA_IN_B[8], not_8_out);
  and and_17 (and_17_out, 1'b0, FA);
  and and_18 (and_18_out, DATA_IN_B[7], not_9_out);
  and and_19 (and_19_out, 1'b0, FA);
  and and_20 (and_20_out, DATA_IN_B[6], not_10_out);
  and and_21 (and_21_out, 1'b0, FA);
  and and_22 (and_22_out, DATA_IN_B[5], not_11_out);
  and and_23 (and_23_out, 1'b0, FA);
  and and_24 (and_24_out, DATA_IN_B[4], not_12_out);
  and and_25 (and_25_out, 1'b0, FA);
  and and_26 (and_26_out, DATA_IN_B[3], not_13_out);
  and and_27 (and_27_out, 1'b0, FA);
  and and_28 (and_28_out, DATA_IN_B[2], not_14_out);
  and and_29 (and_29_out, 1'b0, FA);
  and and_30 (and_30_out, DATA_IN_B[1], not_15_out);
  and and_31 (and_31_out, 1'b0, FA);
  and and_32 (and_32_out, DATA_IN_B[0], not_16_out);
  or or_1 (or_1_out, and_1_out, and_2_out);
  or or_2 (or_2_out, and_3_out, and_4_out);
  or or_3 (or_3_out, and_5_out, and_6_out);
  or or_4 (or_4_out, and_7_out, and_8_out);
  or or_5 (or_5_out, and_9_out, and_10_out);
  or or_6 (or_6_out, and_11_out, and_12_out);
  or or_7 (or_7_out, and_13_out, and_14_out);
  or or_8 (or_8_out, and_15_out, and_16_out);
  or or_9 (or_9_out, and_17_out, and_18_out);
  or or_10 (or_10_out, and_19_out, and_20_out);
  or or_11 (or_11_out, and_21_out, and_22_out);
  or or_12 (or_12_out, and_23_out, and_24_out);
  or or_13 (or_13_out, and_25_out, and_26_out);
  or or_14 (or_14_out, and_27_out, and_28_out);
  or or_15 (or_15_out, and_29_out, and_30_out);
  or or_16 (or_16_out, and_31_out, and_32_out);
  xor xor_1 (xor_1_out, or_1_out, FB);
  xor xor_2 (xor_2_out, or_2_out, FB);
  xor xor_3 (xor_3_out, or_3_out, FB);
  xor xor_4 (xor_4_out, or_4_out, FB);
  xor xor_5 (xor_5_out, or_5_out, FB);
  xor xor_6 (xor_6_out, or_6_out, FB);
  xor xor_7 (xor_7_out, or_7_out, FB);
  xor xor_8 (xor_8_out, or_8_out, FB);
  xor xor_9 (xor_9_out, or_9_out, FB);
  xor xor_10 (xor_10_out, or_10_out, FB);
  xor xor_11 (xor_11_out, or_11_out, FB);
  xor xor_12 (xor_12_out, or_12_out, FB);
  xor xor_13 (xor_13_out, or_13_out, FB);
  xor xor_14 (xor_14_out, or_14_out, FB);
  xor xor_15 (xor_15_out, or_15_out, FB);
  xor xor_16 (xor_16_out, or_16_out, FB);
  xor xor_17 (xor_17_out, DATA_IN_A[15], xor_1_out);
  and and_33 (and_33_out, DATA_IN_A[15], xor_1_out);
  xor xor_18 (xor_18_out, DATA_IN_A[14], xor_2_out);
  and and_34 (and_34_out, DATA_IN_A[14], xor_2_out);
  xor xor_19 (xor_19_out, DATA_IN_A[13], xor_3_out);
  and and_35 (and_35_out, DATA_IN_A[13], xor_3_out);
  xor xor_20 (xor_20_out, DATA_IN_A[12], xor_4_out);
  and and_36 (and_36_out, DATA_IN_A[12], xor_4_out);
  xor xor_21 (xor_21_out, DATA_IN_A[11], xor_5_out);
  and and_37 (and_37_out, DATA_IN_A[11], xor_5_out);
  xor xor_22 (xor_22_out, DATA_IN_A[10], xor_6_out);
  and and_38 (and_38_out, DATA_IN_A[10], xor_6_out);
  xor xor_23 (xor_23_out, DATA_IN_A[9], xor_7_out);
  and and_39 (and_39_out, DATA_IN_A[9], xor_7_out);
  xor xor_24 (xor_24_out, DATA_IN_A[8], xor_8_out);
  and and_40 (and_40_out, DATA_IN_A[8], xor_8_out);
  xor xor_25 (xor_25_out, DATA_IN_A[7], xor_9_out);
  and and_41 (and_41_out, DATA_IN_A[7], xor_9_out);
  xor xor_26 (xor_26_out, DATA_IN_A[6], xor_10_out);
  and and_42 (and_42_out, DATA_IN_A[6], xor_10_out);
  xor xor_27 (xor_27_out, DATA_IN_A[5], xor_11_out);
  and and_43 (and_43_out, DATA_IN_A[5], xor_11_out);
  xor xor_28 (xor_28_out, DATA_IN_A[4], xor_12_out);
  and and_44 (and_44_out, DATA_IN_A[4], xor_12_out);
  xor xor_29 (xor_29_out, DATA_IN_A[3], xor_13_out);
  and and_45 (and_45_out, DATA_IN_A[3], xor_13_out);
  xor xor_30 (xor_30_out, DATA_IN_A[2], xor_14_out);
  and and_46 (and_46_out, DATA_IN_A[2], xor_14_out);
  xor xor_31 (xor_31_out, DATA_IN_A[1], xor_15_out);
  and and_47 (and_47_out, DATA_IN_A[1], xor_15_out);
  xor xor_32 (xor_32_out, DATA_IN_A[0], xor_16_out);
  and and_48 (and_48_out, DATA_IN_A[0], xor_16_out);
  xor xor_33 (xor_33_out, FA, FB);
  xor xor_34 (V, or_19_out, C);
  xor xor_35 (xor_35_out, xor_17_out, or_19_out);
  and and_49 (and_49_out, xor_17_out, or_19_out);
  xor xor_36 (xor_36_out, xor_18_out, or_21_out);
  and and_50 (and_50_out, xor_18_out, or_21_out);
  xor xor_37 (xor_37_out, xor_19_out, or_23_out);
  and and_51 (and_51_out, xor_19_out, or_23_out);
  xor xor_38 (xor_38_out, xor_20_out, or_25_out);
  and and_52 (and_52_out, xor_20_out, or_25_out);
  xor xor_39 (xor_39_out, xor_21_out, or_27_out);
  and and_53 (and_53_out, xor_21_out, or_27_out);
  xor xor_40 (xor_40_out, xor_22_out, or_29_out);
  and and_54 (and_54_out, xor_22_out, or_29_out);
  xor xor_41 (xor_41_out, xor_23_out, or_31_out);
  and and_55 (and_55_out, xor_23_out, or_31_out);
  xor xor_42 (xor_42_out, xor_24_out, or_33_out);
  and and_56 (and_56_out, xor_24_out, or_33_out);
  xor xor_43 (xor_43_out, xor_25_out, or_35_out);
  and and_57 (and_57_out, xor_25_out, or_35_out);
  xor xor_44 (xor_44_out, xor_26_out, or_37_out);
  and and_58 (and_58_out, xor_26_out, or_37_out);
  xor xor_45 (xor_45_out, xor_27_out, or_39_out);
  and and_59 (and_59_out, xor_27_out, or_39_out);
  xor xor_46 (xor_46_out, xor_28_out, or_41_out);
  and and_60 (and_60_out, xor_28_out, or_41_out);
  xor xor_47 (xor_47_out, xor_29_out, or_43_out);
  and and_61 (and_61_out, xor_29_out, or_43_out);
  xor xor_48 (xor_48_out, xor_30_out, or_45_out);
  and and_62 (and_62_out, xor_30_out, or_45_out);
  xor xor_49 (xor_49_out, xor_31_out, or_47_out);
  and and_63 (and_63_out, xor_31_out, or_47_out);
  xor xor_50 (xor_50_out, xor_32_out, xor_33_out);
  and and_64 (and_64_out, xor_32_out, xor_33_out);
  and and_65 (and_65_out, DATA_IN_B[15], FB);
  and and_66 (and_66_out, DATA_IN_A[15], not_17_out);
  not not_17 (not_17_out, FB);
  and and_67 (and_67_out, DATA_IN_B[14], FB);
  and and_68 (and_68_out, DATA_IN_A[14], not_18_out);
  not not_18 (not_18_out, FB);
  and and_69 (and_69_out, DATA_IN_B[13], FB);
  and and_70 (and_70_out, DATA_IN_A[13], not_19_out);
  not not_19 (not_19_out, FB);
  and and_71 (and_71_out, DATA_IN_B[12], FB);
  and and_72 (and_72_out, DATA_IN_A[12], not_20_out);
  not not_20 (not_20_out, FB);
  and and_73 (and_73_out, DATA_IN_B[11], FB);
  and and_74 (and_74_out, DATA_IN_A[11], not_21_out);
  not not_21 (not_21_out, FB);
  and and_75 (and_75_out, DATA_IN_B[10], FB);
  and and_76 (and_76_out, DATA_IN_A[10], not_22_out);
  not not_22 (not_22_out, FB);
  and and_77 (and_77_out, DATA_IN_B[9], FB);
  and and_78 (and_78_out, DATA_IN_A[9], not_23_out);
  not not_23 (not_23_out, FB);
  and and_79 (and_79_out, DATA_IN_B[8], FB);
  and and_80 (and_80_out, DATA_IN_A[8], not_24_out);
  not not_24 (not_24_out, FB);
  and and_81 (and_81_out, DATA_IN_B[7], FB);
  and and_82 (and_82_out, DATA_IN_A[7], not_25_out);
  not not_25 (not_25_out, FB);
  and and_83 (and_83_out, DATA_IN_B[6], FB);
  and and_84 (and_84_out, DATA_IN_A[6], not_26_out);
  not not_26 (not_26_out, FB);
  and and_85 (and_85_out, DATA_IN_B[5], FB);
  and and_86 (and_86_out, DATA_IN_A[5], not_27_out);
  not not_27 (not_27_out, FB);
  and and_87 (and_87_out, DATA_IN_B[4], FB);
  and and_88 (and_88_out, DATA_IN_A[4], not_28_out);
  not not_28 (not_28_out, FB);
  and and_89 (and_89_out, DATA_IN_B[3], FB);
  and and_90 (and_90_out, DATA_IN_A[3], not_29_out);
  not not_29 (not_29_out, FB);
  and and_91 (and_91_out, DATA_IN_B[2], FB);
  and and_92 (and_92_out, DATA_IN_A[2], not_30_out);
  not not_30 (not_30_out, FB);
  and and_93 (and_93_out, DATA_IN_B[1], FB);
  and and_94 (and_94_out, DATA_IN_A[1], not_31_out);
  not not_31 (not_31_out, FB);
  and and_95 (and_95_out, DATA_IN_B[0], FB);
  and and_96 (and_96_out, DATA_IN_A[0], not_32_out);
  not not_32 (not_32_out, FB);
  or or_17 (C, and_33_out, and_49_out);
  or or_18 (or_18_out, and_65_out, and_66_out);
  or or_19 (or_19_out, and_34_out, and_50_out);
  or or_20 (or_20_out, and_67_out, and_68_out);
  or or_21 (or_21_out, and_35_out, and_51_out);
  or or_22 (or_22_out, and_69_out, and_70_out);
  or or_23 (or_23_out, and_36_out, and_52_out);
  or or_24 (or_24_out, and_71_out, and_72_out);
  or or_25 (or_25_out, and_37_out, and_53_out);
  or or_26 (or_26_out, and_73_out, and_74_out);
  or or_27 (or_27_out, and_38_out, and_54_out);
  or or_28 (or_28_out, and_75_out, and_76_out);
  or or_29 (or_29_out, and_39_out, and_55_out);
  or or_30 (or_30_out, and_77_out, and_78_out);
  or or_31 (or_31_out, and_40_out, and_56_out);
  or or_32 (or_32_out, and_79_out, and_80_out);
  or or_33 (or_33_out, and_41_out, and_57_out);
  or or_34 (or_34_out, and_81_out, and_82_out);
  or or_35 (or_35_out, and_42_out, and_58_out);
  or or_36 (or_36_out, and_83_out, and_84_out);
  or or_37 (or_37_out, and_43_out, and_59_out);
  or or_38 (or_38_out, and_85_out, and_86_out);
  or or_39 (or_39_out, and_44_out, and_60_out);
  or or_40 (or_40_out, and_87_out, and_88_out);
  or or_41 (or_41_out, and_45_out, and_61_out);
  or or_42 (or_42_out, and_89_out, and_90_out);
  or or_43 (or_43_out, and_46_out, and_62_out);
  or or_44 (or_44_out, and_91_out, and_92_out);
  or or_45 (or_45_out, and_47_out, and_63_out);
  or or_46 (or_46_out, and_93_out, and_94_out);
  or or_47 (or_47_out, and_48_out, and_64_out);
  or or_48 (or_48_out, and_95_out, and_96_out);
  and and_97 (and_97_out, DATA_IN_A[15], DATA_IN_B[15]);
  or or_49 (or_49_out, DATA_IN_A[15], DATA_IN_B[15]);
  xor xor_51 (xor_51_out, DATA_IN_A[15], DATA_IN_B[15]);
  not not_33 (not_33_out, DATA_IN_A[15]);
  and and_98 (and_98_out, DATA_IN_A[14], DATA_IN_B[14]);
  or or_50 (or_50_out, DATA_IN_A[14], DATA_IN_B[14]);
  xor xor_52 (xor_52_out, DATA_IN_A[14], DATA_IN_B[14]);
  not not_34 (not_34_out, DATA_IN_A[14]);
  and and_99 (and_99_out, DATA_IN_A[13], DATA_IN_B[13]);
  or or_51 (or_51_out, DATA_IN_A[13], DATA_IN_B[13]);
  xor xor_53 (xor_53_out, DATA_IN_A[13], DATA_IN_B[13]);
  not not_35 (not_35_out, DATA_IN_A[13]);
  and and_100 (and_100_out, DATA_IN_A[12], DATA_IN_B[12]);
  or or_52 (or_52_out, DATA_IN_A[12], DATA_IN_B[12]);
  xor xor_54 (xor_54_out, DATA_IN_A[12], DATA_IN_B[12]);
  not not_36 (not_36_out, DATA_IN_A[12]);
  and and_101 (and_101_out, DATA_IN_A[11], DATA_IN_B[11]);
  or or_53 (or_53_out, DATA_IN_A[11], DATA_IN_B[11]);
  xor xor_55 (xor_55_out, DATA_IN_A[11], DATA_IN_B[11]);
  not not_37 (not_37_out, DATA_IN_A[11]);
  and and_102 (and_102_out, DATA_IN_A[10], DATA_IN_B[10]);
  or or_54 (or_54_out, DATA_IN_A[10], DATA_IN_B[10]);
  xor xor_56 (xor_56_out, DATA_IN_A[10], DATA_IN_B[10]);
  not not_38 (not_38_out, DATA_IN_A[10]);
  and and_103 (and_103_out, DATA_IN_A[9], DATA_IN_B[9]);
  or or_55 (or_55_out, DATA_IN_A[9], DATA_IN_B[9]);
  xor xor_57 (xor_57_out, DATA_IN_A[9], DATA_IN_B[9]);
  not not_39 (not_39_out, DATA_IN_A[9]);
  and and_104 (and_104_out, DATA_IN_A[8], DATA_IN_B[8]);
  or or_56 (or_56_out, DATA_IN_A[8], DATA_IN_B[8]);
  xor xor_58 (xor_58_out, DATA_IN_A[8], DATA_IN_B[8]);
  not not_40 (not_40_out, DATA_IN_A[8]);
  and and_105 (and_105_out, DATA_IN_A[7], DATA_IN_B[7]);
  or or_57 (or_57_out, DATA_IN_A[7], DATA_IN_B[7]);
  xor xor_59 (xor_59_out, DATA_IN_A[7], DATA_IN_B[7]);
  not not_41 (not_41_out, DATA_IN_A[7]);
  and and_106 (and_106_out, DATA_IN_A[6], DATA_IN_B[6]);
  or or_58 (or_58_out, DATA_IN_A[6], DATA_IN_B[6]);
  xor xor_60 (xor_60_out, DATA_IN_A[6], DATA_IN_B[6]);
  not not_42 (not_42_out, DATA_IN_A[6]);
  and and_107 (and_107_out, DATA_IN_A[5], DATA_IN_B[5]);
  or or_59 (or_59_out, DATA_IN_A[5], DATA_IN_B[5]);
  xor xor_61 (xor_61_out, DATA_IN_A[5], DATA_IN_B[5]);
  not not_43 (not_43_out, DATA_IN_A[5]);
  and and_108 (and_108_out, DATA_IN_A[4], DATA_IN_B[4]);
  or or_60 (or_60_out, DATA_IN_A[4], DATA_IN_B[4]);
  xor xor_62 (xor_62_out, DATA_IN_A[4], DATA_IN_B[4]);
  not not_44 (not_44_out, DATA_IN_A[4]);
  and and_109 (and_109_out, DATA_IN_A[3], DATA_IN_B[3]);
  or or_61 (or_61_out, DATA_IN_A[3], DATA_IN_B[3]);
  xor xor_63 (xor_63_out, DATA_IN_A[3], DATA_IN_B[3]);
  not not_45 (not_45_out, DATA_IN_A[3]);
  and and_110 (and_110_out, DATA_IN_A[2], DATA_IN_B[2]);
  or or_62 (or_62_out, DATA_IN_A[2], DATA_IN_B[2]);
  xor xor_64 (xor_64_out, DATA_IN_A[2], DATA_IN_B[2]);
  not not_46 (not_46_out, DATA_IN_A[2]);
  and and_111 (and_111_out, DATA_IN_A[1], DATA_IN_B[1]);
  or or_63 (or_63_out, DATA_IN_A[1], DATA_IN_B[1]);
  xor xor_65 (xor_65_out, DATA_IN_A[1], DATA_IN_B[1]);
  not not_47 (not_47_out, DATA_IN_A[1]);
  and and_112 (and_112_out, DATA_IN_A[0], DATA_IN_B[0]);
  or or_64 (or_64_out, DATA_IN_A[0], DATA_IN_B[0]);
  xor xor_66 (xor_66_out, DATA_IN_A[0], DATA_IN_B[0]);
  not not_48 (not_48_out, DATA_IN_A[0]);
  not not_49 (not_49_out, FA);
  not not_50 (not_50_out, FB);
  not not_51 (not_51_out, FA);
  not not_52 (not_52_out, FB);
  not not_53 (not_53_out, FA);
  not not_54 (not_54_out, FB);
  not not_55 (not_55_out, FA);
  not not_56 (not_56_out, FB);
  not not_57 (not_57_out, FA);
  not not_58 (not_58_out, FB);
  not not_59 (not_59_out, FA);
  not not_60 (not_60_out, FB);
  not not_61 (not_61_out, FA);
  not not_62 (not_62_out, FB);
  not not_63 (not_63_out, FA);
  not not_64 (not_64_out, FB);
  not not_65 (not_65_out, FA);
  not not_66 (not_66_out, FB);
  not not_67 (not_67_out, FA);
  not not_68 (not_68_out, FB);
  not not_69 (not_69_out, FA);
  not not_70 (not_70_out, FB);
  not not_71 (not_71_out, FA);
  not not_72 (not_72_out, FB);
  not not_73 (not_73_out, FA);
  not not_74 (not_74_out, FB);
  not not_75 (not_75_out, FA);
  not not_76 (not_76_out, FB);
  not not_77 (not_77_out, FA);
  not not_78 (not_78_out, FB);
  not not_79 (not_79_out, FA);
  not not_80 (not_80_out, FB);
  and and_113 (and_113_out, not_49_out, and_97_out, not_50_out);
  and and_114 (and_114_out, not_49_out, or_49_out, FB);
  and and_115 (and_115_out, FA, xor_51_out, not_50_out);
  and and_116 (and_116_out, FA, not_33_out, FB);
  and and_117 (and_117_out, not_51_out, and_98_out, not_52_out);
  and and_118 (and_118_out, not_51_out, or_50_out, FB);
  and and_119 (and_119_out, FA, xor_52_out, not_52_out);
  and and_120 (and_120_out, FA, not_34_out, FB);
  and and_121 (and_121_out, not_53_out, and_99_out, not_54_out);
  and and_122 (and_122_out, not_53_out, or_51_out, FB);
  and and_123 (and_123_out, FA, xor_53_out, not_54_out);
  and and_124 (and_124_out, FA, not_35_out, FB);
  and and_125 (and_125_out, not_55_out, and_100_out, not_56_out);
  and and_126 (and_126_out, not_55_out, or_52_out, FB);
  and and_127 (and_127_out, FA, xor_54_out, not_56_out);
  and and_128 (and_128_out, FA, not_36_out, FB);
  and and_129 (and_129_out, not_57_out, and_101_out, not_58_out);
  and and_130 (and_130_out, not_57_out, or_53_out, FB);
  and and_131 (and_131_out, FA, xor_55_out, not_58_out);
  and and_132 (and_132_out, FA, not_37_out, FB);
  and and_133 (and_133_out, not_59_out, and_102_out, not_60_out);
  and and_134 (and_134_out, not_59_out, or_54_out, FB);
  and and_135 (and_135_out, FA, xor_56_out, not_60_out);
  and and_136 (and_136_out, FA, not_38_out, FB);
  and and_137 (and_137_out, not_61_out, and_103_out, not_62_out);
  and and_138 (and_138_out, not_61_out, or_55_out, FB);
  and and_139 (and_139_out, FA, xor_57_out, not_62_out);
  and and_140 (and_140_out, FA, not_39_out, FB);
  and and_141 (and_141_out, not_63_out, and_104_out, not_64_out);
  and and_142 (and_142_out, not_63_out, or_56_out, FB);
  and and_143 (and_143_out, FA, xor_58_out, not_64_out);
  and and_144 (and_144_out, FA, not_40_out, FB);
  and and_145 (and_145_out, not_65_out, and_105_out, not_66_out);
  and and_146 (and_146_out, not_65_out, or_57_out, FB);
  and and_147 (and_147_out, FA, xor_59_out, not_66_out);
  and and_148 (and_148_out, FA, not_41_out, FB);
  and and_149 (and_149_out, not_67_out, and_106_out, not_68_out);
  and and_150 (and_150_out, not_67_out, or_58_out, FB);
  and and_151 (and_151_out, FA, xor_60_out, not_68_out);
  and and_152 (and_152_out, FA, not_42_out, FB);
  and and_153 (and_153_out, not_69_out, and_107_out, not_70_out);
  and and_154 (and_154_out, not_69_out, or_59_out, FB);
  and and_155 (and_155_out, FA, xor_61_out, not_70_out);
  and and_156 (and_156_out, FA, not_43_out, FB);
  and and_157 (and_157_out, not_71_out, and_108_out, not_72_out);
  and and_158 (and_158_out, not_71_out, or_60_out, FB);
  and and_159 (and_159_out, FA, xor_62_out, not_72_out);
  and and_160 (and_160_out, FA, not_44_out, FB);
  and and_161 (and_161_out, not_73_out, and_109_out, not_74_out);
  and and_162 (and_162_out, not_73_out, or_61_out, FB);
  and and_163 (and_163_out, FA, xor_63_out, not_74_out);
  and and_164 (and_164_out, FA, not_45_out, FB);
  and and_165 (and_165_out, not_75_out, and_110_out, not_76_out);
  and and_166 (and_166_out, not_75_out, or_62_out, FB);
  and and_167 (and_167_out, FA, xor_64_out, not_76_out);
  and and_168 (and_168_out, FA, not_46_out, FB);
  and and_169 (and_169_out, not_77_out, and_111_out, not_78_out);
  and and_170 (and_170_out, not_77_out, or_63_out, FB);
  and and_171 (and_171_out, FA, xor_65_out, not_78_out);
  and and_172 (and_172_out, FA, not_47_out, FB);
  and and_173 (and_173_out, not_79_out, and_112_out, not_80_out);
  and and_174 (and_174_out, not_79_out, or_64_out, FB);
  and and_175 (and_175_out, FA, xor_66_out, not_80_out);
  and and_176 (and_176_out, FA, not_48_out, FB);
  or or_65 (or_65_out, and_113_out, and_114_out, and_115_out, and_116_out);
  not not_81 (not_81_out, FB);
  or or_66 (or_66_out, and_117_out, and_118_out, and_119_out, and_120_out);
  not not_82 (not_82_out, FB);
  or or_67 (or_67_out, and_121_out, and_122_out, and_123_out, and_124_out);
  not not_83 (not_83_out, FB);
  or or_68 (or_68_out, and_125_out, and_126_out, and_127_out, and_128_out);
  not not_84 (not_84_out, FB);
  or or_69 (or_69_out, and_129_out, and_130_out, and_131_out, and_132_out);
  not not_85 (not_85_out, FB);
  or or_70 (or_70_out, and_133_out, and_134_out, and_135_out, and_136_out);
  not not_86 (not_86_out, FB);
  or or_71 (or_71_out, and_137_out, and_138_out, and_139_out, and_140_out);
  not not_87 (not_87_out, FB);
  or or_72 (or_72_out, and_141_out, and_142_out, and_143_out, and_144_out);
  not not_88 (not_88_out, FB);
  or or_73 (or_73_out, and_145_out, and_146_out, and_147_out, and_148_out);
  not not_89 (not_89_out, FB);
  or or_74 (or_74_out, and_149_out, and_150_out, and_151_out, and_152_out);
  not not_90 (not_90_out, FB);
  or or_75 (or_75_out, and_153_out, and_154_out, and_155_out, and_156_out);
  not not_91 (not_91_out, FB);
  or or_76 (or_76_out, and_157_out, and_158_out, and_159_out, and_160_out);
  not not_92 (not_92_out, FB);
  or or_77 (or_77_out, and_161_out, and_162_out, and_163_out, and_164_out);
  not not_93 (not_93_out, FB);
  or or_78 (or_78_out, and_165_out, and_166_out, and_167_out, and_168_out);
  not not_94 (not_94_out, FB);
  or or_79 (or_79_out, and_169_out, and_170_out, and_171_out, and_172_out);
  not not_95 (not_95_out, FB);
  or or_80 (or_80_out, and_173_out, and_174_out, and_175_out, and_176_out);
  not not_96 (not_96_out, FB);
  and and_177 (and_177_out, 1'b0, FB);
  or or_81 (or_81_out, and_177_out, and_178_out);
  and and_178 (and_178_out, DATA_IN_A[14], not_81_out);
  and and_179 (and_179_out, DATA_IN_A[15], FB);
  or or_82 (or_82_out, and_179_out, and_180_out);
  and and_180 (and_180_out, DATA_IN_A[13], not_82_out);
  and and_181 (and_181_out, DATA_IN_A[14], FB);
  or or_83 (or_83_out, and_181_out, and_182_out);
  and and_182 (and_182_out, DATA_IN_A[12], not_83_out);
  and and_183 (and_183_out, DATA_IN_A[13], FB);
  or or_84 (or_84_out, and_183_out, and_184_out);
  and and_184 (and_184_out, DATA_IN_A[11], not_84_out);
  and and_185 (and_185_out, DATA_IN_A[12], FB);
  or or_85 (or_85_out, and_185_out, and_186_out);
  and and_186 (and_186_out, DATA_IN_A[10], not_85_out);
  and and_187 (and_187_out, DATA_IN_A[11], FB);
  or or_86 (or_86_out, and_187_out, and_188_out);
  and and_188 (and_188_out, DATA_IN_A[9], not_86_out);
  and and_189 (and_189_out, DATA_IN_A[10], FB);
  or or_87 (or_87_out, and_189_out, and_190_out);
  and and_190 (and_190_out, DATA_IN_A[8], not_87_out);
  and and_191 (and_191_out, DATA_IN_A[9], FB);
  or or_88 (or_88_out, and_191_out, and_192_out);
  and and_192 (and_192_out, DATA_IN_A[7], not_88_out);
  and and_193 (and_193_out, DATA_IN_A[8], FB);
  or or_89 (or_89_out, and_193_out, and_194_out);
  and and_194 (and_194_out, DATA_IN_A[6], not_89_out);
  and and_195 (and_195_out, DATA_IN_A[7], FB);
  or or_90 (or_90_out, and_195_out, and_196_out);
  and and_196 (and_196_out, DATA_IN_A[5], not_90_out);
  and and_197 (and_197_out, DATA_IN_A[6], FB);
  or or_91 (or_91_out, and_197_out, and_198_out);
  and and_198 (and_198_out, DATA_IN_A[4], not_91_out);
  and and_199 (and_199_out, DATA_IN_A[5], FB);
  or or_92 (or_92_out, and_199_out, and_200_out);
  and and_200 (and_200_out, DATA_IN_A[3], not_92_out);
  and and_201 (and_201_out, DATA_IN_A[4], FB);
  or or_93 (or_93_out, and_201_out, and_202_out);
  and and_202 (and_202_out, DATA_IN_A[2], not_93_out);
  and and_203 (and_203_out, DATA_IN_A[3], FB);
  or or_94 (or_94_out, and_203_out, and_204_out);
  and and_204 (and_204_out, DATA_IN_A[1], not_94_out);
  and and_205 (and_205_out, DATA_IN_A[2], FB);
  or or_95 (or_95_out, and_205_out, and_206_out);
  and and_206 (and_206_out, DATA_IN_A[0], not_95_out);
  and and_207 (and_207_out, DATA_IN_A[1], FB);
  or or_96 (or_96_out, and_207_out, and_208_out);
  and and_208 (and_208_out, 1'b0, not_96_out);
  not not_97 (not_97_out, UA);
  not not_98 (not_98_out, UB);
  not not_99 (not_99_out, UA);
  not not_100 (not_100_out, UB);
  not not_101 (not_101_out, UA);
  not not_102 (not_102_out, UB);
  not not_103 (not_103_out, UA);
  not not_104 (not_104_out, UB);
  not not_105 (not_105_out, UA);
  not not_106 (not_106_out, UB);
  not not_107 (not_107_out, UA);
  not not_108 (not_108_out, UB);
  not not_109 (not_109_out, UA);
  not not_110 (not_110_out, UB);
  not not_111 (not_111_out, UA);
  not not_112 (not_112_out, UB);
  not not_113 (not_113_out, UA);
  not not_114 (not_114_out, UB);
  not not_115 (not_115_out, UA);
  not not_116 (not_116_out, UB);
  not not_117 (not_117_out, UA);
  not not_118 (not_118_out, UB);
  not not_119 (not_119_out, UA);
  not not_120 (not_120_out, UB);
  not not_121 (not_121_out, UA);
  not not_122 (not_122_out, UB);
  not not_123 (not_123_out, UA);
  not not_124 (not_124_out, UB);
  not not_125 (not_125_out, UA);
  not not_126 (not_126_out, UB);
  not not_127 (not_127_out, UA);
  not not_128 (not_128_out, UB);
  and and_209 (and_209_out, not_97_out, xor_35_out, not_98_out);
  and and_210 (and_210_out, not_97_out, or_65_out, UB);
  and and_211 (and_211_out, UA, or_81_out, not_98_out);
  and and_212 (and_212_out, UA, or_18_out, UB);
  and and_213 (and_213_out, not_99_out, xor_36_out, not_100_out);
  and and_214 (and_214_out, not_99_out, or_66_out, UB);
  and and_215 (and_215_out, UA, or_82_out, not_100_out);
  and and_216 (and_216_out, UA, or_20_out, UB);
  and and_217 (and_217_out, not_101_out, xor_37_out, not_102_out);
  and and_218 (and_218_out, not_101_out, or_67_out, UB);
  and and_219 (and_219_out, UA, or_83_out, not_102_out);
  and and_220 (and_220_out, UA, or_22_out, UB);
  and and_221 (and_221_out, not_103_out, xor_38_out, not_104_out);
  and and_222 (and_222_out, not_103_out, or_68_out, UB);
  and and_223 (and_223_out, UA, or_84_out, not_104_out);
  and and_224 (and_224_out, UA, or_24_out, UB);
  and and_225 (and_225_out, not_105_out, xor_39_out, not_106_out);
  and and_226 (and_226_out, not_105_out, or_69_out, UB);
  and and_227 (and_227_out, UA, or_85_out, not_106_out);
  and and_228 (and_228_out, UA, or_26_out, UB);
  and and_229 (and_229_out, not_107_out, xor_40_out, not_108_out);
  and and_230 (and_230_out, not_107_out, or_70_out, UB);
  and and_231 (and_231_out, UA, or_86_out, not_108_out);
  and and_232 (and_232_out, UA, or_28_out, UB);
  and and_233 (and_233_out, not_109_out, xor_41_out, not_110_out);
  and and_234 (and_234_out, not_109_out, or_71_out, UB);
  and and_235 (and_235_out, UA, or_87_out, not_110_out);
  and and_236 (and_236_out, UA, or_30_out, UB);
  and and_237 (and_237_out, not_111_out, xor_42_out, not_112_out);
  and and_238 (and_238_out, not_111_out, or_72_out, UB);
  and and_239 (and_239_out, UA, or_88_out, not_112_out);
  and and_240 (and_240_out, UA, or_32_out, UB);
  and and_241 (and_241_out, not_113_out, xor_43_out, not_114_out);
  and and_242 (and_242_out, not_113_out, or_73_out, UB);
  and and_243 (and_243_out, UA, or_89_out, not_114_out);
  and and_244 (and_244_out, UA, or_34_out, UB);
  and and_245 (and_245_out, not_115_out, xor_44_out, not_116_out);
  and and_246 (and_246_out, not_115_out, or_74_out, UB);
  and and_247 (and_247_out, UA, or_90_out, not_116_out);
  and and_248 (and_248_out, UA, or_36_out, UB);
  and and_249 (and_249_out, not_117_out, xor_45_out, not_118_out);
  and and_250 (and_250_out, not_117_out, or_75_out, UB);
  and and_251 (and_251_out, UA, or_91_out, not_118_out);
  and and_252 (and_252_out, UA, or_38_out, UB);
  and and_253 (and_253_out, not_119_out, xor_46_out, not_120_out);
  and and_254 (and_254_out, not_119_out, or_76_out, UB);
  and and_255 (and_255_out, UA, or_92_out, not_120_out);
  and and_256 (and_256_out, UA, or_40_out, UB);
  and and_257 (and_257_out, not_121_out, xor_47_out, not_122_out);
  and and_258 (and_258_out, not_121_out, or_77_out, UB);
  and and_259 (and_259_out, UA, or_93_out, not_122_out);
  and and_260 (and_260_out, UA, or_42_out, UB);
  and and_261 (and_261_out, not_123_out, xor_48_out, not_124_out);
  and and_262 (and_262_out, not_123_out, or_78_out, UB);
  and and_263 (and_263_out, UA, or_94_out, not_124_out);
  and and_264 (and_264_out, UA, or_44_out, UB);
  and and_265 (and_265_out, not_125_out, xor_49_out, not_126_out);
  and and_266 (and_266_out, not_125_out, or_79_out, UB);
  and and_267 (and_267_out, UA, or_95_out, not_126_out);
  and and_268 (and_268_out, UA, or_46_out, UB);
  and and_269 (and_269_out, not_127_out, xor_50_out, not_128_out);
  and and_270 (and_270_out, not_127_out, or_80_out, UB);
  and and_271 (and_271_out, UA, or_96_out, not_128_out);
  and and_272 (and_272_out, UA, or_48_out, UB);
  or or_97 (DATA_OUT[15], and_209_out, and_210_out, and_211_out, and_212_out);
  or or_98 (DATA_OUT[14], and_213_out, and_214_out, and_215_out, and_216_out);
  or or_99 (DATA_OUT[13], and_217_out, and_218_out, and_219_out, and_220_out);
  or or_100 (DATA_OUT[12], and_221_out, and_222_out, and_223_out, and_224_out);
  or or_101 (DATA_OUT[11], and_225_out, and_226_out, and_227_out, and_228_out);
  or or_102 (DATA_OUT[10], and_229_out, and_230_out, and_231_out, and_232_out);
  or or_103 (DATA_OUT[9], and_233_out, and_234_out, and_235_out, and_236_out);
  or or_104 (DATA_OUT[8], and_237_out, and_238_out, and_239_out, and_240_out);
  or or_105 (DATA_OUT[7], and_241_out, and_242_out, and_243_out, and_244_out);
  or or_106 (DATA_OUT[6], and_245_out, and_246_out, and_247_out, and_248_out);
  or or_107 (DATA_OUT[5], and_249_out, and_250_out, and_251_out, and_252_out);
  or or_108 (DATA_OUT[4], and_253_out, and_254_out, and_255_out, and_256_out);
  or or_109 (DATA_OUT[3], and_257_out, and_258_out, and_259_out, and_260_out);
  or or_110 (DATA_OUT[2], and_261_out, and_262_out, and_263_out, and_264_out);
  or or_111 (DATA_OUT[1], and_265_out, and_266_out, and_267_out, and_268_out);
  or or_112 (DATA_OUT[0], and_269_out, and_270_out, and_271_out, and_272_out);
  not not_129 (Z, or_113_out);
  or or_113 (or_113_out, DATA_OUT[0], DATA_OUT[1], DATA_OUT[2], DATA_OUT[3], DATA_OUT[4], DATA_OUT[5], DATA_OUT[6], DATA_OUT[7], DATA_OUT[8], DATA_OUT[9], DATA_OUT[10], DATA_OUT[11], DATA_OUT[12], DATA_OUT[13], DATA_OUT[14], DATA_OUT[15]);

  assign N = DATA_OUT[15];
endmodule

module register_4bit (
  input  CLOCK,
  input  [3:0] DATA_IN,
  input  LOAD,
  input  in_4,
  output [3:0] DATA_OUT
);

  wire and_3_out, and_4_out, and_5_out, and_6_out, and_7_out, and_8_out, and_9_out, and_10_out, nand_1_out,
       nand_2_out, nand_3_out, nand_4_out, nand_5_out, nand_6_out, nand_7_out, nand_8_out, nand_9_out,
       nand_10_out, nand_11_out, nand_12_out, nand_13_out, nand_14_out, nand_15_out, nand_16_out,
       nand_17_out, nand_18_out, nand_19_out, nand_20_out, nand_21_out, nand_22_out, nand_23_out,
       nand_24_out, nand_26_out, nand_28_out, nand_30_out, nand_32_out, not_2_out, not_3_out, not_4_out,
       not_5_out, not_6_out, not_7_out, not_8_out, not_9_out, not_10_out, not_11_out, not_12_out, not_13_out,
       not_14_out, not_15_out, not_16_out, not_17_out, or_1_out, or_3_out, or_4_out, or_5_out, or_6_out;
  wire [3:0] and_1_out, and_2_out, not_1_out, or_2_out;

  or or_1 (or_1_out, LOAD, in_4);
  assign or_2_out = and_1_out | and_2_out;  // OR_Gate or_2, 4 bits wide
  assign and_1_out = {4{in_4}} & 4'b0000;  // AND_Gate and_1, 4 bits wide
  assign not_1_out = ~{4{in_4}};  // NOT_Gate not_1, 4 bits wide
  not not_2 (not_2_out, or_1_out);
  not not_3 (not_3_out, or_1_out);
  not not_4 (not_4_out, or_1_out);
  not not_5 (not_5_out, or_1_out);
  assign and_2_out = not_1_out & DATA_IN;  // AND_Gate and_2, 4 bits wide
  and and_3 (and_3_out, or_2_out[3], or_1_out);
  and and_4 (and_4_out, DATA_OUT[3], not_2_out);
  and and_5 (and_5_out, or_2_out[2], or_1_out);
  and and_6 (and_6_out, DATA_OUT[2], not_3_out);
  and and_7 (and_7_out, or_2_out[1], or_1_out);
  and and_8 (and_8_out, DATA_OUT[1], not_4_out);
  and and_9 (and_9_out, or_2_out[0], or_1_out);
  and and_10 (and_10_out, DATA_OUT[0], not_5_out);
  or or_3 (or_3_out, and_3_out, and_4_out);
  not not_6 (not_6_out, or_3_out);
  or or_4 (or_4_out, and_5_out, and_6_out);
  not not_7 (not_7_out, or_4_out);
  or or_5 (or_5_out, and_7_out, and_8_out);
  not not_8 (not_8_out, or_5_out);
  or or_6 (or_6_out, and_9_out, and_10_out);
  not not_9 (not_9_out, or_6_out);
  nand nand_1 (nand_1_out, or_3_out, CLOCK);
  nand nand_2 (nand_2_out, CLOCK, not_6_out);
  nand nand_3 (nand_3_out, or_4_out, CLOCK);
  nand nand_4 (nand_4_out, CLOCK, not_7_out);
  nand nand_5 (nand_5_out, or_5_out, CLOCK);
  nand nand_6 (nand_6_out, CLOCK, not_8_out);
  nand nand_7 (nand_7_out, or_6_out, CLOCK);
  nand nand_8 (nand_8_out, CLOCK, not_9_out);
  nand nand_9 (nand_9_out, nand_1_out, nand_10_out);
  nand nand_10 (nand_10_out, nand_9_out, nand_2_out);
  nand nand_11 (nand_11_out, nand_3_out, nand_12_out);
  nand nand_12 (nand_12_out, nand_11_out, nand_4_out);
  nand nand_13 (nand_13_out, nand_5_out, nand_14_out);
  nand nand_14 (nand_14_out, nand_13_out, nand_6_out);
  nand nand_15 (nand_15_out, nand_7_out, nand_16_out);
  nand nand_16 (nand_16_out, nand_15_out, nand_8_out);
  not not_10 (not_10_out, nand_9_out);
  not not_11 (not_11_out, CLOCK);
  not not_12 (not_12_out, nand_11_out);
  not not_13 (not_13_out, CLOCK);
  not not_14 (not_14_out, nand_13_out);
  not not_15 (not_15_out, CLOCK);
  not not_16 (not_16_out, nand_15_out);
  not not_17 (not_17_out, CLOCK);
  nand nand_17 (nand_17_out, nand_9_out, not_11_out);
  nand nand_18 (nand_18_out, not_11_out, not_10_out);
  nand nand_19 (nand_19_out, nand_11_out, not_13_out);
  nand nand_20 (nand_20_out, not_13_out, not_12_out);
  nand nand_21 (nand_21_out, nand_13_out, not_15_out);
  nand nand_22 (nand_22_out, not_15_out, not_14_out);
  nand nand_23 (nand_23_out, nand_15_out, not_17_out);
  nand nand_24 (nand_24_out, not_17_out, not_16_out);
  nand nand_25 (DATA_OUT[3], nand_17_out, nand_26_out);
  nand nand_26 (nand_26_out, DATA_OUT[3], nand_18_out);
  nand nand_27 (DATA_OUT[2], nand_19_out, nand_28_out);
  nand nand_28 (nand_28_out, DATA_OUT[2], nand_20_out);
  nand nand_29 (DATA_OUT[1], nand_21_out, nand_30_out);
  nand nand_30 (nand_30_out, DATA_OUT[1], nand_22_out);
  nand nand_31 (DATA_OUT[0], nand_23_out, nand_32_out);
  nand nand_32 (nand_32_out, DATA_OUT[0], nand_24_out);
endmodule

module register_16bit (
  input  CLOCK,
  input  LOAD,
  input  [15:0] DATA_IN,
  input  RESET,
  output [15:0] DATA_OUT
);

  wire and_3_out, and_4_out, and_5_out, and_6_out, and_7_out, and_8_out, and_9_out, and_10_out, and_11_out,
       and_12_out, and_13_out, and_14_out, and_15_out, and_16_out, and_17_out, and_18_out, and_19_out,
       and_20_out, and_21_out, and_22_out, and_23_out, and_24_out, and_25_out, and_26_out, and_27_out,
       and_28_out, and_29_out, and_30_out, and_31_out, and_32_out, and_33_out, and_34_out, nand_1_out,
       nand_2_out, nand_3_out, nand_4_out, nand_5_out, nand_6_out, nand_7_out, nand_8_out, nand_9_out,
       nand_10_out, nand_11_out, nand_12_out, nand_13_out, nand_14_out, nand_15_out, nand_16_out,
       nand_17_out, nand_18_out, nand_19_out, nand_20_out, nand_21_out, nand_22_out, nand_23_out,
       nand_24_out, nand_25_out, nand_26_out, nand_27_out, nand_28_out, nand_29_out, nand_30_out,
       nand_31_out, nand_32_out, nand_34_out, nand_36_out, nand_38_out, nand_40_out, nand_42_out,
       nand_44_out, nand_46_out, nand_48_out, nand_50_out, nand_52_out, nand_54_out, nand_56_out,
       nand_58_out, nand_60_out, nand_62_out, nand_64_out, not_1_out, not_2_out, not_3_out, not_4_out,
       not_5_out, not_6_out, not_7_out, not_8_out, not_9_out, not_10_out, not_11_out, not_12_out, not_13_out,
       not_14_out, not_15_out, not_16_out, not_18_out, not_19_out, not_20_out, not_21_out, not_22_out,
       not_23_out, not_24_out, not_25_out, not_26_out, not_27_out, not_28_out, not_29_out, not_30_out,
       not_31_out, not_32_out, not_33_out, or_1_out, or_3_out, or_4_out, or_5_out, or_6_out, or_7_out,
       or_8_out, or_9_out, or_10_out, or_11_out, or_12_out, or_13_out, or_14_out, or_15_out, or_16_out,
       or_17_out, or_18_out;
  wire [15:0] and_1_out, and_2_out, not_17_out, or_2_out;

  or or_1 (or_1_out, LOAD, RESET);
  not not_1 (not_1_out, or_1_out);
  not not_2 (not_2_out, or_1_out);
  not not_3 (not_3_out, or_1_out);
  not not_4 (not_4_out, or_1_out);
  not not_5 (not_5_out, or_1_out);
  not not_6 (not_6_out, or_1_out);
  not not_7 (not_7_out, or_1_out);
  not not_8 (not_8_out, or_1_out);
  not not_9 (not_9_out, or_1_out);
  not not_10 (not_10_out, or_1_out);
  not not_11 (not_11_out, or_1_out);
  not not_12 (not_12_out, or_1_out);
  not not_13 (not_13_out, or_1_out);
  not not_14 (not_14_out, or_1_out);
  not not_15 (not_15_out, or_1_out);
  not not_16 (not_16_out, or_1_out);
  assign or_2_out = and_1_out | and_2_out;  // OR_Gate or_2, 16 bits wide
  assign and_1_out = not_17_out & DATA_IN;  // AND_Gate and_1, 16 bits wide
  assign and_2_out = {16{RESET}} & {16{1'b0}};  // AND_Gate and_2, 16 bits wide
  assign not_17_out = ~{16{RESET}};  // NOT_Gate not_17, 16 bits wide
  and and_3 (and_3_out, or_2_out[15], or_1_out);
  and and_4 (and_4_out, DATA_OUT[15], not_1_out);
  and and_5 (and_5_out, or_2_out[14], or_1_out);
  and and_6 (and_6_out, DATA_OUT[14], not_2_out);
  and and_7 (and_7_out, or_2_out[13], or_1_out);
  and and_8 (and_8_out, DATA_OUT[13], not_3_out);
  and and_9 (and_9_out, or_2_out[12], or_1_out);
  and and_10 (and_10_out, DATA_OUT[12], not_4_out);
  and and_11 (and_11_out, or_2_out[11], or_1_out);
  and and_12 (and_12_out, DATA_OUT[11], not_5_out);
  and and_13 (and_13_out, or_2_out[10], or_1_out);
  and and_14 (and_14_out, DATA_OUT[10], not_6_out);
  and and_15 (and_15_out, or_2_out[9], or_1_out);
  and and_16 (and_16_out, DATA_OUT[9], not_7_out);
  and and_17 (and_17_out, or_2_out[8], or_1_out);
  and and_18 (and_18_out, DATA_OUT[8], not_8_out);
  and and_19 (and_19_out, or_2_out[7], or_1_out);
  and and_20 (and_20_out, DATA_OUT[7], not_9_out);
  and and_21 (and_21_out, or_2_out[6], or_1_out);
  and and_22 (and_22_out, DATA_OUT[6], not_10_out);
  and and_23 (and_23_out, or_2_out[5], or_1_out);
  and and_24 (and_24_out, DATA_OUT[5], not_11_out);
  and and_25 (and_25_out, or_2_out[4], or_1_out);
  and and_26 (and_26_out, DATA_OUT[4], not_12_out);
  and and_27 (and_27_out, or_2_out[3], or_1_out);
  and and_28 (and_28_out, DATA_OUT[3], not_13_out);
  and and_29 (and_29_out, or_2_out[2], or_1_out);
  and and_30 (and_30_out, DATA_OUT[2], not_14_out);
  and and_31 (and_31_out, or_2_out[1], or_1_out);
  and and_32 (and_32_out, DATA_OUT[1], not_15_out);
  and and_33 (and_33_out, or_2_out[0], or_1_out);
  and and_34 (and_34_out, DATA_OUT[0], not_16_out);
  or or_3 (or_3_out, and_3_out, and_4_out);
  not not_18 (not_18_out, or_3_out);
  or or_4 (or_4_out, and_5_out, and_6_out);
  not not_19 (not_19_out, or_4_out);
  or or_5 (or_5_out, and_7_out, and_8_out);
  not not_20 (not_20_out, or_5_out);
  or or_6 (or_6_out, and_9_out, and_10_out);
  not not_21 (not_21_out, or_6_out);
  or or_7 (or_7_out, and_11_out, and_12_out);
  not not_22 (not_22_out, or_7_out);
  or or_8 (or_8_out, and_13_out, and_14_out);
  not not_23 (not_23_out, or_8_out);
  or or_9 (or_9_out, and_15_out, and_16_out);
  not not_24 (not_24_out, or_9_out);
  or or_10 (or_10_out, and_17_out, and_18_out);
  not not_25 (not_25_out, or_10_out);
  or or_11 (or_11_out, and_19_out, and_20_out);
  not not_26 (not_26_out, or_11_out);
  or or_12 (or_12_out, and_21_out, and_22_out);
  not not_27 (not_27_out, or_12_out);
  or or_13 (or_13_out, and_23_out, and_24_out);
  not not_28 (not_28_out, or_13_out);
  or or_14 (or_14_out, and_25_out, and_26_out);
  not not_29 (not_29_out, or_14_out);
  or or_15 (or_15_out, and_27_out, and_28_out);
  not not_30 (not_30_out, or_15_out);
  or or_16 (or_16_out, and_29_out, and_30_out);
  not not_31 (not_31_out, or_16_out);
  or or_17 (or_17_out, and_31_out, and_32_out);
  not not_32 (not_32_out, or_17_out);
  or or_18 (or_18_out, and_33_out, and_34_out);
  not not_33 (not_33_out, or_18_out);
  nand nand_1 (nand_1_out, or_3_out, CLOCK);
  nand nand_2 (nand_2_out, CLOCK, not_18_out);
  nand nand_3 (nand_3_out, or_4_out, CLOCK);
  nand nand_4 (nand_4_out, CLOCK, not_19_out);
  nand nand_5 (nand_5_out, or_5_out, CLOCK);
  nand nand_6 (nand_6_out, CLOCK, not_20_out);
  nand nand_7 (nand_7_out, or_6_out, CLOCK);
  nand nand_8 (nand_8_out, CLOCK, not_21_out);
  nand nand_9 (nand_9_out, or_7_out, CLOCK);
  nand nand_10 (nand_10_out, CLOCK, not_22_out);
  nand nand_11 (nand_11_out, or_8_out, CLOCK);
  nand nand_12 (nand_12_out, CLOCK, not_23_out);
  nand nand_13 (nand_13_out, or_9_out, CLOCK);
  nand nand_14 (nand_14_out, CLOCK, not_24_out);
  nand nand_15 (nand_15_out, or_10_out, CLOCK);
  nand nand_16 (nand_16_out, CLOCK, not_25_out);
  nand nand_17 (nand_17_out, or_11_out, CLOCK);
  nand nand_18 (nand_18_out, CLOCK, not_26_out);
  nand nand_19 (nand_19_out, or_12_out, CLOCK);
  nand nand_20 (nand_20_out, CLOCK, not_27_out);
  nand nand_21 (nand_21_out, or_13_out, CLOCK);
  nand nand_22 (nand_22_out, CLOCK, not_28_out);
  nand nand_23 (nand_23_out, or_14_out, CLOCK);
  nand nand_24 (nand_24_out, CLOCK, not_29_out);
  nand nand_25 (nand_25_out, or_15_out, CLOCK);
  nand nand_26 (nand_26_out, CLOCK, not_30_out);
  nand nand_27 (nand_27_out, or_16_out, CLOCK);
  nand nand_28 (nand_28_out, CLOCK, not_31_out);
  nand nand_29 (nand_29_out, or_17_out, CLOCK);
  nand nand_30 (nand_30_out, CLOCK, not_32_out);
  nand nand_31 (nand_31_out, or_18_out, CLOCK);
  nand nand_32 (nand_32_out, CLOCK, not_33_out);
  nand nand_33 (DATA_OUT[15], nand_1_out, nand_34_out);
  nand nand_34 (nand_34_out, DATA_OUT[15], nand_2_out);
  nand nand_35 (DATA_OUT[14], nand_3_out, nand_36_out);
  nand nand_36 (nand_36_out, DATA_OUT[14], nand_4_out);
  nand nand_37 (DATA_OUT[13], nand_5_out, nand_38_out);
  nand nand_38 (nand_38_out, DATA_OUT[13], nand_6_out);
  nand nand_39 (DATA_OUT[12], nand_7_out, nand_40_out);
  nand nand_40 (nand_40_out, DATA_OUT[12], nand_8_out);
  nand nand_41 (DATA_OUT[11], nand_9_out, nand_42_out);
  nand nand_42 (nand_42_out, DATA_OUT[11], nand_10_out);
  nand nand_43 (DATA_OUT[10], nand_11_out, nand_44_out);
  nand nand_44 (nand_44_out, DATA_OUT[10], nand_12_out);
  nand nand_45 (DATA_OUT[9], nand_13_out, nand_46_out);
  nand nand_46 (nand_46_out, DATA_OUT[9], nand_14_out);
  nand nand_47 (DATA_OUT[8], nand_15_out, nand_48_out);
  nand nand_48 (nand_48_out, DATA_OUT[8], nand_16_out);
  nand nand_49 (DATA_OUT[7], nand_17_out, nand_50_out);
  nand nand_50 (nand_50_out, DATA_OUT[7], nand_18_out);
  nand nand_51 (DATA_OUT[6], nand_19_out, nand_52_out);
  nand nand_52 (nand_52_out, DATA_OUT[6], nand_20_out);
  nand nand_53 (DATA_OUT[5], nand_21_out, nand_54_out);
  nand nand_54 (nand_54_out, DATA_OUT[5], nand_22_out);
  nand nand_55 (DATA_OUT[4], nand_23_out, nand_56_out);
  nand nand_56 (nand_56_out, DATA_OUT[4], nand_24_out);
  nand nand_57 (DATA_OUT[3], nand_25_out, nand_58_out);
  nand nand_58 (nand_58_out, DATA_OUT[3], nand_26_out);
  nand nand_59 (DATA_OUT[2], nand_27_out, nand_60_out);
  nand nand_60 (nand_60_out, DATA_OUT[2], nand_28_out);
  nand nand_61 (DATA_OUT[1], nand_29_out, nand_62_out);
  nand nand_62 (nand_62_out, DATA_OUT[1], nand_30_out);
  nand nand_63 (DATA_OUT[0], nand_31_out, nand_64_out);
  nand nand_64 (nand_64_out, DATA_OUT[0], nand_32_out);
endmodule

module program_counter_16bit (
  input  CLOCK,
  input  FUNC_SELECT,
  input  LOAD,
  input  [15:0] DATA_IN,
  input  RESET,
  output [15:0] DATA_OUT
);

  wire and_3_out, and_4_out, and_5_out, and_6_out, and_7_out, and_8_out, and_9_out, and_10_out, and_11_out,
       and_12_out, and_13_out, and_14_out, and_15_out, and_16_out, and_17_out, and_18_out, and_19_out,
       and_20_out, and_21_out, and_22_out, and_23_out, and_24_out, and_25_out, and_26_out, and_27_out,
       and_28_out, and_29_out, and_30_out, and_31_out, and_32_out, and_33_out, and_34_out, and_35_out,
       and_36_out, and_37_out, and_38_out, and_39_out, and_40_out, and_41_out, and_42_out, and_43_out,
       and_44_out, and_45_out, and_46_out, and_47_out, and_48_out, and_49_out, and_50_out, and_51_out,
       and_52_out, and_53_out, and_54_out, and_55_out, and_56_out, and_57_out, and_58_out, and_59_out,
       and_60_out, and_61_out, and_62_out, and_63_out, and_64_out, and_65_out, and_66_out, and_67_out,
       and_69_out, and_70_out, and_71_out, and_72_out, and_73_out, and_74_out, and_75_out, and_76_out,
       and_77_out, and_78_out, and_79_out, and_80_out, and_81_out, and_82_out, and_83_out, nand_1_out,
       nand_2_out, nand_3_out, nand_4_out, nand_5_out, nand_6_out, nand_7_out, nand_8_out, nand_9_out,
       nand_10_out, nand_11_out, nand_12_out, nand_13_out, nand_14_out, nand_15_out, nand_16_out,
       nand_17_out, nand_18_out, nand_19_out, nand_20_out, nand_21_out, nand_22_out, nand_23_out,
       nand_24_out, nand_25_out, nand_26_out, nand_27_out, nand_28_out, nand_29_out, nand_30_out,
       nand_31_out, nand_32_out, nand_34_out, nand_36_out, nand_38_out, nand_40_out, nand_42_out,
       nand_44_out, nand_46_out, nand_48_out, nand_50_out, nand_52_out, nand_54_out, nand_56_out,
       nand_58_out, nand_60_out, nand_62_out, nand_64_out, nand_65_out, nand_66_out, nand_67_out,
       nand_68_out, nand_69_out, nand_70_out, nand_71_out, nand_72_out, nand_73_out, nand_74_out,
       nand_75_out, nand_76_out, nand_77_out, nand_78_out, nand_79_out, nand_80_out, nand_81_out,
       nand_82_out, nand_83_out, nand_84_out, nand_85_out, nand_86_out, nand_87_out, nand_88_out,
       nand_89_out, nand_90_out, nand_91_out, nand_92_out, nand_93_out, nand_94_out, nand_95_out,
       nand_96_out, nand_97_out, nand_98_out, nand_99_out, nand_100_out, nand_101_out, nand_102_out,
       nand_103_out, nand_104_out, nand_105_out, nand_106_out, nand_107_out, nand_108_out, nand_109_out,
       nand_110_out, nand_111_out, nand_112_out, nand_113_out, nand_114_out, nand_115_out, nand_116_out,
       nand_117_out, nand_118_out, nand_119_out, nand_120_out, nand_121_out, nand_122_out, nand_123_out,
       nand_124_out, nand_125_out, nand_126_out, nand_127_out, nand_128_out, not_2_out, not_3_out, not_4_out,
       not_5_out, not_6_out, not_7_out, not_8_out, not_9_out, not_10_out, not_11_out, not_12_out, not_13_out,
       not_14_out, not_15_out, not_16_out, not_17_out, not_18_out, not_19_out, not_20_out, not_21_out,
       not_22_out, not_23_out, not_24_out, not_25_out, not_26_out, not_27_out, not_28_out, not_29_out,
       not_30_out, not_31_out, not_32_out, not_33_out, not_34_out, not_35_out, not_36_out, not_37_out,
       not_38_out, not_39_out, not_40_out, not_41_out, not_42_out, not_43_out, not_44_out, not_45_out,
       not_46_out, not_47_out, not_48_out, not_49_out, not_50_out, not_51_out, not_52_out, not_53_out,
       not_54_out, not_55_out, not_56_out, not_57_out, not_58_out, not_59_out, not_60_out, not_61_out,
       not_62_out, not_63_out, not_64_out, not_65_out, not_66_out, not_67_out, not_68_out, not_69_out,
       not_70_out, not_71_out, not_72_out, not_73_out, not_74_out, not_75_out, not_76_out, not_77_out,
       not_78_out, not_79_out, not_80_out, not_81_out, not_82_out, or_2_out, or_3_out, or_4_out, or_5_out,
       or_6_out, or_7_out, or_8_out, or_9_out, or_10_out, or_11_out, or_12_out, or_13_out, or_14_out,
       or_15_out, or_16_out, or_17_out, or_18_out, or_19_out, or_20_out, or_21_out, or_22_out, or_23_out,
       or_24_out, or_25_out, or_26_out, or_27_out, or_28_out, or_29_out, or_30_out, or_31_out, or_32_out,
       or_33_out, or_34_out, xor_1_out, xor_2_out, xor_3_out, xor_4_out, xor_5_out, xor_6_out, xor_7_out,
       xor_8_out, xor_9_out, xor_10_out, xor_11_out, xor_12_out, xor_13_out, xor_14_out, xor_15_out,
       xor_16_out;
  wire [15:0] and_1_out, and_2_out, not_1_out, or_1_out;

  assign or_1_out = and_1_out | and_2_out;  // OR_Gate or_1, 16 bits wide
  assign and_1_out = {16{RESET}} & {16{1'b1}};  // AND_Gate and_1, 16 bits wide
  assign not_1_out = ~{16{RESET}};  // NOT_Gate not_1, 16 bits wide
  assign and_2_out = not_1_out & DATA_IN;  // AND_Gate and_2, 16 bits wide
  and and_3 (and_3_out, FUNC_SELECT, not_2_out);
  not not_2 (not_2_out, RESET);
  not not_3 (not_3_out, and_3_out);
  not not_4 (not_4_out, and_3_out);
  not not_5 (not_5_out, and_3_out);
  not not_6 (not_6_out, and_3_out);
  not not_7 (not_7_out, and_3_out);
  not not_8 (not_8_out, and_3_out);
  not not_9 (not_9_out, and_3_out);
  not not_10 (not_10_out, and_3_out);
  not not_11 (not_11_out, and_3_out);
  not not_12 (not_12_out, and_3_out);
  not not_13 (not_13_out, and_3_out);
  not not_14 (not_14_out, and_3_out);
  not not_15 (not_15_out, and_3_out);
  not not_16 (not_16_out, and_3_out);
  not not_17 (not_17_out, and_3_out);
  not not_18 (not_18_out, and_3_out);
  and and_4 (and_4_out, xor_1_out, and_3_out);
  or or_2 (or_2_out, and_4_out, and_5_out);
  and and_5 (and_5_out, or_1_out[15], not_3_out);
  and and_6 (and_6_out, xor_2_out, and_3_out);
  or or_3 (or_3_out, and_6_out, and_7_out);
  and and_7 (and_7_out, or_1_out[14], not_4_out);
  and and_8 (and_8_out, xor_3_out, and_3_out);
  or or_4 (or_4_out, and_8_out, and_9_out);
  and and_9 (and_9_out, or_1_out[13], not_5_out);
  and and_10 (and_10_out, xor_4_out, and_3_out);
  or or_5 (or_5_out, and_10_out, and_11_out);
  and and_11 (and_11_out, or_1_out[12], not_6_out);
  and and_12 (and_12_out, xor_5_out, and_3_out);
  or or_6 (or_6_out, and_12_out, and_13_out);
  and and_13 (and_13_out, or_1_out[11], not_7_out);
  and and_14 (and_14_out, xor_6_out, and_3_out);
  or or_7 (or_7_out, and_14_out, and_15_out);
  and and_15 (and_15_out, or_1_out[10], not_8_out);
  and and_16 (and_16_out, xor_7_out, and_3_out);
  or or_8 (or_8_out, and_16_out, and_17_out);
  and and_17 (and_17_out, or_1_out[9], not_9_out);
  and and_18 (and_18_out, xor_8_out, and_3_out);
  or or_9 (or_9_out, and_18_out, and_19_out);
  and and_19 (and_19_out, or_1_out[8], not_10_out);
  and and_20 (and_20_out, xor_9_out, and_3_out);
  or or_10 (or_10_out, and_20_out, and_21_out);
  and and_21 (and_21_out, or_1_out[7], not_11_out);
  and and_22 (and_22_out, xor_10_out, and_3_out);
  or or_11 (or_11_out, and_22_out, and_23_out);
  and and_23 (and_23_out, or_1_out[6], not_12_out);
  and and_24 (and_24_out, xor_11_out, and_3_out);
  or or_12 (or_12_out, and_24_out, and_25_out);
  and and_25 (and_25_out, or_1_out[5], not_13_out);
  and and_26 (and_26_out, xor_12_out, and_3_out);
  or or_13 (or_13_out, and_26_out, and_27_out);
  and and_27 (and_27_out, or_1_out[4], not_14_out);
  and and_28 (and_28_out, xor_13_out, and_3_out);
  or or_14 (or_14_out, and_28_out, and_29_out);
  and and_29 (and_29_out, or_1_out[3], not_15_out);
  and and_30 (and_30_out, xor_14_out, and_3_out);
  or or_15 (or_15_out, and_30_out, and_31_out);
  and and_31 (and_31_out, or_1_out[2], not_16_out);
  and and_32 (and_32_out, xor_15_out, and_3_out);
  or or_16 (or_16_out, and_32_out, and_33_out);
  and and_33 (and_33_out, or_1_out[1], not_17_out);
  and and_34 (and_34_out, xor_16_out, and_3_out);
  or or_17 (or_17_out, and_34_out, and_35_out);
  and and_35 (and_35_out, or_1_out[0], not_18_out);
  not not_19 (not_19_out, or_18_out);
  not not_20 (not_20_out, or_18_out);
  not not_21 (not_21_out, or_18_out);
  not not_22 (not_22_out, or_18_out);
  not not_23 (not_23_out, or_18_out);
  not not_24 (not_24_out, or_18_out);
  not not_25 (not_25_out, or_18_out);
  not not_26 (not_26_out, or_18_out);
  not not_27 (not_27_out, or_18_out);
  not not_28 (not_28_out, or_18_out);
  not not_29 (not_29_out, or_18_out);
  not not_30 (not_30_out, or_18_out);
  not not_31 (not_31_out, or_18_out);
  not not_32 (not_32_out, or_18_out);
  not not_33 (not_33_out, or_18_out);
  not not_34 (not_34_out, or_18_out);
  or or_18 (or_18_out, LOAD, RESET);
  and and_36 (and_36_out, or_2_out, or_18_out);
  and and_37 (and_37_out, nand_97_out, not_19_out);
  and and_38 (and_38_out, or_3_out, or_18_out);
  and and_39 (and_39_out, nand_99_out, not_20_out);
  and and_40 (and_40_out, or_4_out, or_18_out);
  and and_41 (and_41_out, nand_101_out, not_21_out);
  and and_42 (and_42_out, or_5_out, or_18_out);
  and and_43 (and_43_out, nand_103_out, not_22_out);
  and and_44 (and_44_out, or_6_out, or_18_out);
  and and_45 (and_45_out, nand_105_out, not_23_out);
  and and_46 (and_46_out, or_7_out, or_18_out);
  and and_47 (and_47_out, nand_107_out, not_24_out);
  and and_48 (and_48_out, or_8_out, or_18_out);
  and and_49 (and_49_out, nand_109_out, not_25_out);
  and and_50 (and_50_out, or_9_out, or_18_out);
  and and_51 (and_51_out, nand_111_out, not_26_out);
  and and_52 (and_52_out, or_10_out, or_18_out);
  and and_53 (and_53_out, nand_113_out, not_27_out);
  and and_54 (and_54_out, or_11_out, or_18_out);
  and and_55 (and_55_out, nand_115_out, not_28_out);
  and and_56 (and_56_out, or_12_out, or_18_out);
  and and_57 (and_57_out, nand_117_out, not_29_out);
  and and_58 (and_58_out, or_13_out, or_18_out);
  and and_59 (and_59_out, nand_119_out, not_30_out);
  and and_60 (and_60_out, or_14_out, or_18_out);
  and and_61 (and_61_out, nand_121_out, not_31_out);
  and and_62 (and_62_out, or_15_out, or_18_out);
  and and_63 (and_63_out, nand_123_out, not_32_out);
  and and_64 (and_64_out, or_16_out, or_18_out);
  and and_65 (and_65_out, nand_125_out, not_33_out);
  and and_66 (and_66_out, or_17_out, or_18_out);
  and and_67 (and_67_out, nand_127_out, not_34_out);
  or or_19 (or_19_out, and_36_out, and_37_out);
  or or_20 (or_20_out, and_38_out, and_39_out);
  or or_21 (or_21_out, and_40_out, and_41_out);
  or or_22 (or_22_out, and_42_out, and_43_out);
  or or_23 (or_23_out, and_44_out, and_45_out);
  or or_24 (or_24_out, and_46_out, and_47_out);
  or or_25 (or_25_out, and_48_out, and_49_out);
  or or_26 (or_26_out, and_50_out, and_51_out);
  or or_27 (or_27_out, and_52_out, and_53_out);
  or or_28 (or_28_out, and_54_out, and_55_out);
  or or_29 (or_29_out, and_56_out, and_57_out);
  or or_30 (or_30_out, and_58_out, and_59_out);
  or or_31 (or_31_out, and_60_out, and_61_out);
  or or_32 (or_32_out, and_62_out, and_63_out);
  or or_33 (or_33_out, and_64_out, and_65_out);
  or or_34 (or_34_out, and_66_out, and_67_out);
  nand nand_1 (nand_1_out, or_19_out, CLOCK);
  nand nand_2 (nand_2_out, CLOCK, not_35_out);
  not not_35 (not_35_out, or_19_out);
  nand nand_3 (nand_3_out, or_20_out, CLOCK);
  nand nand_4 (nand_4_out, CLOCK, not_36_out);
  not not_36 (not_36_out, or_20_out);
  nand nand_5 (nand_5_out, or_21_out, CLOCK);
  nand nand_6 (nand_6_out, CLOCK, not_37_out);
  not not_37 (not_37_out, or_21_out);
  nand nand_7 (nand_7_out, or_22_out, CLOCK);
  nand nand_8 (nand_8_out, CLOCK, not_38_out);
  not not_38 (not_38_out, or_22_out);
  nand nand_9 (nand_9_out, or_23_out, CLOCK);
  nand nand_10 (nand_10_out, CLOCK, not_39_out);
  not not_39 (not_39_out, or_23_out);
  nand nand_11 (nand_11_out, or_24_out, CLOCK);
  nand nand_12 (nand_12_out, CLOCK, not_40_out);
  not not_40 (not_40_out, or_24_out);
  nand nand_13 (nand_13_out, or_25_out, CLOCK);
  nand nand_14 (nand_14_out, CLOCK, not_41_out);
  not not_41 (not_41_out, or_25_out);
  nand nand_15 (nand_15_out, or_26_out, CLOCK);
  nand nand_16 (nand_16_out, CLOCK, not_42_out);
  not not_42 (not_42_out, or_26_out);
  nand nand_17 (nand_17_out, or_27_out, CLOCK);
  nand nand_18 (nand_18_out, CLOCK, not_43_out);
  not not_43 (not_43_out, or_27_out);
  nand nand_19 (nand_19_out, or_28_out, CLOCK);
  nand nand_20 (nand_20_out, CLOCK, not_44_out);
  not not_44 (not_44_out, or_28_out);
  nand nand_21 (nand_21_out, or_29_out, CLOCK);
  nand nand_22 (nand_22_out, CLOCK, not_45_out);
  not not_45 (not_45_out, or_29_out);
  nand nand_23 (nand_23_out, or_30_out, CLOCK);
  nand nand_24 (nand_24_out, CLOCK, not_46_out);
  not not_46 (not_46_out, or_30_out);
  nand nand_25 (nand_25_out, or_31_out, CLOCK);
  nand nand_26 (nand_26_out, CLOCK, not_47_out);
  not not_47 (not_47_out, or_31_out);
  nand nand_27 (nand_27_out, or_32_out, CLOCK);
  nand nand_28 (nand_28_out, CLOCK, not_48_out);
  not not_48 (not_48_out, or_32_out);
  nand nand_29 (nand_29_out, or_33_out, CLOCK);
  nand nand_30 (nand_30_out, CLOCK, not_49_out);
  not not_49 (not_49_out, or_33_out);
  nand nand_31 (nand_31_out, or_34_out, CLOCK);
  nand nand_32 (nand_32_out, CLOCK, not_50_out);
  not not_50 (not_50_out, or_34_out);
  nand nand_33 (DATA_OUT[15], nand_1_out, nand_34_out);
  nand nand_34 (nand_34_out, DATA_OUT[15], nand_2_out);
  not not_51 (not_51_out, CLOCK);
  nand nand_35 (DATA_OUT[14], nand_3_out, nand_36_out);
  nand nand_36 (nand_36_out, DATA_OUT[14], nand_4_out);
  not not_52 (not_52_out, CLOCK);
  nand nand_37 (DATA_OUT[13], nand_5_out, nand_38_out);
  nand nand_38 (nand_38_out, DATA_OUT[13], nand_6_out);
  not not_53 (not_53_out, CLOCK);
  nand nand_39 (DATA_OUT[12], nand_7_out, nand_40_out);
  nand nand_40 (nand_40_out, DATA_OUT[12], nand_8_out);
  not not_54 (not_54_out, CLOCK);
  nand nand_41 (DATA_OUT[11], nand_9_out, nand_42_out);
  nand nand_42 (nand_42_out, DATA_OUT[11], nand_10_out);
  not not_55 (not_55_out, CLOCK);
  nand nand_43 (DATA_OUT[10], nand_11_out, nand_44_out);
  nand nand_44 (nand_44_out, DATA_OUT[10], nand_12_out);
  not not_56 (not_56_out, CLOCK);
  nand nand_45 (DATA_OUT[9], nand_13_out, nand_46_out);
  nand nand_46 (nand_46_out, DATA_OUT[9], nand_14_out);
  not not_57 (not_57_out, CLOCK);
  nand nand_47 (DATA_OUT[8], nand_15_out, nand_48_out);
  nand nand_48 (nand_48_out, DATA_OUT[8], nand_16_out);
  not not_58 (not_58_out, CLOCK);
  nand nand_49 (DATA_OUT[7], nand_17_out, nand_50_out);
  nand nand_50 (nand_50_out, DATA_OUT[7], nand_18_out);
  not not_59 (not_59_out, CLOCK);
  nand nand_51 (DATA_OUT[6], nand_19_out, nand_52_out);
  nand nand_52 (nand_52_out, DATA_OUT[6], nand_20_out);
  not not_60 (not_60_out, CLOCK);
  nand nand_53 (DATA_OUT[5], nand_21_out, nand_54_out);
  nand nand_54 (nand_54_out, DATA_OUT[5], nand_22_out);
  not not_61 (not_61_out, CLOCK);
  nand nand_55 (DATA_OUT[4], nand_23_out, nand_56_out);
  nand nand_56 (nand_56_out, DATA_OUT[4], nand_24_out);
  not not_62 (not_62_out, CLOCK);
  nand nand_57 (DATA_OUT[3], nand_25_out, nand_58_out);
  nand nand_58 (nand_58_out, DATA_OUT[3], nand_26_out);
  not not_63 (not_63_out, CLOCK);
  nand nand_59 (DATA_OUT[2], nand_27_out, nand_60_out);
  nand nand_60 (nand_60_out, DATA_OUT[2], nand_28_out);
  not not_64 (not_64_out, CLOCK);
  nand nand_61 (DATA_OUT[1], nand_29_out, nand_62_out);
  nand nand_62 (nand_62_out, DATA_OUT[1], nand_30_out);
  not not_65 (not_65_out, CLOCK);
  nand nand_63 (DATA_OUT[0], nand_31_out, nand_64_out);
  nand nand_64 (nand_64_out, DATA_OUT[0], nand_32_out);
  not not_66 (not_66_out, CLOCK);
  not not_67 (not_67_out, DATA_OUT[15]);
  not not_68 (not_68_out, DATA_OUT[14]);
  not not_69 (not_69_out, DATA_OUT[13]);
  not not_70 (not_70_out, DATA_OUT[12]);
  not not_71 (not_71_out, DATA_OUT[11]);
  not not_72 (not_72_out, DATA_OUT[10]);
  not not_73 (not_73_out, DATA_OUT[9]);
  not not_74 (not_74_out, DATA_OUT[8]);
  not not_75 (not_75_out, DATA_OUT[7]);
  not not_76 (not_76_out, DATA_OUT[6]);
  not not_77 (not_77_out, DATA_OUT[5]);
  not not_78 (not_78_out, DATA_OUT[4]);
  not not_79 (not_79_out, DATA_OUT[3]);
  not not_80 (not_80_out, DATA_OUT[2]);
  not not_81 (not_81_out, DATA_OUT[1]);
  not not_82 (not_82_out, DATA_OUT[0]);
  nand nand_65 (nand_65_out, DATA_OUT[15], not_51_out);
  nand nand_66 (nand_66_out, not_51_out, not_67_out);
  nand nand_67 (nand_67_out, DATA_OUT[14], not_52_out);
  nand nand_68 (nand_68_out, not_52_out, not_68_out);
  nand nand_69 (nand_69_out, DATA_OUT[13], not_53_out);
  nand nand_70 (nand_70_out, not_53_out, not_69_out);
  nand nand_71 (nand_71_out, DATA_OUT[12], not_54_out);
  nand nand_72 (nand_72_out, not_54_out, not_70_out);
  nand nand_73 (nand_73_out, DATA_OUT[11], not_55_out);
  nand nand_74 (nand_74_out, not_55_out, not_71_out);
  nand nand_75 (nand_75_out, DATA_OUT[10], not_56_out);
  nand nand_76 (nand_76_out, not_56_out, not_72_out);
  nand nand_77 (nand_77_out, DATA_OUT[9], not_57_out);
  nand nand_78 (nand_78_out, not_57_out, not_73_out);
  nand nand_79 (nand_79_out, DATA_OUT[8], not_58_out);
  nand nand_80 (nand_80_out, not_58_out, not_74_out);
  nand nand_81 (nand_81_out, DATA_OUT[7], not_59_out);
  nand nand_82 (nand_82_out, not_59_out, not_75_out);
  nand nand_83 (nand_83_out, DATA_OUT[6], not_60_out);
  nand nand_84 (nand_84_out, not_60_out, not_76_out);
  nand nand_85 (nand_85_out, DATA_OUT[5], not_61_out);
  nand nand_86 (nand_86_out, not_61_out, not_77_out);
  nand nand_87 (nand_87_out, DATA_OUT[4], not_62_out);
  nand nand_88 (nand_88_out, not_62_out, not_78_out);
  nand nand_89 (nand_89_out, DATA_OUT[3], not_63_out);
  nand nand_90 (nand_90_out, not_63_out, not_79_out);
  nand nand_91 (nand_91_out, DATA_OUT[2], not_64_out);
  nand nand_92 (nand_92_out, not_64_out, not_80_out);
  nand nand_93 (nand_93_out, DATA_OUT[1], not_65_out);
  nand nand_94 (nand_94_out, not_65_out, not_81_out);
  nand nand_95 (nand_95_out, DATA_OUT[0], not_66_out);
  nand nand_96 (nand_96_out, not_66_out, not_82_out);
  nand nand_97 (nand_97_out, nand_65_out, nand_98_out);
  nand nand_98 (nand_98_out, nand_97_out, nand_66_out);
  nand nand_99 (nand_99_out, nand_67_out, nand_100_out);
  nand nand_100 (nand_100_out, nand_99_out, nand_68_out);
  nand nand_101 (nand_101_out, nand_69_out, nand_102_out);
  nand nand_102 (nand_102_out, nand_101_out, nand_70_out);
  nand nand_103 (nand_103_out, nand_71_out, nand_104_out);
  nand nand_104 (nand_104_out, nand_103_out, nand_72_out);
  nand nand_105 (nand_105_out, nand_73_out, nand_106_out);
  nand nand_106 (nand_106_out, nand_105_out, nand_74_out);
  nand nand_107 (nand_107_out, nand_75_out, nand_108_out);
  nand nand_108 (nand_108_out, nand_107_out, nand_76_out);
  nand nand_109 (nand_109_out, nand_77_out, nand_110_out);
  nand nand_110 (nand_110_out, nand_109_out, nand_78_out);
  nand nand_111 (nand_111_out, nand_79_out, nand_112_out);
  nand nand_112 (nand_112_out, nand_111_out, nand_80_out);
  nand nand_113 (nand_113_out, nand_81_out, nand_114_out);
  nand nand_114 (nand_114_out, nand_113_out, nand_82_out);
  nand nand_115 (nand_115_out, nand_83_out, nand_116_out);
  nand nand_116 (nand_116_out, nand_115_out, nand_84_out);
  nand nand_117 (nand_117_out, nand_85_out, nand_118_out);
  nand nand_118 (nand_118_out, nand_117_out, nand_86_out);
  nand nand_119 (nand_119_out, nand_87_out, nand_120_out);
  nand nand_120 (nand_120_out, nand_119_out, nand_88_out);
  nand nand_121 (nand_121_out, nand_89_out, nand_122_out);
  nand nand_122 (nand_122_out, nand_121_out, nand_90_out);
  nand nand_123 (nand_123_out, nand_91_out, nand_124_out);
  nand nand_124 (nand_124_out, nand_123_out, nand_92_out);
  nand nand_125 (nand_125_out, nand_93_out, nand_126_out);
  nand nand_126 (nand_126_out, nand_125_out, nand_94_out);
  nand nand_127 (nand_127_out, nand_95_out, nand_128_out);
  nand nand_128 (nand_128_out, nand_127_out, nand_96_out);
  xor xor_1 (xor_1_out, nand_97_out, and_69_out);
  // AND_Gate and_68 has open pins: in0=nand_97_out, in1=and_69_out, out=open
  xor xor_2 (xor_2_out, nand_99_out, and_70_out);
  and and_69 (and_69_out, nand_99_out, and_70_out);
  xor xor_3 (xor_3_out, nand_101_out, and_71_out);
  and and_70 (and_70_out, nand_101_out, and_71_out);
  xor xor_4 (xor_4_out, nand_103_out, and_72_out);
  and and_71 (and_71_out, nand_103_out, and_72_out);
  xor xor_5 (xor_5_out, nand_105_out, and_73_out);
  and and_72 (and_72_out, nand_105_out, and_73_out);
  xor xor_6 (xor_6_out, nand_107_out, and_74_out);
  and and_73 (and_73_out, nand_107_out, and_74_out);
  xor xor_7 (xor_7_out, nand_109_out, and_75_out);
  and and_74 (and_74_out, nand_109_out, and_75_out);
  xor xor_8 (xor_8_out, nand_111_out, and_76_out);
  and and_75 (and_75_out, nand_111_out, and_76_out);
  xor xor_9 (xor_9_out, nand_113_out, and_77_out);
  and and_76 (and_76_out, nand_113_out, and_77_out);
  xor xor_10 (xor_10_out, nand_115_out, and_78_out);
  and and_77 (and_77_out, nand_115_out, and_78_out);
  xor xor_11 (xor_11_out, nand_117_out, and_79_out);
  and and_78 (and_78_out, nand_117_out, and_79_out);
  xor xor_12 (xor_12_out, nand_119_out, and_80_out);
  and and_79 (and_79_out, nand_119_out, and_80_out);
  xor xor_13 (xor_13_out, nand_121_out, and_81_out);
  and and_80 (and_80_out, nand_121_out, and_81_out);
  xor xor_14 (xor_14_out, nand_123_out, and_82_out);
  and and_81 (and_81_out, nand_123_out, and_82_out);
  xor xor_15 (xor_15_out, nand_125_out, and_83_out);
  and and_82 (and_82_out, nand_125_out, and_83_out);
  xor xor_16 (xor_16_out, nand_127_out, 1'b1);
  and and_83 (and_83_out, nand_127_out, 1'b1);
endmodule

module MAR_5bit (
  input  CLOCK,
  input  LOAD,
  input  [4:0] DATA_IN,
  input  RESET,
  output [4:0] out_5
);

  wire and_3_out, and_4_out, and_5_out, and_6_out, and_7_out, and_8_out, and_9_out, and_10_out, and_11_out,
       and_12_out, nand_1_out, nand_2_out, nand_3_out, nand_4_out, nand_5_out, nand_6_out, nand_7_out,
       nand_8_out, nand_9_out, nand_10_out, nand_12_out, nand_14_out, nand_16_out, nand_18_out, nand_20_out,
       not_2_out, not_3_out, not_4_out, not_5_out, not_6_out, not_7_out, not_8_out, not_9_out, not_10_out,
       not_11_out, or_1_out, or_3_out, or_4_out, or_5_out, or_6_out, or_7_out;
  wire [4:0] and_1_out, and_2_out, not_1_out, or_2_out;

  or or_1 (or_1_out, LOAD, RESET);
  assign or_2_out = and_1_out | and_2_out;  // OR_Gate or_2, 5 bits wide
  assign and_1_out = not_1_out & DATA_IN;  // AND_Gate and_1, 5 bits wide
  assign not_1_out = ~{5{RESET}};  // NOT_Gate not_1, 5 bits wide
  not not_2 (not_2_out, or_1_out);
  not not_3 (not_3_out, or_1_out);
  not not_4 (not_4_out, or_1_out);
  not not_5 (not_5_out, or_1_out);
  not not_6 (not_6_out, or_1_out);
  assign and_2_out = {5{1'b0}} & {5{RESET}};  // AND_Gate and_2, 5 bits wide
  and and_3 (and_3_out, or_2_out[4], or_1_out);
  and and_4 (and_4_out, out_5[4], not_2_out);
  and and_5 (and_5_out, or_2_out[3], or_1_out);
  and and_6 (and_6_out, out_5[3], not_3_out);
  and and_7 (and_7_out, or_2_out[2], or_1_out);
  and and_8 (and_8_out, out_5[2], not_4_out);
  and and_9 (and_9_out, or_2_out[1], or_1_out);
  and and_10 (and_10_out, out_5[1], not_5_out);
  and and_11 (and_11_out, or_2_out[0], or_1_out);
  and and_12 (and_12_out, out_5[0], not_6_out);
  or or_3 (or_3_out, and_3_out, and_4_out);
  not not_7 (not_7_out, or_3_out);
  or or_4 (or_4_out, and_5_out, and_6_out);
  not not_8 (not_8_out, or_4_out);
  or or_5 (or_5_out, and_7_out, and_8_out);
  not not_9 (not_9_out, or_5_out);
  or or_6 (or_6_out, and_9_out, and_10_out);
  not not_10 (not_10_out, or_6_out);
  or or_7 (or_7_out, and_11_out, and_12_out);
  not not_11 (not_11_out, or_7_out);
  nand nand_1 (nand_1_out, or_3_out, CLOCK);
  nand nand_2 (nand_2_out, CLOCK, not_7_out);
  nand nand_3 (nand_3_out, or_4_out, CLOCK);
  nand nand_4 (nand_4_out, CLOCK, not_8_out);
  nand nand_5 (nand_5_out, or_5_out, CLOCK);
  nand nand_6 (nand_6_out, CLOCK, not_9_out);
  nand nand_7 (nand_7_out, or_6_out, CLOCK);
  nand nand_8 (nand_8_out, CLOCK, not_10_out);
  nand nand_9 (nand_9_out, or_7_out, CLOCK);
  nand nand_10 (nand_10_out, CLOCK, not_11_out);
  nand nand_11 (out_5[4], nand_1_out, nand_12_out);
  nand nand_12 (nand_12_out, out_5[4], nand_2_out);
  nand nand_13 (out_5[3], nand_3_out, nand_14_out);
  nand nand_14 (nand_14_out, out_5[3], nand_4_out);
  nand nand_15 (out_5[2], nand_5_out, nand_16_out);
  nand nand_16 (nand_16_out, out_5[2], nand_6_out);
  nand nand_17 (out_5[1], nand_7_out, nand_18_out);
  nand nand_18 (nand_18_out, out_5[1], nand_8_out);
  nand nand_19 (out_5[0], nand_9_out, nand_20_out);
  nand nand_20 (nand_20_out, out_5[0], nand_10_out);
endmodule
module register_file_8byte (
  input  CLOCK,
  input  [15:0] DATA_IN,
  input  LOAD,
  input  LOAD_SELECT_1,
  input  LOAD_SELECT_0,
  input  RESET,
  output [15:0] OUT_A,
  output [15:0] OUT_B,
  output [15:0] OUT_C,
  output [15:0] OUT_D
);

  wire and_3_out, and_4_out, and_5_out, and_6_out, and_7_out, and_8_out, and_9_out, and_10_out, and_11_out,
       and_12_out, and_13_out, and_14_out, and_15_out, and_16_out, and_17_out, and_18_out, and_19_out,
       and_20_out, and_21_out, and_22_out, and_23_out, and_24_out, and_25_out, and_26_out, and_27_out,
       and_28_out, and_29_out, and_30_out, and_31_out, and_32_out, and_33_out, and_34_out, and_35_out,
       and_36_out, and_37_out, and_38_out, and_39_out, and_40_out, and_41_out, and_42_out, and_43_out,
       and_44_out, and_45_out, and_46_out, and_47_out, and_48_out, and_49_out, and_50_out, and_51_out,
       and_52_out, and_53_out, and_54_out, and_55_out, and_56_out, and_57_out, and_58_out, and_59_out,
       and_60_out, and_61_out, and_62_out, and_63_out, and_64_out, and_65_out, and_66_out, and_67_out,
       and_68_out, and_69_out, and_70_out, and_71_out, and_72_out, and_73_out, and_74_out, and_75_out,
       and_76_out, and_77_out, and_78_out, and_79_out, and_80_out, and_81_out, and_82_out, and_83_out,
       and_84_out, and_85_out, and_86_out, and_87_out, and_88_out, and_89_out, and_90_out, and_91_out,
       and_92_out, and_93_out, and_94_out, and_95_out, and_96_out, and_97_out, and_98_out, and_99_out,
       and_100_out, and_101_out, and_102_out, and_103_out, and_104_out, and_105_out, and_106_out,
       and_107_out, and_108_out, and_109_out, and_110_out, and_111_out, and_112_out, and_113_out,
       and_114_out, and_115_out, and_116_out, and_117_out, and_118_out, and_119_out, and_120_out,
       and_121_out, and_122_out, and_123_out, and_124_out, and_125_out, and_126_out, and_127_out,
       and_128_out, and_129_out, and_130_out, and_131_out, and_132_out, and_133_out, and_134_out, nand_1_out,
       nand_2_out, nand_3_out, nand_4_out, nand_5_out, nand_6_out, nand_7_out, nand_8_out, nand_9_out,
       nand_10_out, nand_11_out, nand_12_out, nand_13_out, nand_14_out, nand_15_out, nand_16_out,
       nand_17_out, nand_18_out, nand_19_out, nand_20_out, nand_21_out, nand_22_out, nand_23_out,
       nand_24_out, nand_25_out, nand_26_out, nand_27_out, nand_28_out, nand_29_out, nand_30_out,
       nand_31_out, nand_32_out, nand_33_out, nand_34_out, nand_35_out, nand_36_out, nand_37_out,
       nand_38_out, nand_39_out, nand_40_out, nand_41_out, nand_42_out, nand_43_out, nand_44_out,
       nand_45_out, nand_46_out, nand_47_out, nand_48_out, nand_49_out, nand_50_out, nand_51_out,
       nand_52_out, nand_53_out, nand_54_out, nand_55_out, nand_56_out, nand_57_out, nand_58_out,
       nand_59_out, nand_60_out, nand_61_out, nand_62_out, nand_63_out, nand_64_out, nand_65_out,
       nand_66_out, nand_67_out, nand_68_out, nand_69_out, nand_70_out, nand_71_out, nand_72_out,
       nand_73_out, nand_74_out, nand_75_out, nand_76_out, nand_77_out, nand_78_out, nand_79_out,
       nand_80_out, nand_81_out, nand_82_out, nand_83_out, nand_84_out, nand_85_out, nand_86_out,
       nand_87_out, nand_88_out, nand_89_out, nand_90_out, nand_91_out, nand_92_out, nand_93_out,
       nand_94_out, nand_95_out, nand_96_out, nand_98_out, nand_100_out, nand_102_out, nand_104_out,
       nand_106_out, nand_108_out, nand_110_out, nand_112_out, nand_114_out, nand_116_out, nand_118_out,
       nand_120_out, nand_122_out, nand_124_out, nand_126_out, nand_128_out, nand_129_out, nand_130_out,
       nand_131_out, nand_132_out, nand_133_out, nand_134_out, nand_135_out, nand_136_out, nand_137_out,
       nand_138_out, nand_139_out, nand_140_out, nand_141_out, nand_142_out, nand_143_out, nand_144_out,
       nand_145_out, nand_146_out, nand_147_out, nand_148_out, nand_149_out, nand_150_out, nand_151_out,
       nand_152_out, nand_153_out, nand_154_out, nand_155_out, nand_156_out, nand_157_out, nand_158_out,
       nand_159_out, nand_160_out, nand_161_out, nand_162_out, nand_163_out, nand_164_out, nand_165_out,
       nand_166_out, nand_167_out, nand_168_out, nand_169_out, nand_170_out, nand_171_out, nand_172_out,
       nand_173_out, nand_174_out, nand_175_out, nand_176_out, nand_177_out, nand_178_out, nand_179_out,
       nand_180_out, nand_181_out, nand_182_out, nand_183_out, nand_184_out, nand_185_out, nand_186_out,
       nand_187_out, nand_188_out, nand_189_out, nand_190_out, nand_191_out, nand_192_out, nand_193_out,
       nand_194_out, nand_195_out, nand_196_out, nand_197_out, nand_198_out, nand_199_out, nand_200_out,
       nand_201_out, nand_202_out, nand_203_out, nand_204_out, nand_205_out, nand_206_out, nand_207_out,
       nand_208_out, nand_209_out, nand_210_out, nand_211_out, nand_212_out, nand_213_out, nand_214_out,
       nand_215_out, nand_216_out, nand_217_out, nand_218_out, nand_219_out, nand_220_out, nand_221_out,
       nand_222_out, nand_223_out, nand_224_out, nand_226_out, nand_228_out, nand_230_out, nand_232_out,
       nand_234_out, nand_236_out, nand_238_out, nand_240_out, nand_242_out, nand_244_out, nand_246_out,
       nand_248_out, nand_250_out, nand_252_out, nand_254_out, nand_256_out, nand_257_out, nand_258_out,
       nand_259_out, nand_260_out, nand_261_out, nand_262_out, nand_263_out, nand_264_out, nand_265_out,
       nand_266_out, nand_267_out, nand_268_out, nand_269_out, nand_270_out, nand_271_out, nand_272_out,
       nand_273_out, nand_274_out, nand_275_out, nand_276_out, nand_277_out, nand_278_out, nand_279_out,
       nand_280_out, nand_281_out, nand_282_out, nand_283_out, nand_284_out, nand_285_out, nand_286_out,
       nand_287_out, nand_288_out, nand_289_out, nand_290_out, nand_291_out, nand_292_out, nand_293_out,
       nand_294_out, nand_295_out, nand_296_out, nand_297_out, nand_298_out, nand_299_out, nand_300_out,
       nand_301_out, nand_302_out, nand_303_out, nand_304_out, nand_305_out, nand_306_out, nand_307_out,
       nand_308_out, nand_309_out, nand_310_out, nand_311_out, nand_312_out, nand_313_out, nand_314_out,
       nand_315_out, nand_316_out, nand_317_out, nand_318_out, nand_319_out, nand_320_out, nand_321_out,
       nand_322_out, nand_323_out, nand_324_out, nand_325_out, nand_326_out, nand_327_out, nand_328_out,
       nand_329_out, nand_330_out, nand_331_out, nand_332_out, nand_333_out, nand_334_out, nand_335_out,
       nand_336_out, nand_337_out, nand_338_out, nand_339_out, nand_340_out, nand_341_out, nand_342_out,
       nand_343_out, nand_344_out, nand_345_out, nand_346_out, nand_347_out, nand_348_out, nand_349_out,
       nand_350_out, nand_351_out, nand_352_out, nand_354_out, nand_356_out, nand_358_out, nand_360_out,
       nand_362_out, nand_364_out, nand_366_out, nand_368_out, nand_370_out, nand_372_out, nand_374_out,
       nand_376_out, nand_378_out, nand_380_out, nand_382_out, nand_384_out, nand_385_out, nand_386_out,
       nand_387_out, nand_388_out, nand_389_out, nand_390_out, nand_391_out, nand_392_out, nand_393_out,
       nand_394_out, nand_395_out, nand_396_out, nand_397_out, nand_398_out, nand_399_out, nand_400_out,
       nand_401_out, nand_402_out, nand_403_out, nand_404_out, nand_405_out, nand_406_out, nand_407_out,
       nand_408_out, nand_409_out, nand_410_out, nand_411_out, nand_412_out, nand_413_out, nand_414_out,
       nand_415_out, nand_416_out, nand_417_out, nand_418_out, nand_419_out, nand_420_out, nand_421_out,
       nand_422_out, nand_423_out, nand_424_out, nand_425_out, nand_426_out, nand_427_out, nand_428_out,
       nand_429_out, nand_430_out, nand_431_out, nand_432_out, nand_433_out, nand_434_out, nand_435_out,
       nand_436_out, nand_437_out, nand_438_out, nand_439_out, nand_440_out, nand_441_out, nand_442_out,
       nand_443_out, nand_444_out, nand_445_out, nand_446_out, nand_447_out, nand_448_out, nand_449_out,
       nand_450_out, nand_451_out, nand_452_out, nand_453_out, nand_454_out, nand_455_out, nand_456_out,
       nand_457_out, nand_458_out, nand_459_out, nand_460_out, nand_461_out, nand_462_out, nand_463_out,
       nand_464_out, nand_465_out, nand_466_out, nand_467_out, nand_468_out, nand_469_out, nand_470_out,
       nand_471_out, nand_472_out, nand_473_out, nand_474_out, nand_475_out, nand_476_out, nand_477_out,
       nand_478_out, nand_479_out, nand_480_out, nand_482_out, nand_484_out, nand_486_out, nand_488_out,
       nand_490_out, nand_492_out, nand_494_out, nand_496_out, nand_498_out, nand_500_out, nand_502_out,
       nand_504_out, nand_506_out, nand_508_out, nand_510_out, nand_512_out, not_2_out, not_3_out, not_4_out,
       not_5_out, not_6_out, not_7_out, not_8_out, not_9_out, not_10_out, not_11_out, not_12_out, not_13_out,
       not_14_out, not_15_out, not_16_out, not_17_out, not_18_out, not_19_out, not_20_out, not_21_out,
       not_22_out, not_23_out, not_24_out, not_25_out, not_26_out, not_27_out, not_28_out, not_29_out,
       not_30_out, not_31_out, not_32_out, not_33_out, not_34_out, not_35_out, not_36_out, not_37_out,
       not_38_out, not_39_out, not_40_out, not_41_out, not_42_out, not_43_out, not_44_out, not_45_out,
       not_46_out, not_47_out, not_48_out, not_49_out, not_50_out, not_51_out, not_52_out, not_53_out,
       not_54_out, not_55_out, not_56_out, not_57_out, not_58_out, not_59_out, not_60_out, not_61_out,
       not_62_out, not_63_out, not_64_out, not_65_out, not_66_out, not_67_out, not_68_out, not_69_out,
       not_70_out, not_71_out, not_72_out, not_73_out, not_74_out, not_75_out, not_76_out, not_77_out,
       not_78_out, not_79_out, not_80_out, not_81_out, not_82_out, not_83_out, not_84_out, not_85_out,
       not_86_out, not_87_out, not_88_out, not_89_out, not_90_out, not_91_out, not_92_out, not_93_out,
       not_94_out, not_95_out, not_96_out, not_97_out, not_98_out, not_99_out, not_100_out, not_101_out,
       not_102_out, not_103_out, not_104_out, not_105_out, not_106_out, not_107_out, not_108_out,
       not_109_out, not_110_out, not_111_out, not_112_out, not_113_out, not_114_out, not_115_out,
       not_116_out, not_117_out, not_118_out, not_119_out, not_120_out, not_121_out, not_122_out,
       not_123_out, not_124_out, not_125_out, not_126_out, not_127_out, not_128_out, not_129_out,
       not_130_out, not_131_out, not_132_out, not_133_out, not_134_out, not_135_out, not_136_out,
       not_137_out, not_138_out, not_139_out, not_140_out, not_141_out, not_142_out, not_143_out,
       not_144_out, not_145_out, not_146_out, not_147_out, not_148_out, not_149_out, not_150_out,
       not_151_out, not_152_out, not_153_out, not_154_out, not_155_out, not_156_out, not_157_out,
       not_158_out, not_159_out, not_160_out, not_161_out, not_162_out, not_163_out, not_164_out,
       not_165_out, not_166_out, not_167_out, not_168_out, not_169_out, not_170_out, not_171_out,
       not_172_out, not_173_out, not_174_out, not_175_out, not_176_out, not_177_out, not_178_out,
       not_179_out, not_180_out, not_181_out, not_182_out, not_183_out, not_184_out, not_185_out,
       not_186_out, not_187_out, not_188_out, not_189_out, not_190_out, not_191_out, not_192_out,
       not_193_out, not_194_out, not_195_out, not_196_out, not_197_out, not_198_out, not_199_out,
       not_200_out, not_201_out, not_202_out, not_203_out, not_204_out, not_205_out, not_206_out,
       not_207_out, not_208_out, not_209_out, not_210_out, not_211_out, not_212_out, not_213_out,
       not_214_out, not_215_out, not_216_out, not_217_out, not_218_out, not_219_out, not_220_out,
       not_221_out, not_222_out, not_223_out, not_224_out, not_225_out, not_226_out, not_227_out,
       not_228_out, not_229_out, not_230_out, not_231_out, not_232_out, not_233_out, not_234_out,
       not_235_out, not_236_out, not_237_out, not_238_out, not_239_out, not_240_out, not_241_out,
       not_242_out, not_243_out, not_244_out, not_245_out, not_246_out, not_247_out, not_248_out,
       not_249_out, not_250_out, not_251_out, not_252_out, not_253_out, not_254_out, not_255_out,
       not_256_out, not_257_out, not_258_out, not_259_out, or_2_out, or_3_out, or_4_out, or_5_out, or_6_out,
       or_7_out, or_8_out, or_9_out, or_10_out, or_11_out, or_12_out, or_13_out, or_14_out, or_15_out,
       or_16_out, or_17_out, or_18_out, or_19_out, or_20_out, or_21_out, or_22_out, or_23_out, or_24_out,
       or_25_out, or_26_out, or_27_out, or_28_out, or_29_out, or_30_out, or_31_out, or_32_out, or_33_out,
       or_34_out, or_35_out, or_36_out, or_37_out, or_38_out, or_39_out, or_40_out, or_41_out, or_42_out,
       or_43_out, or_44_out, or_45_out, or_46_out, or_47_out, or_48_out, or_49_out, or_50_out, or_51_out,
       or_52_out, or_53_out, or_54_out, or_55_out, or_56_out, or_57_out, or_58_out, or_59_out, or_60_out,
       or_61_out, or_62_out, or_63_out, or_64_out, or_65_out, or_66_out, or_67_out, or_68_out, or_69_out,
       or_70_out;
  wire [15:0] and_1_out, and_2_out, not_1_out, or_1_out;

  assign or_1_out = and_1_out | and_2_out;  // OR_Gate or_1, 16 bits wide
  assign and_1_out = {16{RESET}} & {16{1'b0}};  // AND_Gate and_1, 16 bits wide
  assign not_1_out = ~{16{RESET}};  // NOT_Gate not_1, 16 bits wide
  assign and_2_out = not_1_out & DATA_IN;  // AND_Gate and_2, 16 bits wide
  or or_2 (or_2_out, RESET, LOAD);
  not not_2 (not_2_out, or_19_out);
  not not_3 (not_3_out, or_19_out);
  not not_4 (not_4_out, or_19_out);
  not not_5 (not_5_out, or_19_out);
  not not_6 (not_6_out, or_19_out);
  not not_7 (not_7_out, or_19_out);
  not not_8 (not_8_out, or_19_out);
  not not_9 (not_9_out, or_19_out);
  not not_10 (not_10_out, or_19_out);
  not not_11 (not_11_out, or_19_out);
  not not_12 (not_12_out, or_19_out);
  not not_13 (not_13_out, or_19_out);
  not not_14 (not_14_out, or_19_out);
  not not_15 (not_15_out, or_19_out);
  not not_16 (not_16_out, or_19_out);
  not not_17 (not_17_out, or_19_out);
  not not_18 (not_18_out, LOAD_SELECT_1);
  not not_19 (not_19_out, LOAD_SELECT_0);
  and and_3 (and_3_out, or_1_out[15], or_19_out);
  and and_4 (and_4_out, OUT_A[15], not_2_out);
  and and_5 (and_5_out, or_1_out[14], or_19_out);
  and and_6 (and_6_out, OUT_A[14], not_3_out);
  and and_7 (and_7_out, or_1_out[13], or_19_out);
  and and_8 (and_8_out, OUT_A[13], not_4_out);
  and and_9 (and_9_out, or_1_out[12], or_19_out);
  and and_10 (and_10_out, OUT_A[12], not_5_out);
  and and_11 (and_11_out, or_1_out[11], or_19_out);
  and and_12 (and_12_out, OUT_A[11], not_6_out);
  and and_13 (and_13_out, or_1_out[10], or_19_out);
  and and_14 (and_14_out, OUT_A[10], not_7_out);
  and and_15 (and_15_out, or_1_out[9], or_19_out);
  and and_16 (and_16_out, OUT_A[9], not_8_out);
  and and_17 (and_17_out, or_1_out[8], or_19_out);
  and and_18 (and_18_out, OUT_A[8], not_9_out);
  and and_19 (and_19_out, or_1_out[7], or_19_out);
  and and_20 (and_20_out, OUT_A[7], not_10_out);
  and and_21 (and_21_out, or_1_out[6], or_19_out);
  and and_22 (and_22_out, OUT_A[6], not_11_out);
  and and_23 (and_23_out, or_1_out[5], or_19_out);
  and and_24 (and_24_out, OUT_A[5], not_12_out);
  and and_25 (and_25_out, or_1_out[4], or_19_out);
  and and_26 (and_26_out, OUT_A[4], not_13_out);
  and and_27 (and_27_out, or_1_out[3], or_19_out);
  and and_28 (and_28_out, OUT_A[3], not_14_out);
  and and_29 (and_29_out, or_1_out[2], or_19_out);
  and and_30 (and_30_out, OUT_A[2], not_15_out);
  and and_31 (and_31_out, or_1_out[1], or_19_out);
  and and_32 (and_32_out, OUT_A[1], not_16_out);
  and and_33 (and_33_out, or_1_out[0], or_19_out);
  and and_34 (and_34_out, OUT_A[0], not_17_out);
  and and_35 (and_35_out, LOAD_SELECT_1, or_2_out, LOAD_SELECT_0);
  and and_36 (and_36_out, LOAD_SELECT_1, or_2_out, not_19_out);
  and and_37 (and_37_out, not_18_out, or_2_out, LOAD_SELECT_0);
  and and_38 (and_38_out, not_18_out, or_2_out, not_19_out);
  or or_3 (or_3_out, and_3_out, and_4_out);
  not not_20 (not_20_out, or_3_out);
  or or_4 (or_4_out, and_5_out, and_6_out);
  not not_21 (not_21_out, or_4_out);
  or or_5 (or_5_out, and_7_out, and_8_out);
  not not_22 (not_22_out, or_5_out);
  or or_6 (or_6_out, and_9_out, and_10_out);
  not not_23 (not_23_out, or_6_out);
  or or_7 (or_7_out, and_11_out, and_12_out);
  not not_24 (not_24_out, or_7_out);
  or or_8 (or_8_out, and_13_out, and_14_out);
  not not_25 (not_25_out, or_8_out);
  or or_9 (or_9_out, and_15_out, and_16_out);
  not not_26 (not_26_out, or_9_out);
  or or_10 (or_10_out, and_17_out, and_18_out);
  not not_27 (not_27_out, or_10_out);
  or or_11 (or_11_out, and_19_out, and_20_out);
  not not_28 (not_28_out, or_11_out);
  or or_12 (or_12_out, and_21_out, and_22_out);
  not not_29 (not_29_out, or_12_out);
  or or_13 (or_13_out, and_23_out, and_24_out);
  not not_30 (not_30_out, or_13_out);
  or or_14 (or_14_out, and_25_out, and_26_out);
  not not_31 (not_31_out, or_14_out);
  or or_15 (or_15_out, and_27_out, and_28_out);
  not not_32 (not_32_out, or_15_out);
  or or_16 (or_16_out, and_29_out, and_30_out);
  not not_33 (not_33_out, or_16_out);
  or or_17 (or_17_out, and_31_out, and_32_out);
  not not_34 (not_34_out, or_17_out);
  or or_18 (or_18_out, and_33_out, and_34_out);
  not not_35 (not_35_out, or_18_out);
  or or_19 (or_19_out, and_38_out, RESET);
  nand nand_1 (nand_1_out, or_3_out, CLOCK);
  nand nand_2 (nand_2_out, CLOCK, not_20_out);
  nand nand_3 (nand_3_out, or_4_out, CLOCK);
  nand nand_4 (nand_4_out, CLOCK, not_21_out);
  nand nand_5 (nand_5_out, or_5_out, CLOCK);
  nand nand_6 (nand_6_out, CLOCK, not_22_out);
  nand nand_7 (nand_7_out, or_6_out, CLOCK);
  nand nand_8 (nand_8_out, CLOCK, not_23_out);
  nand nand_9 (nand_9_out, or_7_out, CLOCK);
  nand nand_10 (nand_10_out, CLOCK, not_24_out);
  nand nand_11 (nand_11_out, or_8_out, CLOCK);
  nand nand_12 (nand_12_out, CLOCK, not_25_out);
  nand nand_13 (nand_13_out, or_9_out, CLOCK);
  nand nand_14 (nand_14_out, CLOCK, not_26_out);
  nand nand_15 (nand_15_out, or_10_out, CLOCK);
  nand nand_16 (nand_16_out, CLOCK, not_27_out);
  nand nand_17 (nand_17_out, or_11_out, CLOCK);
  nand nand_18 (nand_18_out, CLOCK, not_28_out);
  nand nand_19 (nand_19_out, or_12_out, CLOCK);
  nand nand_20 (nand_20_out, CLOCK, not_29_out);
  nand nand_21 (nand_21_out, or_13_out, CLOCK);
  nand nand_22 (nand_22_out, CLOCK, not_30_out);
  nand nand_23 (nand_23_out, or_14_out, CLOCK);
  nand nand_24 (nand_24_out, CLOCK, not_31_out);
  nand nand_25 (nand_25_out, or_15_out, CLOCK);
  nand nand_26 (nand_26_out, CLOCK, not_32_out);
  nand nand_27 (nand_27_out, or_16_out, CLOCK);
  nand nand_28 (nand_28_out, CLOCK, not_33_out);
  nand nand_29 (nand_29_out, or_17_out, CLOCK);
  nand nand_30 (nand_30_out, CLOCK, not_34_out);
  nand nand_31 (nand_31_out, or_18_out, CLOCK);
  nand nand_32 (nand_32_out, CLOCK, not_35_out);
  or or_20 (or_20_out, and_35_out, RESET);
  or or_21 (or_21_out, and_36_out, RESET);
  or or_22 (or_22_out, and_37_out, RESET);
  nand nand_33 (nand_33_out, nand_1_out, nand_34_out);
  nand nand_34 (nand_34_out, nand_33_out, nand_2_out);
  nand nand_35 (nand_35_out, nand_3_out, nand_36_out);
  nand nand_36 (nand_36_out, nand_35_out, nand_4_out);
  nand nand_37 (nand_37_out, nand_5_out, nand_38_out);
  nand nand_38 (nand_38_out, nand_37_out, nand_6_out);
  nand nand_39 (nand_39_out, nand_7_out, nand_40_out);
  nand nand_40 (nand_40_out, nand_39_out, nand_8_out);
  nand nand_41 (nand_41_out, nand_9_out, nand_42_out);
  nand nand_42 (nand_42_out, nand_41_out, nand_10_out);
  nand nand_43 (nand_43_out, nand_11_out, nand_44_out);
  nand nand_44 (nand_44_out, nand_43_out, nand_12_out);
  nand nand_45 (nand_45_out, nand_13_out, nand_46_out);
  nand nand_46 (nand_46_out, nand_45_out, nand_14_out);
  nand nand_47 (nand_47_out, nand_15_out, nand_48_out);
  nand nand_48 (nand_48_out, nand_47_out, nand_16_out);
  nand nand_49 (nand_49_out, nand_17_out, nand_50_out);
  nand nand_50 (nand_50_out, nand_49_out, nand_18_out);
  nand nand_51 (nand_51_out, nand_19_out, nand_52_out);
  nand nand_52 (nand_52_out, nand_51_out, nand_20_out);
  nand nand_53 (nand_53_out, nand_21_out, nand_54_out);
  nand nand_54 (nand_54_out, nand_53_out, nand_22_out);
  nand nand_55 (nand_55_out, nand_23_out, nand_56_out);
  nand nand_56 (nand_56_out, nand_55_out, nand_24_out);
  nand nand_57 (nand_57_out, nand_25_out, nand_58_out);
  nand nand_58 (nand_58_out, nand_57_out, nand_26_out);
  nand nand_59 (nand_59_out, nand_27_out, nand_60_out);
  nand nand_60 (nand_60_out, nand_59_out, nand_28_out);
  nand nand_61 (nand_61_out, nand_29_out, nand_62_out);
  nand nand_62 (nand_62_out, nand_61_out, nand_30_out);
  nand nand_63 (nand_63_out, nand_31_out, nand_64_out);
  nand nand_64 (nand_64_out, nand_63_out, nand_32_out);
  not not_36 (not_36_out, nand_33_out);
  not not_37 (not_37_out, CLOCK);
  not not_38 (not_38_out, nand_35_out);
  not not_39 (not_39_out, CLOCK);
  not not_40 (not_40_out, nand_37_out);
  not not_41 (not_41_out, CLOCK);
  not not_42 (not_42_out, nand_39_out);
  not not_43 (not_43_out, CLOCK);
  not not_44 (not_44_out, nand_41_out);
  not not_45 (not_45_out, CLOCK);
  not not_46 (not_46_out, nand_43_out);
  not not_47 (not_47_out, CLOCK);
  not not_48 (not_48_out, nand_45_out);
  not not_49 (not_49_out, CLOCK);
  not not_50 (not_50_out, nand_47_out);
  not not_51 (not_51_out, CLOCK);
  not not_52 (not_52_out, nand_49_out);
  not not_53 (not_53_out, CLOCK);
  not not_54 (not_54_out, nand_51_out);
  not not_55 (not_55_out, CLOCK);
  not not_56 (not_56_out, nand_53_out);
  not not_57 (not_57_out, CLOCK);
  not not_58 (not_58_out, nand_55_out);
  not not_59 (not_59_out, CLOCK);
  not not_60 (not_60_out, nand_57_out);
  not not_61 (not_61_out, CLOCK);
  not not_62 (not_62_out, nand_59_out);
  not not_63 (not_63_out, CLOCK);
  not not_64 (not_64_out, nand_61_out);
  not not_65 (not_65_out, CLOCK);
  not not_66 (not_66_out, nand_63_out);
  not not_67 (not_67_out, CLOCK);
  nand nand_65 (nand_65_out, nand_33_out, not_37_out);
  nand nand_66 (nand_66_out, not_37_out, not_36_out);
  nand nand_67 (nand_67_out, nand_35_out, not_39_out);
  nand nand_68 (nand_68_out, not_39_out, not_38_out);
  nand nand_69 (nand_69_out, nand_37_out, not_41_out);
  nand nand_70 (nand_70_out, not_41_out, not_40_out);
  nand nand_71 (nand_71_out, nand_39_out, not_43_out);
  nand nand_72 (nand_72_out, not_43_out, not_42_out);
  nand nand_73 (nand_73_out, nand_41_out, not_45_out);
  nand nand_74 (nand_74_out, not_45_out, not_44_out);
  nand nand_75 (nand_75_out, nand_43_out, not_47_out);
  nand nand_76 (nand_76_out, not_47_out, not_46_out);
  nand nand_77 (nand_77_out, nand_45_out, not_49_out);
  nand nand_78 (nand_78_out, not_49_out, not_48_out);
  nand nand_79 (nand_79_out, nand_47_out, not_51_out);
  nand nand_80 (nand_80_out, not_51_out, not_50_out);
  nand nand_81 (nand_81_out, nand_49_out, not_53_out);
  nand nand_82 (nand_82_out, not_53_out, not_52_out);
  nand nand_83 (nand_83_out, nand_51_out, not_55_out);
  nand nand_84 (nand_84_out, not_55_out, not_54_out);
  nand nand_85 (nand_85_out, nand_53_out, not_57_out);
  nand nand_86 (nand_86_out, not_57_out, not_56_out);
  nand nand_87 (nand_87_out, nand_55_out, not_59_out);
  nand nand_88 (nand_88_out, not_59_out, not_58_out);
  nand nand_89 (nand_89_out, nand_57_out, not_61_out);
  nand nand_90 (nand_90_out, not_61_out, not_60_out);
  nand nand_91 (nand_91_out, nand_59_out, not_63_out);
  nand nand_92 (nand_92_out, not_63_out, not_62_out);
  nand nand_93 (nand_93_out, nand_61_out, not_65_out);
  nand nand_94 (nand_94_out, not_65_out, not_64_out);
  nand nand_95 (nand_95_out, nand_63_out, not_67_out);
  nand nand_96 (nand_96_out, not_67_out, not_66_out);
  nand nand_97 (OUT_A[15], nand_65_out, nand_98_out);
  nand nand_98 (nand_98_out, OUT_A[15], nand_66_out);
  nand nand_99 (OUT_A[14], nand_67_out, nand_100_out);
  nand nand_100 (nand_100_out, OUT_A[14], nand_68_out);
  nand nand_101 (OUT_A[13], nand_69_out, nand_102_out);
  nand nand_102 (nand_102_out, OUT_A[13], nand_70_out);
  nand nand_103 (OUT_A[12], nand_71_out, nand_104_out);
  nand nand_104 (nand_104_out, OUT_A[12], nand_72_out);
  nand nand_105 (OUT_A[11], nand_73_out, nand_106_out);
  nand nand_106 (nand_106_out, OUT_A[11], nand_74_out);
  nand nand_107 (OUT_A[10], nand_75_out, nand_108_out);
  nand nand_108 (nand_108_out, OUT_A[10], nand_76_out);
  nand nand_109 (OUT_A[9], nand_77_out, nand_110_out);
  nand nand_110 (nand_110_out, OUT_A[9], nand_78_out);
  nand nand_111 (OUT_A[8], nand_79_out, nand_112_out);
  nand nand_112 (nand_112_out, OUT_A[8], nand_80_out);
  nand nand_113 (OUT_A[7], nand_81_out, nand_114_out);
  nand nand_114 (nand_114_out, OUT_A[7], nand_82_out);
  nand nand_115 (OUT_A[6], nand_83_out, nand_116_out);
  nand nand_116 (nand_116_out, OUT_A[6], nand_84_out);
  nand nand_117 (OUT_A[5], nand_85_out, nand_118_out);
  nand nand_118 (nand_118_out, OUT_A[5], nand_86_out);
  nand nand_119 (OUT_A[4], nand_87_out, nand_120_out);
  nand nand_120 (nand_120_out, OUT_A[4], nand_88_out);
  nand nand_121 (OUT_A[3], nand_89_out, nand_122_out);
  nand nand_122 (nand_122_out, OUT_A[3], nand_90_out);
  nand nand_123 (OUT_A[2], nand_91_out, nand_124_out);
  nand nand_124 (nand_124_out, OUT_A[2], nand_92_out);
  nand nand_125 (OUT_A[1], nand_93_out, nand_126_out);
  nand nand_126 (nand_126_out, OUT_A[1], nand_94_out);
  nand nand_127 (OUT_A[0], nand_95_out, nand_128_out);
  nand nand_128 (nand_128_out, OUT_A[0], nand_96_out);
  not not_68 (not_68_out, or_22_out);
  not not_69 (not_69_out, or_22_out);
  not not_70 (not_70_out, or_22_out);
  not not_71 (not_71_out, or_22_out);
  not not_72 (not_72_out, or_22_out);
  not not_73 (not_73_out, or_22_out);
  not not_74 (not_74_out, or_22_out);
  not not_75 (not_75_out, or_22_out);
  not not_76 (not_76_out, or_22_out);
  not not_77 (not_77_out, or_22_out);
  not not_78 (not_78_out, or_22_out);
  not not_79 (not_79_out, or_22_out);
  not not_80 (not_80_out, or_22_out);
  not not_81 (not_81_out, or_22_out);
  not not_82 (not_82_out, or_22_out);
  not not_83 (not_83_out, or_22_out);
  and and_39 (and_39_out, or_1_out[15], or_22_out);
  and and_40 (and_40_out, OUT_B[15], not_68_out);
  and and_41 (and_41_out, or_1_out[14], or_22_out);
  and and_42 (and_42_out, OUT_B[14], not_69_out);
  and and_43 (and_43_out, or_1_out[13], or_22_out);
  and and_44 (and_44_out, OUT_B[13], not_70_out);
  and and_45 (and_45_out, or_1_out[12], or_22_out);
  and and_46 (and_46_out, OUT_B[12], not_71_out);
  and and_47 (and_47_out, or_1_out[11], or_22_out);
  and and_48 (and_48_out, OUT_B[11], not_72_out);
  and and_49 (and_49_out, or_1_out[10], or_22_out);
  and and_50 (and_50_out, OUT_B[10], not_73_out);
  and and_51 (and_51_out, or_1_out[9], or_22_out);
  and and_52 (and_52_out, OUT_B[9], not_74_out);
  and and_53 (and_53_out, or_1_out[8], or_22_out);
  and and_54 (and_54_out, OUT_B[8], not_75_out);
  and and_55 (and_55_out, or_1_out[7], or_22_out);
  and and_56 (and_56_out, OUT_B[7], not_76_out);
  and and_57 (and_57_out, or_1_out[6], or_22_out);
  and and_58 (and_58_out, OUT_B[6], not_77_out);
  and and_59 (and_59_out, or_1_out[5], or_22_out);
  and and_60 (and_60_out, OUT_B[5], not_78_out);
  and and_61 (and_61_out, or_1_out[4], or_22_out);
  and and_62 (and_62_out, OUT_B[4], not_79_out);
  and and_63 (and_63_out, or_1_out[3], or_22_out);
  and and_64 (and_64_out, OUT_B[3], not_80_out);
  and and_65 (and_65_out, or_1_out[2], or_22_out);
  and and_66 (and_66_out, OUT_B[2], not_81_out);
  and and_67 (and_67_out, or_1_out[1], or_22_out);
  and and_68 (and_68_out, OUT_B[2], not_82_out);
  and and_69 (and_69_out, or_1_out[0], or_22_out);
  and and_70 (and_70_out, OUT_B[2], not_83_out);
  or or_23 (or_23_out, and_39_out, and_40_out);
  not not_84 (not_84_out, or_23_out);
  or or_24 (or_24_out, and_41_out, and_42_out);
  not not_85 (not_85_out, or_24_out);
  or or_25 (or_25_out, and_43_out, and_44_out);
  not not_86 (not_86_out, or_25_out);
  or or_26 (or_26_out, and_45_out, and_46_out);
  not not_87 (not_87_out, or_26_out);
  or or_27 (or_27_out, and_47_out, and_48_out);
  not not_88 (not_88_out, or_27_out);
  or or_28 (or_28_out, and_49_out, and_50_out);
  not not_89 (not_89_out, or_28_out);
  or or_29 (or_29_out, and_51_out, and_52_out);
  not not_90 (not_90_out, or_29_out);
  or or_30 (or_30_out, and_53_out, and_54_out);
  not not_91 (not_91_out, or_30_out);
  or or_31 (or_31_out, and_55_out, and_56_out);
  not not_92 (not_92_out, or_31_out);
  or or_32 (or_32_out, and_57_out, and_58_out);
  not not_93 (not_93_out, or_32_out);
  or or_33 (or_33_out, and_59_out, and_60_out);
  not not_94 (not_94_out, or_33_out);
  or or_34 (or_34_out, and_61_out, and_62_out);
  not not_95 (not_95_out, or_34_out);
  or or_35 (or_35_out, and_63_out, and_64_out);
  not not_96 (not_96_out, or_35_out);
  or or_36 (or_36_out, and_65_out, and_66_out);
  not not_97 (not_97_out, or_36_out);
  or or_37 (or_37_out, and_67_out, and_68_out);
  not not_98 (not_98_out, or_37_out);
  or or_38 (or_38_out, and_69_out, and_70_out);
  not not_99 (not_99_out, or_38_out);
  nand nand_129 (nand_129_out, or_23_out, CLOCK);
  nand nand_130 (nand_130_out, CLOCK, not_84_out);
  nand nand_131 (nand_131_out, or_24_out, CLOCK);
  nand nand_132 (nand_132_out, CLOCK, not_85_out);
  nand nand_133 (nand_133_out, or_25_out, CLOCK);
  nand nand_134 (nand_134_out, CLOCK, not_86_out);
  nand nand_135 (nand_135_out, or_26_out, CLOCK);
  nand nand_136 (nand_136_out, CLOCK, not_87_out);
  nand nand_137 (nand_137_out, or_27_out, CLOCK);
  nand nand_138 (nand_138_out, CLOCK, not_88_out);
  nand nand_139 (nand_139_out, or_28_out, CLOCK);
  nand nand_140 (nand_140_out, CLOCK, not_89_out);
  nand nand_141 (nand_141_out, or_29_out, CLOCK);
  nand nand_142 (nand_142_out, CLOCK, not_90_out);
  nand nand_143 (nand_143_out, or_30_out, CLOCK);
  nand nand_144 (nand_144_out, CLOCK, not_91_out);
  nand nand_145 (nand_145_out, or_31_out, CLOCK);
  nand nand_146 (nand_146_out, CLOCK, not_92_out);
  nand nand_147 (nand_147_out, or_32_out, CLOCK);
  nand nand_148 (nand_148_out, CLOCK, not_93_out);
  nand nand_149 (nand_149_out, or_33_out, CLOCK);
  nand nand_150 (nand_150_out, CLOCK, not_94_out);
  nand nand_151 (nand_151_out, or_34_out, CLOCK);
  nand nand_152 (nand_152_out, CLOCK, not_95_out);
  nand nand_153 (nand_153_out, or_35_out, CLOCK);
  nand nand_154 (nand_154_out, CLOCK, not_96_out);
  nand nand_155 (nand_155_out, or_36_out, CLOCK);
  nand nand_156 (nand_156_out, CLOCK, not_97_out);
  nand nand_157 (nand_157_out, or_37_out, CLOCK);
  nand nand_158 (nand_158_out, CLOCK, not_98_out);
  nand nand_159 (nand_159_out, or_38_out, CLOCK);
  nand nand_160 (nand_160_out, CLOCK, not_99_out);
  nand nand_161 (nand_161_out, nand_129_out, nand_162_out);
  nand nand_162 (nand_162_out, nand_161_out, nand_130_out);
  not not_100 (not_100_out, CLOCK);
  nand nand_163 (nand_163_out, nand_131_out, nand_164_out);
  nand nand_164 (nand_164_out, nand_163_out, nand_132_out);
  not not_101 (not_101_out, CLOCK);
  nand nand_165 (nand_165_out, nand_133_out, nand_166_out);
  nand nand_166 (nand_166_out, nand_165_out, nand_134_out);
  not not_102 (not_102_out, CLOCK);
  nand nand_167 (nand_167_out, nand_135_out, nand_168_out);
  nand nand_168 (nand_168_out, nand_167_out, nand_136_out);
  not not_103 (not_103_out, CLOCK);
  nand nand_169 (nand_169_out, nand_137_out, nand_170_out);
  nand nand_170 (nand_170_out, nand_169_out, nand_138_out);
  not not_104 (not_104_out, CLOCK);
  nand nand_171 (nand_171_out, nand_139_out, nand_172_out);
  nand nand_172 (nand_172_out, nand_171_out, nand_140_out);
  not not_105 (not_105_out, CLOCK);
  nand nand_173 (nand_173_out, nand_141_out, nand_174_out);
  nand nand_174 (nand_174_out, nand_173_out, nand_142_out);
  not not_106 (not_106_out, CLOCK);
  nand nand_175 (nand_175_out, nand_143_out, nand_176_out);
  nand nand_176 (nand_176_out, nand_175_out, nand_144_out);
  not not_107 (not_107_out, CLOCK);
  nand nand_177 (nand_177_out, nand_145_out, nand_178_out);
  nand nand_178 (nand_178_out, nand_177_out, nand_146_out);
  not not_108 (not_108_out, CLOCK);
  nand nand_179 (nand_179_out, nand_147_out, nand_180_out);
  nand nand_180 (nand_180_out, nand_179_out, nand_148_out);
  not not_109 (not_109_out, CLOCK);
  nand nand_181 (nand_181_out, nand_149_out, nand_182_out);
  nand nand_182 (nand_182_out, nand_181_out, nand_150_out);
  not not_110 (not_110_out, CLOCK);
  nand nand_183 (nand_183_out, nand_151_out, nand_184_out);
  nand nand_184 (nand_184_out, nand_183_out, nand_152_out);
  not not_111 (not_111_out, CLOCK);
  nand nand_185 (nand_185_out, nand_153_out, nand_186_out);
  nand nand_186 (nand_186_out, nand_185_out, nand_154_out);
  not not_112 (not_112_out, CLOCK);
  nand nand_187 (nand_187_out, nand_155_out, nand_188_out);
  nand nand_188 (nand_188_out, nand_187_out, nand_156_out);
  not not_113 (not_113_out, CLOCK);
  nand nand_189 (nand_189_out, nand_157_out, nand_190_out);
  nand nand_190 (nand_190_out, nand_189_out, nand_158_out);
  not not_114 (not_114_out, CLOCK);
  nand nand_191 (nand_191_out, nand_159_out, nand_192_out);
  nand nand_192 (nand_192_out, nand_191_out, nand_160_out);
  not not_115 (not_115_out, CLOCK);
  nand nand_193 (nand_193_out, nand_161_out, not_100_out);
  nand nand_194 (nand_194_out, not_100_out, not_116_out);
  not not_116 (not_116_out, nand_161_out);
  nand nand_195 (nand_195_out, nand_163_out, not_101_out);
  nand nand_196 (nand_196_out, not_101_out, not_117_out);
  not not_117 (not_117_out, nand_163_out);
  nand nand_197 (nand_197_out, nand_165_out, not_102_out);
  nand nand_198 (nand_198_out, not_102_out, not_118_out);
  not not_118 (not_118_out, nand_165_out);
  nand nand_199 (nand_199_out, nand_167_out, not_103_out);
  nand nand_200 (nand_200_out, not_103_out, not_119_out);
  not not_119 (not_119_out, nand_167_out);
  nand nand_201 (nand_201_out, nand_169_out, not_104_out);
  nand nand_202 (nand_202_out, not_104_out, not_120_out);
  not not_120 (not_120_out, nand_169_out);
  nand nand_203 (nand_203_out, nand_171_out, not_105_out);
  nand nand_204 (nand_204_out, not_105_out, not_121_out);
  not not_121 (not_121_out, nand_171_out);
  nand nand_205 (nand_205_out, nand_173_out, not_106_out);
  nand nand_206 (nand_206_out, not_106_out, not_122_out);
  not not_122 (not_122_out, nand_173_out);
  nand nand_207 (nand_207_out, nand_175_out, not_107_out);
  nand nand_208 (nand_208_out, not_107_out, not_123_out);
  not not_123 (not_123_out, nand_175_out);
  nand nand_209 (nand_209_out, nand_177_out, not_108_out);
  nand nand_210 (nand_210_out, not_108_out, not_124_out);
  not not_124 (not_124_out, nand_177_out);
  nand nand_211 (nand_211_out, nand_179_out, not_109_out);
  nand nand_212 (nand_212_out, not_109_out, not_125_out);
  not not_125 (not_125_out, nand_179_out);
  nand nand_213 (nand_213_out, nand_181_out, not_110_out);
  nand nand_214 (nand_214_out, not_110_out, not_126_out);
  not not_126 (not_126_out, nand_181_out);
  nand nand_215 (nand_215_out, nand_183_out, not_111_out);
  nand nand_216 (nand_216_out, not_111_out, not_127_out);
  not not_127 (not_127_out, nand_183_out);
  nand nand_217 (nand_217_out, nand_185_out, not_112_out);
  nand nand_218 (nand_218_out, not_112_out, not_128_out);
  not not_128 (not_128_out, nand_185_out);
  nand nand_219 (nand_219_out, nand_187_out, not_113_out);
  nand nand_220 (nand_220_out, not_113_out, not_129_out);
  not not_129 (not_129_out, nand_187_out);
  nand nand_221 (nand_221_out, nand_189_out, not_114_out);
  nand nand_222 (nand_222_out, not_114_out, not_130_out);
  not not_130 (not_130_out, nand_189_out);
  nand nand_223 (nand_223_out, nand_191_out, not_115_out);
  nand nand_224 (nand_224_out, not_115_out, not_131_out);
  not not_131 (not_131_out, nand_191_out);
  nand nand_225 (OUT_B[15], nand_193_out, nand_226_out);
  nand nand_226 (nand_226_out, OUT_B[15], nand_194_out);
  nand nand_227 (OUT_B[14], nand_195_out, nand_228_out);
  nand nand_228 (nand_228_out, OUT_B[14], nand_196_out);
  nand nand_229 (OUT_B[13], nand_197_out, nand_230_out);
  nand nand_230 (nand_230_out, OUT_B[13], nand_198_out);
  nand nand_231 (OUT_B[12], nand_199_out, nand_232_out);
  nand nand_232 (nand_232_out, OUT_B[12], nand_200_out);
  nand nand_233 (OUT_B[11], nand_201_out, nand_234_out);
  nand nand_234 (nand_234_out, OUT_B[11], nand_202_out);
  nand nand_235 (OUT_B[10], nand_203_out, nand_236_out);
  nand nand_236 (nand_236_out, OUT_B[10], nand_204_out);
  nand nand_237 (OUT_B[9], nand_205_out, nand_238_out);
  nand nand_238 (nand_238_out, OUT_B[9], nand_206_out);
  nand nand_239 (OUT_B[8], nand_207_out, nand_240_out);
  nand nand_240 (nand_240_out, OUT_B[8], nand_208_out);
  nand nand_241 (OUT_B[7], nand_209_out, nand_242_out);
  nand nand_242 (nand_242_out, OUT_B[7], nand_210_out);
  nand nand_243 (OUT_B[6], nand_211_out, nand_244_out);
  nand nand_244 (nand_244_out, OUT_B[6], nand_212_out);
  nand nand_245 (OUT_B[5], nand_213_out, nand_246_out);
  nand nand_246 (nand_246_out, OUT_B[5], nand_214_out);
  nand nand_247 (OUT_B[4], nand_215_out, nand_248_out);
  nand nand_248 (nand_248_out, OUT_B[4], nand_216_out);
  nand nand_249 (OUT_B[3], nand_217_out, nand_250_out);
  nand nand_250 (nand_250_out, OUT_B[3], nand_218_out);
  nand nand_251 (OUT_B[2], nand_219_out, nand_252_out);
  nand nand_252 (nand_252_out, OUT_B[2], nand_220_out);
  nand nand_253 (OUT_B[2], nand_221_out, nand_254_out);
  nand nand_254 (nand_254_out, OUT_B[2], nand_222_out);
  nand nand_255 (OUT_B[2], nand_223_out, nand_256_out);
  nand nand_256 (nand_256_out, OUT_B[2], nand_224_out);
  not not_132 (not_132_out, or_21_out);
  not not_133 (not_133_out, or_21_out);
  not not_134 (not_134_out, or_21_out);
  not not_135 (not_135_out, or_21_out);
  not not_136 (not_136_out, or_21_out);
  not not_137 (not_137_out, or_21_out);
  not not_138 (not_138_out, or_21_out);
  not not_139 (not_139_out, or_21_out);
  not not_140 (not_140_out, or_21_out);
  not not_141 (not_141_out, or_21_out);
  not not_142 (not_142_out, or_21_out);
  not not_143 (not_143_out, or_21_out);
  not not_144 (not_144_out, or_21_out);
  not not_145 (not_145_out, or_21_out);
  not not_146 (not_146_out, or_21_out);
  not not_147 (not_147_out, or_21_out);
  and and_71 (and_71_out, or_1_out[15], or_21_out);
  and and_72 (and_72_out, OUT_C[15], not_132_out);
  and and_73 (and_73_out, or_1_out[14], or_21_out);
  and and_74 (and_74_out, OUT_C[14], not_133_out);
  and and_75 (and_75_out, or_1_out[13], or_21_out);
  and and_76 (and_76_out, OUT_C[13], not_134_out);
  and and_77 (and_77_out, or_1_out[12], or_21_out);
  and and_78 (and_78_out, OUT_C[12], not_135_out);
  and and_79 (and_79_out, or_1_out[11], or_21_out);
  and and_80 (and_80_out, OUT_C[11], not_136_out);
  and and_81 (and_81_out, or_1_out[10], or_21_out);
  and and_82 (and_82_out, OUT_C[10], not_137_out);
  and and_83 (and_83_out, or_1_out[9], or_21_out);
  and and_84 (and_84_out, OUT_C[9], not_138_out);
  and and_85 (and_85_out, or_1_out[8], or_21_out);
  and and_86 (and_86_out, OUT_C[8], not_139_out);
  and and_87 (and_87_out, or_1_out[7], or_21_out);
  and and_88 (and_88_out, OUT_C[7], not_140_out);
  and and_89 (and_89_out, or_1_out[6], or_21_out);
  and and_90 (and_90_out, OUT_C[6], not_141_out);
  and and_91 (and_91_out, or_1_out[5], or_21_out);
  and and_92 (and_92_out, OUT_C[5], not_142_out);
  and and_93 (and_93_out, or_1_out[4], or_21_out);
  and and_94 (and_94_out, OUT_C[4], not_143_out);
  and and_95 (and_95_out, or_1_out[3], or_21_out);
  and and_96 (and_96_out, OUT_C[3], not_144_out);
  and and_97 (and_97_out, or_1_out[2], or_21_out);
  and and_98 (and_98_out, OUT_C[2], not_145_out);
  and and_99 (and_99_out, or_1_out[1], or_21_out);
  and and_100 (and_100_out, OUT_C[2], not_146_out);
  and and_101 (and_101_out, or_1_out[0], or_21_out);
  and and_102 (and_102_out, OUT_C[2], not_147_out);
  or or_39 (or_39_out, and_71_out, and_72_out);
  not not_148 (not_148_out, or_39_out);
  or or_40 (or_40_out, and_73_out, and_74_out);
  not not_149 (not_149_out, or_40_out);
  or or_41 (or_41_out, and_75_out, and_76_out);
  not not_150 (not_150_out, or_41_out);
  or or_42 (or_42_out, and_77_out, and_78_out);
  not not_151 (not_151_out, or_42_out);
  or or_43 (or_43_out, and_79_out, and_80_out);
  not not_152 (not_152_out, or_43_out);
  or or_44 (or_44_out, and_81_out, and_82_out);
  not not_153 (not_153_out, or_44_out);
  or or_45 (or_45_out, and_83_out, and_84_out);
  not not_154 (not_154_out, or_45_out);
  or or_46 (or_46_out, and_85_out, and_86_out);
  not not_155 (not_155_out, or_46_out);
  or or_47 (or_47_out, and_87_out, and_88_out);
  not not_156 (not_156_out, or_47_out);
  or or_48 (or_48_out, and_89_out, and_90_out);
  not not_157 (not_157_out, or_48_out);
  or or_49 (or_49_out, and_91_out, and_92_out);
  not not_158 (not_158_out, or_49_out);
  or or_50 (or_50_out, and_93_out, and_94_out);
  not not_159 (not_159_out, or_50_out);
  or or_51 (or_51_out, and_95_out, and_96_out);
  not not_160 (not_160_out, or_51_out);
  or or_52 (or_52_out, and_97_out, and_98_out);
  not not_161 (not_161_out, or_52_out);
  or or_53 (or_53_out, and_99_out, and_100_out);
  not not_162 (not_162_out, or_53_out);
  or or_54 (or_54_out, and_101_out, and_102_out);
  not not_163 (not_163_out, or_54_out);
  nand nand_257 (nand_257_out, or_39_out, CLOCK);
  nand nand_258 (nand_258_out, CLOCK, not_148_out);
  nand nand_259 (nand_259_out, or_40_out, CLOCK);
  nand nand_260 (nand_260_out, CLOCK, not_149_out);
  nand nand_261 (nand_261_out, or_41_out, CLOCK);
  nand nand_262 (nand_262_out, CLOCK, not_150_out);
  nand nand_263 (nand_263_out, or_42_out, CLOCK);
  nand nand_264 (nand_264_out, CLOCK, not_151_out);
  nand nand_265 (nand_265_out, or_43_out, CLOCK);
  nand nand_266 (nand_266_out, CLOCK, not_152_out);
  nand nand_267 (nand_267_out, or_44_out, CLOCK);
  nand nand_268 (nand_268_out, CLOCK, not_153_out);
  nand nand_269 (nand_269_out, or_45_out, CLOCK);
  nand nand_270 (nand_270_out, CLOCK, not_154_out);
  nand nand_271 (nand_271_out, or_46_out, CLOCK);
  nand nand_272 (nand_272_out, CLOCK, not_155_out);
  nand nand_273 (nand_273_out, or_47_out, CLOCK);
  nand nand_274 (nand_274_out, CLOCK, not_156_out);
  nand nand_275 (nand_275_out, or_48_out, CLOCK);
  nand nand_276 (nand_276_out, CLOCK, not_157_out);
  nand nand_277 (nand_277_out, or_49_out, CLOCK);
  nand nand_278 (nand_278_out, CLOCK, not_158_out);
  nand nand_279 (nand_279_out, or_50_out, CLOCK);
  nand nand_280 (nand_280_out, CLOCK, not_159_out);
  nand nand_281 (nand_281_out, or_51_out, CLOCK);
  nand nand_282 (nand_282_out, CLOCK, not_160_out);
  nand nand_283 (nand_283_out, or_52_out, CLOCK);
  nand nand_284 (nand_284_out, CLOCK, not_161_out);
  nand nand_285 (nand_285_out, or_53_out, CLOCK);
  nand nand_286 (nand_286_out, CLOCK, not_162_out);
  nand nand_287 (nand_287_out, or_54_out, CLOCK);
  nand nand_288 (nand_288_out, CLOCK, not_163_out);
  nand nand_289 (nand_289_out, nand_257_out, nand_290_out);
  nand nand_290 (nand_290_out, nand_289_out, nand_258_out);
  not not_164 (not_164_out, CLOCK);
  nand nand_291 (nand_291_out, nand_259_out, nand_292_out);
  nand nand_292 (nand_292_out, nand_291_out, nand_260_out);
  not not_165 (not_165_out, CLOCK);
  nand nand_293 (nand_293_out, nand_261_out, nand_294_out);
  nand nand_294 (nand_294_out, nand_293_out, nand_262_out);
  not not_166 (not_166_out, CLOCK);
  nand nand_295 (nand_295_out, nand_263_out, nand_296_out);
  nand nand_296 (nand_296_out, nand_295_out, nand_264_out);
  not not_167 (not_167_out, CLOCK);
  nand nand_297 (nand_297_out, nand_265_out, nand_298_out);
  nand nand_298 (nand_298_out, nand_297_out, nand_266_out);
  not not_168 (not_168_out, CLOCK);
  nand nand_299 (nand_299_out, nand_267_out, nand_300_out);
  nand nand_300 (nand_300_out, nand_299_out, nand_268_out);
  not not_169 (not_169_out, CLOCK);
  nand nand_301 (nand_301_out, nand_269_out, nand_302_out);
  nand nand_302 (nand_302_out, nand_301_out, nand_270_out);
  not not_170 (not_170_out, CLOCK);
  nand nand_303 (nand_303_out, nand_271_out, nand_304_out);
  nand nand_304 (nand_304_out, nand_303_out, nand_272_out);
  not not_171 (not_171_out, CLOCK);
  nand nand_305 (nand_305_out, nand_273_out, nand_306_out);
  nand nand_306 (nand_306_out, nand_305_out, nand_274_out);
  not not_172 (not_172_out, CLOCK);
  nand nand_307 (nand_307_out, nand_275_out, nand_308_out);
  nand nand_308 (nand_308_out, nand_307_out, nand_276_out);
  not not_173 (not_173_out, CLOCK);
  nand nand_309 (nand_309_out, nand_277_out, nand_310_out);
  nand nand_310 (nand_310_out, nand_309_out, nand_278_out);
  not not_174 (not_174_out, CLOCK);
  nand nand_311 (nand_311_out, nand_279_out, nand_312_out);
  nand nand_312 (nand_312_out, nand_311_out, nand_280_out);
  not not_175 (not_175_out, CLOCK);
  nand nand_313 (nand_313_out, nand_281_out, nand_314_out);
  nand nand_314 (nand_314_out, nand_313_out, nand_282_out);
  not not_176 (not_176_out, CLOCK);
  nand nand_315 (nand_315_out, nand_283_out, nand_316_out);
  nand nand_316 (nand_316_out, nand_315_out, nand_284_out);
  not not_177 (not_177_out, CLOCK);
  nand nand_317 (nand_317_out, nand_285_out, nand_318_out);
  nand nand_318 (nand_318_out, nand_317_out, nand_286_out);
  not not_178 (not_178_out, CLOCK);
  nand nand_319 (nand_319_out, nand_287_out, nand_320_out);
  nand nand_320 (nand_320_out, nand_319_out, nand_288_out);
  not not_179 (not_179_out, CLOCK);
  not not_180 (not_180_out, nand_289_out);
  not not_181 (not_181_out, nand_291_out);
  not not_182 (not_182_out, nand_293_out);
  not not_183 (not_183_out, nand_295_out);
  not not_184 (not_184_out, nand_297_out);
  not not_185 (not_185_out, nand_299_out);
  not not_186 (not_186_out, nand_301_out);
  not not_187 (not_187_out, nand_303_out);
  not not_188 (not_188_out, nand_305_out);
  not not_189 (not_189_out, nand_307_out);
  not not_190 (not_190_out, nand_309_out);
  not not_191 (not_191_out, nand_311_out);
  not not_192 (not_192_out, nand_313_out);
  not not_193 (not_193_out, nand_315_out);
  not not_194 (not_194_out, nand_317_out);
  not not_195 (not_195_out, nand_319_out);
  nand nand_321 (nand_321_out, nand_289_out, not_164_out);
  nand nand_322 (nand_322_out, not_164_out, not_180_out);
  nand nand_323 (nand_323_out, nand_291_out, not_165_out);
  nand nand_324 (nand_324_out, not_165_out, not_181_out);
  nand nand_325 (nand_325_out, nand_293_out, not_166_out);
  nand nand_326 (nand_326_out, not_166_out, not_182_out);
  nand nand_327 (nand_327_out, nand_295_out, not_167_out);
  nand nand_328 (nand_328_out, not_167_out, not_183_out);
  nand nand_329 (nand_329_out, nand_297_out, not_168_out);
  nand nand_330 (nand_330_out, not_168_out, not_184_out);
  nand nand_331 (nand_331_out, nand_299_out, not_169_out);
  nand nand_332 (nand_332_out, not_169_out, not_185_out);
  nand nand_333 (nand_333_out, nand_301_out, not_170_out);
  nand nand_334 (nand_334_out, not_170_out, not_186_out);
  nand nand_335 (nand_335_out, nand_303_out, not_171_out);
  nand nand_336 (nand_336_out, not_171_out, not_187_out);
  nand nand_337 (nand_337_out, nand_305_out, not_172_out);
  nand nand_338 (nand_338_out, not_172_out, not_188_out);
  nand nand_339 (nand_339_out, nand_307_out, not_173_out);
  nand nand_340 (nand_340_out, not_173_out, not_189_out);
  nand nand_341 (nand_341_out, nand_309_out, not_174_out);
  nand nand_342 (nand_342_out, not_174_out, not_190_out);
  nand nand_343 (nand_343_out, nand_311_out, not_175_out);
  nand nand_344 (nand_344_out, not_175_out, not_191_out);
  nand nand_345 (nand_345_out, nand_313_out, not_176_out);
  nand nand_346 (nand_346_out, not_176_out, not_192_out);
  nand nand_347 (nand_347_out, nand_315_out, not_177_out);
  nand nand_348 (nand_348_out, not_177_out, not_193_out);
  nand nand_349 (nand_349_out, nand_317_out, not_178_out);
  nand nand_350 (nand_350_out, not_178_out, not_194_out);
  nand nand_351 (nand_351_out, nand_319_out, not_179_out);
  nand nand_352 (nand_352_out, not_179_out, not_195_out);
  nand nand_353 (OUT_C[15], nand_321_out, nand_354_out);
  nand nand_354 (nand_354_out, OUT_C[15], nand_322_out);
  nand nand_355 (OUT_C[14], nand_323_out, nand_356_out);
  nand nand_356 (nand_356_out, OUT_C[14], nand_324_out);
  nand nand_357 (OUT_C[13], nand_325_out, nand_358_out);
  nand nand_358 (nand_358_out, OUT_C[13], nand_326_out);
  nand nand_359 (OUT_C[12], nand_327_out, nand_360_out);
  nand nand_360 (nand_360_out, OUT_C[12], nand_328_out);
  nand nand_361 (OUT_C[11], nand_329_out, nand_362_out);
  nand nand_362 (nand_362_out, OUT_C[11], nand_330_out);
  nand nand_363 (OUT_C[10], nand_331_out, nand_364_out);
  nand nand_364 (nand_364_out, OUT_C[10], nand_332_out);
  nand nand_365 (OUT_C[9], nand_333_out, nand_366_out);
  nand nand_366 (nand_366_out, OUT_C[9], nand_334_out);
  nand nand_367 (OUT_C[8], nand_335_out, nand_368_out);
  nand nand_368 (nand_368_out, OUT_C[8], nand_336_out);
  nand nand_369 (OUT_C[7], nand_337_out, nand_370_out);
  nand nand_370 (nand_370_out, OUT_C[7], nand_338_out);
  nand nand_371 (OUT_C[6], nand_339_out, nand_372_out);
  nand nand_372 (nand_372_out, OUT_C[6], nand_340_out);
  nand nand_373 (OUT_C[5], nand_341_out, nand_374_out);
  nand nand_374 (nand_374_out, OUT_C[5], nand_342_out);
  nand nand_375 (OUT_C[4], nand_343_out, nand_376_out);
  nand nand_376 (nand_376_out, OUT_C[4], nand_344_out);
  nand nand_377 (OUT_C[3], nand_345_out, nand_378_out);
  nand nand_378 (nand_378_out, OUT_C[3], nand_346_out);
  nand nand_379 (OUT_C[2], nand_347_out, nand_380_out);
  nand nand_380 (nand_380_out, OUT_C[2], nand_348_out);
  nand nand_381 (OUT_C[2], nand_349_out, nand_382_out);
  nand nand_382 (nand_382_out, OUT_C[2], nand_350_out);
  nand nand_383 (OUT_C[2], nand_351_out, nand_384_out);
  nand nand_384 (nand_384_out, OUT_C[2], nand_352_out);
  not not_196 (not_196_out, or_20_out);
  not not_197 (not_197_out, or_20_out);
  not not_198 (not_198_out, or_20_out);
  not not_199 (not_199_out, or_20_out);
  not not_200 (not_200_out, or_20_out);
  not not_201 (not_201_out, or_20_out);
  not not_202 (not_202_out, or_20_out);
  not not_203 (not_203_out, or_20_out);
  not not_204 (not_204_out, or_20_out);
  not not_205 (not_205_out, or_20_out);
  not not_206 (not_206_out, or_20_out);
  not not_207 (not_207_out, or_20_out);
  not not_208 (not_208_out, or_20_out);
  not not_209 (not_209_out, or_20_out);
  not not_210 (not_210_out, or_20_out);
  not not_211 (not_211_out, or_20_out);
  and and_103 (and_103_out, or_1_out[15], or_20_out);
  and and_104 (and_104_out, OUT_D[15], not_196_out);
  and and_105 (and_105_out, or_1_out[14], or_20_out);
  and and_106 (and_106_out, OUT_D[14], not_197_out);
  and and_107 (and_107_out, or_1_out[13], or_20_out);
  and and_108 (and_108_out, OUT_D[13], not_198_out);
  and and_109 (and_109_out, or_1_out[12], or_20_out);
  and and_110 (and_110_out, OUT_D[12], not_199_out);
  and and_111 (and_111_out, or_1_out[11], or_20_out);
  and and_112 (and_112_out, OUT_D[11], not_200_out);
  and and_113 (and_113_out, or_1_out[10], or_20_out);
  and and_114 (and_114_out, OUT_D[10], not_201_out);
  and and_115 (and_115_out, or_1_out[9], or_20_out);
  and and_116 (and_116_out, OUT_D[9], not_202_out);
  and and_117 (and_117_out, or_1_out[8], or_20_out);
  and and_118 (and_118_out, OUT_D[8], not_203_out);
  and and_119 (and_119_out, or_1_out[7], or_20_out);
  and and_120 (and_120_out, OUT_D[7], not_204_out);
  and and_121 (and_121_out, or_1_out[6], or_20_out);
  and and_122 (and_122_out, OUT_D[6], not_205_out);
  and and_123 (and_123_out, or_1_out[5], or_20_out);
  and and_124 (and_124_out, OUT_D[5], not_206_out);
  and and_125 (and_125_out, or_1_out[4], or_20_out);
  and and_126 (and_126_out, OUT_D[4], not_207_out);
  and and_127 (and_127_out, or_1_out[3], or_20_out);
  and and_128 (and_128_out, OUT_D[3], not_208_out);
  and and_129 (and_129_out, or_1_out[2], or_20_out);
  and and_130 (and_130_out, OUT_D[2], not_209_out);
  and and_131 (and_131_out, or_1_out[1], or_20_out);
  and and_132 (and_132_out, OUT_D[1], not_210_out);
  and and_133 (and_133_out, or_1_out[0], or_20_out);
  and and_134 (and_134_out, OUT_D[0], not_211_out);
  or or_55 (or_55_out, and_103_out, and_104_out);
  not not_212 (not_212_out, or_55_out);
  or or_56 (or_56_out, and_105_out, and_106_out);
  not not_213 (not_213_out, or_56_out);
  or or_57 (or_57_out, and_107_out, and_108_out);
  not not_214 (not_214_out, or_57_out);
  or or_58 (or_58_out, and_109_out, and_110_out);
  not not_215 (not_215_out, or_58_out);
  or or_59 (or_59_out, and_111_out, and_112_out);
  not not_216 (not_216_out, or_59_out);
  or or_60 (or_60_out, and_113_out, and_114_out);
  not not_217 (not_217_out, or_60_out);
  or or_61 (or_61_out, and_115_out, and_116_out);
  not not_218 (not_218_out, or_61_out);
  or or_62 (or_62_out, and_117_out, and_118_out);
  not not_219 (not_219_out, or_62_out);
  or or_63 (or_63_out, and_119_out, and_120_out);
  not not_220 (not_220_out, or_63_out);
  or or_64 (or_64_out, and_121_out, and_122_out);
  not not_221 (not_221_out, or_64_out);
  or or_65 (or_65_out, and_123_out, and_124_out);
  not not_222 (not_222_out, or_65_out);
  or or_66 (or_66_out, and_125_out, and_126_out);
  not not_223 (not_223_out, or_66_out);
  or or_67 (or_67_out, and_127_out, and_128_out);
  not not_224 (not_224_out, or_67_out);
  or or_68 (or_68_out, and_129_out, and_130_out);
  not not_225 (not_225_out, or_68_out);
  or or_69 (or_69_out, and_131_out, and_132_out);
  not not_226 (not_226_out, or_69_out);
  or or_70 (or_70_out, and_133_out, and_134_out);
  not not_227 (not_227_out, or_70_out);
  nand nand_385 (nand_385_out, or_55_out, CLOCK);
  nand nand_386 (nand_386_out, CLOCK, not_212_out);
  nand nand_387 (nand_387_out, or_56_out, CLOCK);
  nand nand_388 (nand_388_out, CLOCK, not_213_out);
  nand nand_389 (nand_389_out, or_57_out, CLOCK);
  nand nand_390 (nand_390_out, CLOCK, not_214_out);
  nand nand_391 (nand_391_out, or_58_out, CLOCK);
  nand nand_392 (nand_392_out, CLOCK, not_215_out);
  nand nand_393 (nand_393_out, or_59_out, CLOCK);
  nand nand_394 (nand_394_out, CLOCK, not_216_out);
  nand nand_395 (nand_395_out, or_60_out, CLOCK);
  nand nand_396 (nand_396_out, CLOCK, not_217_out);
  nand nand_397 (nand_397_out, or_61_out, CLOCK);
  nand nand_398 (nand_398_out, CLOCK, not_218_out);
  nand nand_399 (nand_399_out, or_62_out, CLOCK);
  nand nand_400 (nand_400_out, CLOCK, not_219_out);
  nand nand_401 (nand_401_out, or_63_out, CLOCK);
  nand nand_402 (nand_402_out, CLOCK, not_220_out);
  nand nand_403 (nand_403_out, or_64_out, CLOCK);
  nand nand_404 (nand_404_out, CLOCK, not_221_out);
  nand nand_405 (nand_405_out, or_65_out, CLOCK);
  nand nand_406 (nand_406_out, CLOCK, not_222_out);
  nand nand_407 (nand_407_out, or_66_out, CLOCK);
  nand nand_408 (nand_408_out, CLOCK, not_223_out);
  nand nand_409 (nand_409_out, or_67_out, CLOCK);
  nand nand_410 (nand_410_out, CLOCK, not_224_out);
  nand nand_411 (nand_411_out, or_68_out, CLOCK);
  nand nand_412 (nand_412_out, CLOCK, not_225_out);
  nand nand_413 (nand_413_out, or_69_out, CLOCK);
  nand nand_414 (nand_414_out, CLOCK, not_226_out);
  nand nand_415 (nand_415_out, or_70_out, CLOCK);
  nand nand_416 (nand_416_out, CLOCK, not_227_out);
  nand nand_417 (nand_417_out, nand_385_out, nand_418_out);
  nand nand_418 (nand_418_out, nand_417_out, nand_386_out);
  not not_228 (not_228_out, CLOCK);
  nand nand_419 (nand_419_out, nand_387_out, nand_420_out);
  nand nand_420 (nand_420_out, nand_419_out, nand_388_out);
  not not_229 (not_229_out, CLOCK);
  nand nand_421 (nand_421_out, nand_389_out, nand_422_out);
  nand nand_422 (nand_422_out, nand_421_out, nand_390_out);
  not not_230 (not_230_out, CLOCK);
  nand nand_423 (nand_423_out, nand_391_out, nand_424_out);
  nand nand_424 (nand_424_out, nand_423_out, nand_392_out);
  not not_231 (not_231_out, CLOCK);
  nand nand_425 (nand_425_out, nand_393_out, nand_426_out);
  nand nand_426 (nand_426_out, nand_425_out, nand_394_out);
  not not_232 (not_232_out, CLOCK);
  nand nand_427 (nand_427_out, nand_395_out, nand_428_out);
  nand nand_428 (nand_428_out, nand_427_out, nand_396_out);
  not not_233 (not_233_out, CLOCK);
  nand nand_429 (nand_429_out, nand_397_out, nand_430_out);
  nand nand_430 (nand_430_out, nand_429_out, nand_398_out);
  not not_234 (not_234_out, CLOCK);
  nand nand_431 (nand_431_out, nand_399_out, nand_432_out);
  nand nand_432 (nand_432_out, nand_431_out, nand_400_out);
  not not_235 (not_235_out, CLOCK);
  nand nand_433 (nand_433_out, nand_401_out, nand_434_out);
  nand nand_434 (nand_434_out, nand_433_out, nand_402_out);
  not not_236 (not_236_out, CLOCK);
  nand nand_435 (nand_435_out, nand_403_out, nand_436_out);
  nand nand_436 (nand_436_out, nand_435_out, nand_404_out);
  not not_237 (not_237_out, CLOCK);
  nand nand_437 (nand_437_out, nand_405_out, nand_438_out);
  nand nand_438 (nand_438_out, nand_437_out, nand_406_out);
  not not_238 (not_238_out, CLOCK);
  nand nand_439 (nand_439_out, nand_407_out, nand_440_out);
  nand nand_440 (nand_440_out, nand_439_out, nand_408_out);
  not not_239 (not_239_out, CLOCK);
  nand nand_441 (nand_441_out, nand_409_out, nand_442_out);
  nand nand_442 (nand_442_out, nand_441_out, nand_410_out);
  not not_240 (not_240_out, CLOCK);
  nand nand_443 (nand_443_out, nand_411_out, nand_444_out);
  nand nand_444 (nand_444_out, nand_443_out, nand_412_out);
  not not_241 (not_241_out, CLOCK);
  nand nand_445 (nand_445_out, nand_413_out, nand_446_out);
  nand nand_446 (nand_446_out, nand_445_out, nand_414_out);
  not not_242 (not_242_out, CLOCK);
  nand nand_447 (nand_447_out, nand_415_out, nand_448_out);
  nand nand_448 (nand_448_out, nand_447_out, nand_416_out);
  not not_243 (not_243_out, CLOCK);
  not not_244 (not_244_out, nand_417_out);
  not not_245 (not_245_out, nand_419_out);
  not not_246 (not_246_out, nand_421_out);
  not not_247 (not_247_out, nand_423_out);
  not not_248 (not_248_out, nand_425_out);
  not not_249 (not_249_out, nand_427_out);
  not not_250 (not_250_out, nand_429_out);
  not not_251 (not_251_out, nand_431_out);
  not not_252 (not_252_out, nand_433_out);
  not not_253 (not_253_out, nand_435_out);
  not not_254 (not_254_out, nand_437_out);
  not not_255 (not_255_out, nand_439_out);
  not not_256 (not_256_out, nand_441_out);
  not not_257 (not_257_out, nand_443_out);
  not not_258 (not_258_out, nand_445_out);
  not not_259 (not_259_out, nand_447_out);
  nand nand_449 (nand_449_out, nand_417_out, not_228_out);
  nand nand_450 (nand_450_out, not_228_out, not_244_out);
  nand nand_451 (nand_451_out, nand_419_out, not_229_out);
  nand nand_452 (nand_452_out, not_229_out, not_245_out);
  nand nand_453 (nand_453_out, nand_421_out, not_230_out);
  nand nand_454 (nand_454_out, not_230_out, not_246_out);
  nand nand_455 (nand_455_out, nand_423_out, not_231_out);
  nand nand_456 (nand_456_out, not_231_out, not_247_out);
  nand nand_457 (nand_457_out, nand_425_out, not_232_out);
  nand nand_458 (nand_458_out, not_232_out, not_248_out);
  nand nand_459 (nand_459_out, nand_427_out, not_233_out);
  nand nand_460 (nand_460_out, not_233_out, not_249_out);
  nand nand_461 (nand_461_out, nand_429_out, not_234_out);
  nand nand_462 (nand_462_out, not_234_out, not_250_out);
  nand nand_463 (nand_463_out, nand_431_out, not_235_out);
  nand nand_464 (nand_464_out, not_235_out, not_251_out);
  nand nand_465 (nand_465_out, nand_433_out, not_236_out);
  nand nand_466 (nand_466_out, not_236_out, not_252_out);
  nand nand_467 (nand_467_out, nand_435_out, not_237_out);
  nand nand_468 (nand_468_out, not_237_out, not_253_out);
  nand nand_469 (nand_469_out, nand_437_out, not_238_out);
  nand nand_470 (nand_470_out, not_238_out, not_254_out);
  nand nand_471 (nand_471_out, nand_439_out, not_239_out);
  nand nand_472 (nand_472_out, not_239_out, not_255_out);
  nand nand_473 (nand_473_out, nand_441_out, not_240_out);
  nand nand_474 (nand_474_out, not_240_out, not_256_out);
  nand nand_475 (nand_475_out, nand_443_out, not_241_out);
  nand nand_476 (nand_476_out, not_241_out, not_257_out);
  nand nand_477 (nand_477_out, nand_445_out, not_242_out);
  nand nand_478 (nand_478_out, not_242_out, not_258_out);
  nand nand_479 (nand_479_out, nand_447_out, not_243_out);
  nand nand_480 (nand_480_out, not_243_out, not_259_out);
  nand nand_481 (OUT_D[15], nand_449_out, nand_482_out);
  nand nand_482 (nand_482_out, OUT_D[15], nand_450_out);
  nand nand_483 (OUT_D[14], nand_451_out, nand_484_out);
  nand nand_484 (nand_484_out, OUT_D[14], nand_452_out);
  nand nand_485 (OUT_D[13], nand_453_out, nand_486_out);
  nand nand_486 (nand_486_out, OUT_D[13], nand_454_out);
  nand nand_487 (OUT_D[12], nand_455_out, nand_488_out);
  nand nand_488 (nand_488_out, OUT_D[12], nand_456_out);
  nand nand_489 (OUT_D[11], nand_457_out, nand_490_out);
  nand nand_490 (nand_490_out, OUT_D[11], nand_458_out);
  nand nand_491 (OUT_D[10], nand_459_out, nand_492_out);
  nand nand_492 (nand_492_out, OUT_D[10], nand_460_out);
  nand nand_493 (OUT_D[9], nand_461_out, nand_494_out);
  nand nand_494 (nand_494_out, OUT_D[9], nand_462_out);
  nand nand_495 (OUT_D[8], nand_463_out, nand_496_out);
  nand nand_496 (nand_496_out, OUT_D[8], nand_464_out);
  nand nand_497 (OUT_D[7], nand_465_out, nand_498_out);
  nand nand_498 (nand_498_out, OUT_D[7], nand_466_out);
  nand nand_499 (OUT_D[6], nand_467_out, nand_500_out);
  nand nand_500 (nand_500_out, OUT_D[6], nand_468_out);
  nand nand_501 (OUT_D[5], nand_469_out, nand_502_out);
  nand nand_502 (nand_502_out, OUT_D[5], nand_470_out);
  nand nand_503 (OUT_D[4], nand_471_out, nand_504_out);
  nand nand_504 (nand_504_out, OUT_D[4], nand_472_out);
  nand nand_505 (OUT_D[3], nand_473_out, nand_506_out);
  nand nand_506 (nand_506_out, OUT_D[3], nand_474_out);
  nand nand_507 (OUT_D[2], nand_475_out, nand_508_out);
  nand nand_508 (nand_508_out, OUT_D[2], nand_476_out);
  nand nand_509 (OUT_D[1], nand_477_out, nand_510_out);
  nand nand_510 (nand_510_out, OUT_D[1], nand_478_out);
  nand nand_511 (OUT_D[0], nand_479_out, nand_512_out);
  nand nand_512 (nand_512_out, OUT_D[0], nand_480_out);

  assign OUT_B[1:0] = {2{OUT_B[2]}};
  assign OUT_C[1:0] = {2{OUT_C[2]}};
endmodule

module state_counter_2bit (
  input  CLOCK,
  input  LOAD,
  output [1:0] DATA_OUT
);

  wire and_1_out, and_2_out, and_3_out, and_4_out, and_6_out, nand_1_out, nand_2_out, nand_3_out, nand_4_out,
       nand_5_out, nand_6_out, nand_7_out, nand_8_out, nand_9_out, nand_10_out, nand_11_out, nand_12_out,
       nand_14_out, nand_16_out, not_1_out, not_2_out, not_3_out, not_4_out, not_5_out, not_6_out, not_7_out,
       not_8_out, or_1_out, or_2_out, xor_1_out, xor_2_out;

  not not_1 (not_1_out, LOAD);
  not not_2 (not_2_out, LOAD);
  and and_1 (and_1_out, xor_1_out, LOAD);
  and and_2 (and_2_out, 1'b0, not_1_out);
  and and_3 (and_3_out, xor_2_out, LOAD);
  and and_4 (and_4_out, 1'b0, not_2_out);
  or or_1 (or_1_out, and_1_out, and_2_out);
  not not_3 (not_3_out, or_1_out);
  or or_2 (or_2_out, and_3_out, and_4_out);
  not not_4 (not_4_out, or_2_out);
  nand nand_1 (nand_1_out, or_1_out, CLOCK);
  nand nand_2 (nand_2_out, CLOCK, not_3_out);
  nand nand_3 (nand_3_out, or_2_out, CLOCK);
  nand nand_4 (nand_4_out, CLOCK, not_4_out);
  nand nand_5 (nand_5_out, nand_1_out, nand_6_out);
  nand nand_6 (nand_6_out, nand_5_out, nand_2_out);
  nand nand_7 (nand_7_out, nand_3_out, nand_8_out);
  nand nand_8 (nand_8_out, nand_7_out, nand_4_out);
  not not_5 (not_5_out, nand_5_out);
  not not_6 (not_6_out, CLOCK);
  not not_7 (not_7_out, nand_7_out);
  not not_8 (not_8_out, CLOCK);
  nand nand_9 (nand_9_out, nand_5_out, not_6_out);
  nand nand_10 (nand_10_out, not_6_out, not_5_out);
  nand nand_11 (nand_11_out, nand_7_out, not_8_out);
  nand nand_12 (nand_12_out, not_8_out, not_7_out);
  nand nand_13 (DATA_OUT[1], nand_9_out, nand_14_out);
  nand nand_14 (nand_14_out, DATA_OUT[1], nand_10_out);
  nand nand_15 (DATA_OUT[0], nand_11_out, nand_16_out);
  nand nand_16 (nand_16_out, DATA_OUT[0], nand_12_out);
  xor xor_1 (xor_1_out, DATA_OUT[1], and_6_out);
  // AND_Gate and_5 has open pins: in0=DATA_OUT[1], in1=and_6_out, out=open
  xor xor_2 (xor_2_out, DATA_OUT[0], 1'b1);
  and and_6 (and_6_out, DATA_OUT[0], 1'b1);
endmodule
